// Logisim project cpu24.circ as structural Verilog: 28 circuits, main circuit ◇单周期MIPS
module \单周期MIPS  (
  input  IR1,
  input  IR2,
  input  IR3,
  output RegWrite,
  output MemWrite,
  output [31:0] PC,
  output [31:0] IR,
  output [31:0] RDin,
  output [31:0] MDin,
  output [31:0] LedData
);

  wire AluSrcB, and_1_out, and_2_out, and_3_out, Beq, BGTZ, Bne, BranchTaken, CLK, clock_2_out,
       comparator_1_gt, comparator_2_eq, comparator_2_lt, comparator_3_eq, d_ff_1_q, En, Equal, Go, Halt,
       IR1_t, IR2_t, IR3_t, IRA, IRB, IRC, JAL, JMP, JR, LED_EN, MemToReg, nand_1_out, not_1_out, RegDst,
       RST, SB, SignedExt, SLLV, Syscall, W1, W2, W3;
  wire [3:0] AluOP;
  wire [4:0] multiplexer_2_out, multiplexer_3_out, multiplexer_4_out, multiplexer_5_out, multiplexer_8_out;
  wire [12:0] CNT_num;
  wire [15:0] \总周期数 ;
  wire [27:0] PC_4;
  wire [31:0] A0, bit_extender_1_out, bit_extender_2_out, BranchAddr, GPRrs, IP, mips_alu_1_result,
       multiplexer_6_out, multiplexer_7_out, multiplexer_9_out, ram_1_data, shifter_1_out, \按字节存储电路_1_ddata ;
  wire [31:28] JMPAddr;

  Clock #(.highDuration(1), .lowDuration(1)) clock_1 ();  // open: out
  Button _1 (.out(IRA));
  Button _2 (.out(IRB));
  Button _3 (.out(IRC));
  Button \u_继续运行  (.out(Go));
  LED #(.active("true")) led_1 (.in(W1));
  LED #(.active("true")) led_2 (.in(W2));
  LED #(.active("true")) led_3 (.in(W3));
  Register #(.width(32), .trigger("rising"), .Select("low")) u_PC (.D(IP), .en(En), .Q(PC), .clk(CLK), .clr(RST));
  Hex_Digit_Display hex_digit_display_1 (.value(LedData[31:28]));  // open: dp
  not not_1 (not_1_out, Halt);
  Adder #(.width(32)) adder_1 (.a(PC), .b(32'h4), .out({JMPAddr, PC_4}), .cin(1'b0));  // open: cout
  D_Flip_Flop #(.trigger("high"), .Pre_Clr_Positions("LEGACY"), .NegatePresetClear("false"), .enable("true"), .NewFFLayout("false")) d_ff_1 (.Q(d_ff_1_q));  // open: clk, D, Qn, preset, en, reset
  // Probe on 13'hc
  Comparator #(.width(32), .mode("twosComplement")) comparator_1 (
    .a(GPRrs), .b({32{1'b0}}), .gt(comparator_1_gt));  // open: eq, lt
  Hex_Digit_Display hex_digit_display_2 (.value(LedData[23:20]));  // open: dp
  Hex_Digit_Display hex_digit_display_3 (.value(LedData[27:24]));  // open: dp
  or or_1 (En, not_1_out, Go);
  Comparator #(.width(13), .mode("twosComplement")) comparator_2 (
    .a(CNT_num), .b(13'hc), .eq(comparator_2_eq), .lt(comparator_2_lt));  // open: gt
  Clock #(.highDuration(1), .lowDuration(1)) clock_2 (.out(clock_2_out));
  and and_1 (and_1_out, Beq, Equal);
  and and_2 (and_2_out, ~Equal, Bne);  // AND_Gate
  and and_3 (and_3_out, comparator_1_gt, BGTZ);
  Hex_Digit_Display hex_digit_display_4 (.value(LedData[15:12]));  // open: dp
  Hex_Digit_Display hex_digit_display_5 (.value(LedData[19:16]));  // open: dp
  // Mips_Probe mips_probe_1: pin names not known; wires that end beside it: IR
  ROM #(.addrWidth(10), .dataWidth(32), .Select("high")) rom_1 (.addr(PC[11:2]), .data(IR));
  nand nand_1 (nand_1_out, d_ff_1_q, comparator_2_eq);
  Counter #(.width(13), .max('h1fff), .ongoal("stay"), .trigger("rising"), .behavior("old")) counter_1 (
    .count(comparator_2_lt), .Q(CNT_num), .clk(clock_2_out));  // open: load, D, carry, clr, preset
  or or_2 (BranchTaken, and_1_out, and_2_out, and_3_out);
  Hex_Digit_Display hex_digit_display_6 (.value(LedData[7:4]));  // open: dp
  Hex_Digit_Display hex_digit_display_7 (.value(LedData[11:8]));  // open: dp
  // Probe on \总周期数 
  assign CLK = nand_1_out ? clock_2_out : 1'bz;  // Controlled_Buffer controlled_buffer_1
  Hex_Digit_Display hex_digit_display_8 (.value(LedData[3:0]));  // open: dp
  Pull_Resistor #(.pull(1)) pull_resistor_1 (.node(CLK));
  or or_3 (IR1_t, IR1, IRA);
  Counter #(.width(16), .max('hffff), .ongoal("wrap"), .trigger("rising"), .behavior("new")) counter_2 (
    .count(En), .Q(\总周期数 ), .clk(CLK), .clr(RST));  // open: load, D, carry, preset, down
  or or_4 (IR2_t, IR2, IRB);
  Multiplexer #(.select(3), .width(32), .disabled("Z"), .enable("false")) multiplexer_1 (
    .in0({JMPAddr, PC_4}), .in1(BranchAddr), .in2({JMPAddr, IR[25:0], 2'b00}), .in6(GPRrs), .out(IP),
    .sel({JR, JMP, BranchTaken}));  // open: in3, in4, in5, in7
  or or_5 (IR3_t, IR3, IRC);
  assign bit_extender_1_out = {{16{1'b0}}, IR[15:0]};  // Bit_Extender bit_extender_1
  assign bit_extender_2_out = {{16{IR[15]}}, IR[15:0]};  // Bit_Extender bit_extender_2
  Multiplexer #(.select(1), .width(5), .disabled("Z"), .enable("false")) multiplexer_2 (
    .in0(IR[25:21]), .in1(5'b00010), .out(multiplexer_2_out), .sel(Syscall));
  Multiplexer #(.select(1), .width(5), .disabled("Z"), .enable("false")) multiplexer_3 (
    .in0(IR[20:16]), .in1(5'b00100), .out(multiplexer_3_out), .sel(Syscall));
  Multiplexer #(.select(1), .width(5), .disabled("Z"), .enable("false")) multiplexer_4 (
    .in0(IR[20:16]), .in1(IR[15:11]), .out(multiplexer_4_out), .sel(RegDst));
  Multiplexer #(.select(1), .width(5), .disabled("Z"), .enable("false")) multiplexer_5 (
    .in0(multiplexer_4_out), .in1({5{1'b1}}), .out(multiplexer_5_out), .sel(JAL));
  Multiplexer #(.select(1), .width(32), .disabled("Z"), .enable("false")) multiplexer_6 (
    .in0(bit_extender_1_out), .in1(bit_extender_2_out), .out(multiplexer_6_out), .sel(SignedExt));
  // Probe on GPRrs
  MIPS_Regifile mips_regifile_1 (
    .Din(RDin), .Clk(CLK), .R1(GPRrs), .R2(A0), .WE(RegWrite), .W_num(multiplexer_5_out),
    .R1_num(multiplexer_2_out), .R2_num(multiplexer_3_out));
  Shifter #(.width(32), .shift("ll")) shifter_1 (.in(bit_extender_2_out), .\dist (5'b00010), .out(shifter_1_out));
  Comparator #(.width(32), .mode("twosComplement")) comparator_3 (
    .a(GPRrs), .b(32'ha), .eq(comparator_3_eq));  // open: gt, lt
  Register #(.width(32), .trigger("rising"), .Select("low")) register_1 (
    .D(A0), .en(LED_EN), .Q(LedData), .clk(CLK));  // open: clr
  and and_4 (Halt, Syscall, comparator_3_eq);
  Multiplexer #(.select(1), .width(32), .disabled("Z"), .enable("false")) multiplexer_7 (
    .in0(A0), .in1(multiplexer_6_out), .out(multiplexer_7_out), .sel(AluSrcB));
  Multiplexer #(.select(1), .width(5), .disabled("Z"), .enable("false")) multiplexer_8 (
    .in0(IR[10:6]), .in1(GPRrs[4:0]), .out(multiplexer_8_out), .sel(SLLV));
  Adder #(.width(32)) adder_2 (.a(shifter_1_out), .b({JMPAddr, PC_4}), .out(BranchAddr), .cin(1'b0));  // open: cout
  and and_5 (LED_EN, ~comparator_3_eq, Syscall);  // AND_Gate
  Button RESET (.out(RST));
  MIPS_ALU mips_alu_1 (
    .X(GPRrs), .Y(multiplexer_7_out), .AluOP(AluOP), .Equal(Equal), .Result(mips_alu_1_result),
    .shamt(multiplexer_8_out));  // open: Result_2
  RAM #(.addrWidth(10), .dataWidth(32), .bus("separate"), .Select("high")) ram_1 (
    .addr(mips_alu_1_result[11:2]), .din(MDin), .data(ram_1_data), .str(MemWrite), .clk(CLK), .ld(1'b1));  // open: sel, clr
  \按字节存储电路  \u_按字节存储电路_1  (.cdata(A0), .sel(mips_alu_1_result), .sdata(ram_1_data), .ddata(\按字节存储电路_1_ddata ));
  \单周期硬布线控制器  \u_单周期硬布线控制器_1  (
    .Func(IR[5:0]), .OP(IR[31:26]), .ALU_OP(AluOP), .MemToReg(MemToReg), .MemWrite(MemWrite),
    .ALU_SRC(AluSrcB), .RegWrite(RegWrite), .SysCALL(Syscall), .SignedExt(SignedExt), .RegDst(RegDst),
    .JR(JR), .JMP(JMP), .Beq(Beq), .JAL(JAL), .Bne(Bne), .SB(SB), .BGTZ(BGTZ), .SLLV(SLLV));
  Multiplexer #(.select(1), .width(32), .disabled("Z"), .enable("false")) multiplexer_9 (
    .in0(mips_alu_1_result), .in1(ram_1_data), .out(multiplexer_9_out), .sel(MemToReg));
  Multiplexer #(.select(1), .width(32), .disabled("Z"), .enable("false")) multiplexer_10 (
    .in0(multiplexer_9_out), .in1({JMPAddr, PC_4}), .out(RDin), .sel(JAL));
  Multiplexer #(.select(1), .width(32), .disabled("Z"), .enable("false")) multiplexer_11 (
    .in0(A0), .in1(\按字节存储电路_1_ddata ), .out(MDin), .sel(SB));
  // Probe on RDin

  // Other names for the same wires on the sheet: GPRrt[31:0] = A0; addr[25:0] = IR[25:0]; Func[5:0] = IR[5:0];
  //   imm[15:0] = IR[15:0]; JMPAddr[27:2] = IR[25:0]; shamt[4:0] = IR[10:6]; rd[4:0] = IR[15:11]; rt[4:0] = IR[20:16];
  //   rs[4:0] = IR[25:21]; OP[5:0] = IR[31:26]; PC_4[31:28] = JMPAddr; V0[31:0] = GPRrs

  // Notes on the sheet:
  //   中断源
  //   中断等待指示
  //   总复位信号应将除ROM以外所有存储组件全部清零
  //   控制位
  //   暂停节拍，不能为0
  //   指令存储器
  //   用这个时钟源需要去掉电路中的其他时钟源
  //   戳工具置1进入计数暂停模式，ctrl+k时钟自动运行到对应节拍暂停
  //   ctrl+k关闭时钟连续运行，将控制位置零，进入单步调试模式调试
  //   数码管输出
  //   指令字
  //   contents of rom_1 (hex, n*v repeats v):
  //   2008ffff 20117777 112020 20020022 c 200b0010 3a31ffff 112020 20020022 c 216bffff 1560fffa 2002000a c
  //   数码管输出应该用寄存器锁存，否则显示数据只能一闪而过
  //   OP
  //   Func
  //   rs
  //   rt
  //   rd
  //   imm
  //   addr
  //   可计数暂停的时钟源
  //   为方便自动评测，需要输出PC，IR，寄存器堆写如数据RDin
  //   RAM写使能MemWrite、RAM写入数据MDin等信号
  //   符号扩展
  //   BGTZ
  //   SB
  //   Beq
  //   JMP
  //   JR
  //   Bne
  //   SLLV
  //   OP
  //   JAL
  //   Func
  //   Syscall
  //   MemToReg
  //   MemWrite
  //   AluOP
  //   AluSrcB
  //   RegWrite
  //   RegDst
endmodule

// 单周期硬布线控制器
module \单周期硬布线控制器  (
  input  [5:0] OP,
  input  [5:0] Func,
  output [3:0] ALU_OP,
  output MemToReg,
  output MemWrite,
  output ALU_SRC,
  output RegWrite,
  output SysCALL,
  output SignedExt,
  output RegDst,
  output Beq,
  output Bne,
  output JR,
  output JMP,
  output JAL,
  output SLLV,
  output BGTZ,
  output SB
);

  \运算控制器自动生成  \u_运算控制器自动生成_1  (
    .OP0(OP[0]), .OP1(OP[1]), .OP2(OP[2]), .OP3(OP[3]), .OP4(OP[4]), .OP5(OP[5]), .F0(Func[0]), .F1(Func[1]),
    .F2(Func[2]), .F3(Func[3]), .F4(Func[4]), .F5(Func[5]), .S0(ALU_OP[0]), .S1(ALU_OP[1]), .S2(ALU_OP[2]),
    .S3(ALU_OP[3]));
  \控制信号自动生成  \u_控制信号自动生成_1  (
    .OP0(OP[0]), .MemToReg(MemToReg), .OP1(OP[1]), .OP2(OP[2]), .OP3(OP[3]), .OP4(OP[4]),
    .MemWrite(MemWrite), .OP5(OP[5]), .F0(Func[0]), .F1(Func[1]), .F2(Func[2]), .F3(Func[3]), .F4(Func[4]),
    .F5(Func[5]), .ALU_SRC(ALU_SRC), .RegWrite(RegWrite), .SysCALL(SysCALL), .SignedExt(SignedExt),
    .RegDst(RegDst), .BEQ(Beq), .BNE(Bne), .JR(JR), .JUMP(JMP), .JAL(JAL), .SLLV(SLLV), .BGTZ(BGTZ), .SB(SB));

  // Other names for the same wires on the sheet: OP_CODE[5:0] = OP

  // Notes on the sheet:
  //   运算器控制器，根据指令生成运算器功能选择信号
  //   控制信号生成，产生数据通路需要的其他控制信号
endmodule

// 运算器控制器
module \运算控制器自动生成  (
  input  OP0,
  input  OP1,
  input  OP2,
  input  OP3,
  input  OP4,
  input  OP5,
  input  F0,
  input  F1,
  input  F2,
  input  F3,
  input  F4,
  input  F5,
  output S0,
  output S1,
  output S2,
  output S3
);

  wire and_1_out, and_2_out, and_3_out, and_4_out, and_5_out, and_6_out, and_7_out, and_8_out, and_9_out,
       and_10_out, and_11_out, and_12_out, and_13_out, and_14_out, and_15_out, and_16_out, and_17_out,
       and_18_out, and_19_out, and_20_out, and_21_out, and_22_out, and_23_out, and_24_out, and_25_out,
       and_26_out, and_27_out, and_28_out, and_29_out, and_30_out, and_31_out, and_32_out, and_33_out,
       and_34_out, and_35_out, and_36_out, and_37_out, and_38_out, and_39_out, and_40_out, and_41_out,
       not_1_out, not_2_out, not_3_out, not_4_out, not_5_out, not_6_out, not_7_out, not_8_out, not_9_out,
       not_10_out, not_11_out, not_12_out, not_13_out, not_14_out, not_15_out, not_16_out, not_17_out,
       not_18_out, not_19_out, not_20_out, not_21_out, not_22_out, not_23_out, not_24_out, not_25_out,
       not_26_out, not_27_out, not_28_out, not_29_out, not_30_out, not_31_out, not_32_out, not_33_out,
       not_34_out, not_35_out, not_36_out, not_37_out, not_38_out, not_39_out, not_40_out, not_41_out,
       not_42_out, not_43_out, not_44_out, not_45_out, not_46_out, not_47_out, not_48_out, not_49_out,
       not_50_out, not_51_out, not_52_out, not_53_out, not_54_out, not_55_out, not_56_out, not_57_out,
       not_58_out, not_59_out, not_60_out, not_61_out, not_62_out, not_63_out, not_64_out, not_65_out,
       not_66_out, not_67_out, not_68_out, not_69_out, not_70_out, not_71_out, not_72_out, not_73_out,
       not_74_out, not_75_out, not_76_out, not_77_out, not_78_out, not_79_out, not_80_out, not_81_out,
       not_82_out, not_83_out, not_84_out, not_85_out, not_86_out, not_87_out, not_88_out, not_89_out,
       not_90_out, not_91_out, not_92_out, not_93_out, not_94_out, not_95_out, not_96_out, not_97_out,
       not_98_out, not_99_out, not_100_out, not_101_out, not_102_out, not_103_out, not_104_out, not_105_out,
       not_106_out, not_107_out, not_108_out, not_109_out, not_110_out, not_111_out, not_112_out,
       not_113_out, not_114_out, not_115_out, not_116_out, not_117_out, not_118_out, not_119_out,
       not_120_out, not_121_out, not_122_out, not_123_out, not_124_out, not_125_out, not_126_out,
       not_127_out, not_128_out, not_129_out, not_130_out, not_131_out, not_132_out, not_133_out,
       not_134_out, not_135_out, not_136_out, not_137_out, not_138_out, not_139_out, not_140_out,
       not_141_out, not_142_out, not_143_out, not_144_out, not_145_out, not_146_out, not_147_out,
       not_148_out, not_149_out, not_150_out, not_151_out, not_152_out, not_153_out, not_154_out,
       not_155_out, not_156_out, not_157_out, not_158_out, not_159_out, not_160_out, not_161_out,
       not_162_out, not_163_out, not_164_out, not_165_out, not_166_out, not_167_out, not_168_out,
       not_169_out, not_170_out, not_171_out, not_172_out, not_173_out, not_174_out, not_175_out,
       not_176_out, not_177_out, not_178_out, not_179_out, not_180_out, not_181_out, not_182_out,
       not_183_out, not_184_out, not_185_out, not_186_out, not_187_out, not_188_out, not_189_out,
       not_190_out, not_191_out, not_192_out, not_193_out, not_194_out, not_195_out, not_196_out,
       not_197_out, not_198_out, not_199_out, not_200_out, not_201_out, not_202_out, not_203_out,
       not_204_out, not_205_out, not_206_out, not_207_out, not_208_out, not_209_out, not_210_out,
       not_211_out, not_212_out, not_213_out, not_214_out, not_215_out, not_216_out, not_217_out,
       not_218_out, not_219_out, not_220_out, not_221_out, not_222_out, not_223_out, not_224_out,
       not_225_out, not_226_out, not_227_out, not_228_out, not_229_out, not_230_out, not_231_out,
       not_232_out, not_233_out, not_234_out, not_235_out, not_236_out, not_237_out, not_238_out,
       not_239_out, not_240_out, not_241_out, not_242_out, not_243_out, not_244_out, not_245_out,
       not_246_out, not_247_out, not_248_out, not_249_out, not_250_out, not_251_out, not_252_out,
       not_253_out, not_254_out, not_255_out, not_256_out, not_257_out, not_258_out, not_259_out;

  not not_1 (not_1_out, OP5);
  not not_2 (not_2_out, OP4);
  not not_3 (not_3_out, OP3);
  not not_4 (not_4_out, OP2);
  not not_5 (not_5_out, OP1);
  not not_6 (not_6_out, OP0);
  not not_7 (not_7_out, F5);
  not not_8 (not_8_out, F4);
  not not_9 (not_9_out, F3);
  not not_10 (not_10_out, F2);
  not not_11 (not_11_out, OP5);
  not not_12 (not_12_out, OP4);
  not not_13 (not_13_out, OP3);
  not not_14 (not_14_out, OP2);
  not not_15 (not_15_out, OP1);
  not not_16 (not_16_out, OP0);
  not not_17 (not_17_out, F4);
  not not_18 (not_18_out, F3);
  not not_19 (not_19_out, F2);
  not not_20 (not_20_out, F1);
  not not_21 (not_21_out, F0);
  not not_22 (not_22_out, OP5);
  not not_23 (not_23_out, OP4);
  not not_24 (not_24_out, OP3);
  not not_25 (not_25_out, OP2);
  not not_26 (not_26_out, OP1);
  not not_27 (not_27_out, OP0);
  not not_28 (not_28_out, F4);
  not not_29 (not_29_out, F3);
  not not_30 (not_30_out, F2);
  not not_31 (not_31_out, F1);
  not not_32 (not_32_out, OP5);
  not not_33 (not_33_out, OP4);
  not not_34 (not_34_out, OP3);
  not not_35 (not_35_out, OP2);
  not not_36 (not_36_out, OP1);
  not not_37 (not_37_out, OP0);
  not not_38 (not_38_out, F4);
  not not_39 (not_39_out, F3);
  not not_40 (not_40_out, F1);
  not not_41 (not_41_out, F0);
  not not_42 (not_42_out, OP5);
  not not_43 (not_43_out, OP4);
  not not_44 (not_44_out, OP3);
  not not_45 (not_45_out, OP2);
  not not_46 (not_46_out, OP1);
  not not_47 (not_47_out, OP0);
  not not_48 (not_48_out, F4);
  not not_49 (not_49_out, F2);
  not not_50 (not_50_out, F0);
  not not_51 (not_51_out, OP5);
  not not_52 (not_52_out, OP4);
  not not_53 (not_53_out, OP2);
  not not_54 (not_54_out, OP1);
  not not_55 (not_55_out, OP0);
  not not_56 (not_56_out, OP5);
  not not_57 (not_57_out, OP4);
  not not_58 (not_58_out, OP1);
  not not_59 (not_59_out, OP0);
  not not_60 (not_60_out, OP5);
  not not_61 (not_61_out, OP4);
  not not_62 (not_62_out, OP2);
  not not_63 (not_63_out, OP1);
  not not_64 (not_64_out, OP5);
  not not_65 (not_65_out, OP4);
  not not_66 (not_66_out, OP2);
  not not_67 (not_67_out, OP0);
  not not_68 (not_68_out, OP4);
  not not_69 (not_69_out, OP3);
  not not_70 (not_70_out, OP2);
  not not_71 (not_71_out, OP4);
  not not_72 (not_72_out, OP2);
  not not_73 (not_73_out, OP5);
  not not_74 (not_74_out, OP4);
  not not_75 (not_75_out, OP0);
  not not_76 (not_76_out, OP5);
  not not_77 (not_77_out, OP4);
  not not_78 (not_78_out, OP3);
  not not_79 (not_79_out, OP4);
  not not_80 (not_80_out, OP2);
  not not_81 (not_81_out, OP1);
  not not_82 (not_82_out, OP0);
  not not_83 (not_83_out, OP5);
  not not_84 (not_84_out, OP4);
  not not_85 (not_85_out, OP3);
  not not_86 (not_86_out, OP2);
  not not_87 (not_87_out, OP1);
  not not_88 (not_88_out, OP0);
  not not_89 (not_89_out, F5);
  not not_90 (not_90_out, F4);
  not not_91 (not_91_out, F3);
  not not_92 (not_92_out, F2);
  not not_93 (not_93_out, F0);
  not not_94 (not_94_out, OP5);
  not not_95 (not_95_out, OP4);
  not not_96 (not_96_out, OP3);
  not not_97 (not_97_out, OP2);
  not not_98 (not_98_out, OP1);
  not not_99 (not_99_out, OP0);
  not not_100 (not_100_out, F4);
  not not_101 (not_101_out, F3);
  not not_102 (not_102_out, F2);
  not not_103 (not_103_out, F0);
  not not_104 (not_104_out, OP5);
  not not_105 (not_105_out, OP4);
  not not_106 (not_106_out, OP3);
  not not_107 (not_107_out, OP2);
  not not_108 (not_108_out, OP1);
  not not_109 (not_109_out, OP0);
  not not_110 (not_110_out, F4);
  not not_111 (not_111_out, F3);
  not not_112 (not_112_out, F1);
  not not_113 (not_113_out, F0);
  not not_114 (not_114_out, OP5);
  not not_115 (not_115_out, OP4);
  not not_116 (not_116_out, OP3);
  not not_117 (not_117_out, OP2);
  not not_118 (not_118_out, OP1);
  not not_119 (not_119_out, OP0);
  not not_120 (not_120_out, F4);
  not not_121 (not_121_out, F3);
  not not_122 (not_122_out, OP5);
  not not_123 (not_123_out, OP4);
  not not_124 (not_124_out, OP3);
  not not_125 (not_125_out, OP2);
  not not_126 (not_126_out, OP1);
  not not_127 (not_127_out, OP0);
  not not_128 (not_128_out, F4);
  not not_129 (not_129_out, F2);
  not not_130 (not_130_out, F0);
  not not_131 (not_131_out, OP5);
  not not_132 (not_132_out, OP4);
  not not_133 (not_133_out, OP1);
  not not_134 (not_134_out, OP0);
  not not_135 (not_135_out, OP5);
  not not_136 (not_136_out, OP4);
  not not_137 (not_137_out, OP2);
  not not_138 (not_138_out, OP0);
  not not_139 (not_139_out, OP5);
  not not_140 (not_140_out, OP4);
  not not_141 (not_141_out, OP3);
  not not_142 (not_142_out, OP5);
  not not_143 (not_143_out, OP4);
  not not_144 (not_144_out, OP3);
  not not_145 (not_145_out, OP2);
  not not_146 (not_146_out, OP1);
  not not_147 (not_147_out, OP0);
  not not_148 (not_148_out, F4);
  not not_149 (not_149_out, F3);
  not not_150 (not_150_out, F2);
  not not_151 (not_151_out, F1);
  not not_152 (not_152_out, F0);
  not not_153 (not_153_out, OP5);
  not not_154 (not_154_out, OP4);
  not not_155 (not_155_out, OP3);
  not not_156 (not_156_out, OP2);
  not not_157 (not_157_out, OP1);
  not not_158 (not_158_out, OP0);
  not not_159 (not_159_out, F4);
  not not_160 (not_160_out, F3);
  not not_161 (not_161_out, F2);
  not not_162 (not_162_out, F1);
  not not_163 (not_163_out, OP5);
  not not_164 (not_164_out, OP4);
  not not_165 (not_165_out, OP3);
  not not_166 (not_166_out, OP2);
  not not_167 (not_167_out, OP1);
  not not_168 (not_168_out, OP0);
  not not_169 (not_169_out, F4);
  not not_170 (not_170_out, F3);
  not not_171 (not_171_out, F2);
  not not_172 (not_172_out, F0);
  not not_173 (not_173_out, OP5);
  not not_174 (not_174_out, OP4);
  not not_175 (not_175_out, OP3);
  not not_176 (not_176_out, OP2);
  not not_177 (not_177_out, OP1);
  not not_178 (not_178_out, OP0);
  not not_179 (not_179_out, F4);
  not not_180 (not_180_out, F3);
  not not_181 (not_181_out, F1);
  not not_182 (not_182_out, F0);
  not not_183 (not_183_out, OP5);
  not not_184 (not_184_out, OP4);
  not not_185 (not_185_out, OP3);
  not not_186 (not_186_out, OP2);
  not not_187 (not_187_out, OP1);
  not not_188 (not_188_out, OP0);
  not not_189 (not_189_out, F4);
  not not_190 (not_190_out, F2);
  not not_191 (not_191_out, OP5);
  not not_192 (not_192_out, OP4);
  not not_193 (not_193_out, OP2);
  not not_194 (not_194_out, OP1);
  not not_195 (not_195_out, OP0);
  not not_196 (not_196_out, OP5);
  not not_197 (not_197_out, OP4);
  not not_198 (not_198_out, OP1);
  not not_199 (not_199_out, OP0);
  not not_200 (not_200_out, OP5);
  not not_201 (not_201_out, OP4);
  not not_202 (not_202_out, OP2);
  not not_203 (not_203_out, OP1);
  not not_204 (not_204_out, OP4);
  not not_205 (not_205_out, OP3);
  not not_206 (not_206_out, OP2);
  not not_207 (not_207_out, OP4);
  not not_208 (not_208_out, OP2);
  not not_209 (not_209_out, OP4);
  not not_210 (not_210_out, OP2);
  not not_211 (not_211_out, OP1);
  not not_212 (not_212_out, OP0);
  not not_213 (not_213_out, OP5);
  not not_214 (not_214_out, OP4);
  not not_215 (not_215_out, OP3);
  not not_216 (not_216_out, OP2);
  not not_217 (not_217_out, OP1);
  not not_218 (not_218_out, OP0);
  not not_219 (not_219_out, F4);
  not not_220 (not_220_out, F3);
  not not_221 (not_221_out, F1);
  not not_222 (not_222_out, OP5);
  not not_223 (not_223_out, OP4);
  not not_224 (not_224_out, OP3);
  not not_225 (not_225_out, OP2);
  not not_226 (not_226_out, OP1);
  not not_227 (not_227_out, OP0);
  not not_228 (not_228_out, F4);
  not not_229 (not_229_out, F3);
  not not_230 (not_230_out, OP5);
  not not_231 (not_231_out, OP4);
  not not_232 (not_232_out, OP3);
  not not_233 (not_233_out, OP2);
  not not_234 (not_234_out, OP1);
  not not_235 (not_235_out, OP0);
  not not_236 (not_236_out, F4);
  not not_237 (not_237_out, F2);
  not not_238 (not_238_out, F0);
  not not_239 (not_239_out, OP5);
  not not_240 (not_240_out, OP4);
  not not_241 (not_241_out, OP3);
  not not_242 (not_242_out, OP2);
  not not_243 (not_243_out, OP1);
  not not_244 (not_244_out, OP0);
  not not_245 (not_245_out, F4);
  not not_246 (not_246_out, F2);
  not not_247 (not_247_out, OP5);
  not not_248 (not_248_out, OP4);
  not not_249 (not_249_out, OP2);
  not not_250 (not_250_out, OP0);
  not not_251 (not_251_out, OP5);
  not not_252 (not_252_out, OP4);
  not not_253 (not_253_out, OP1);
  not not_254 (not_254_out, OP5);
  not not_255 (not_255_out, OP4);
  not not_256 (not_256_out, OP0);
  not not_257 (not_257_out, OP5);
  not not_258 (not_258_out, OP4);
  not not_259 (not_259_out, OP3);
  and and_1 (and_1_out, not_1_out, not_2_out, not_3_out, not_4_out, not_5_out, not_6_out, not_7_out, not_8_out, not_9_out, not_10_out, F1, F0);
  and and_2 (and_2_out, not_11_out, not_12_out, not_13_out, not_14_out, not_15_out, not_16_out, F5, not_17_out, not_18_out, not_19_out, not_20_out, not_21_out);
  and and_3 (and_3_out, not_22_out, not_23_out, not_24_out, not_25_out, not_26_out, not_27_out, F5, not_28_out, not_29_out, not_30_out, not_31_out, F0);
  and and_4 (and_4_out, not_32_out, not_33_out, not_34_out, not_35_out, not_36_out, not_37_out, F5, not_38_out, not_39_out, F2, not_40_out, not_41_out);
  and and_5 (and_5_out, not_42_out, not_43_out, not_44_out, not_45_out, not_46_out, not_47_out, F5, not_48_out, F3, not_49_out, F1, not_50_out);
  and and_6 (and_6_out, not_51_out, not_52_out, OP3, not_53_out, not_54_out, not_55_out);
  and and_7 (and_7_out, not_56_out, not_57_out, OP3, OP2, not_58_out, not_59_out);
  and and_8 (and_8_out, not_60_out, not_61_out, OP3, not_62_out, not_63_out, OP0);
  and and_9 (and_9_out, not_64_out, not_65_out, OP3, not_66_out, OP1, not_67_out);
  and and_10 (and_10_out, OP5, not_68_out, not_69_out, not_70_out, OP1, OP0);
  and and_11 (and_11_out, OP5, not_71_out, OP3, not_72_out, OP1, OP0);
  and and_12 (and_12_out, not_73_out, not_74_out, OP3, OP2, OP1, not_75_out);
  and and_13 (and_13_out, not_76_out, not_77_out, not_78_out, OP2, OP1, OP0);
  and and_14 (and_14_out, OP5, not_79_out, OP3, not_80_out, not_81_out, not_82_out);
  and and_15 (and_15_out, not_83_out, not_84_out, not_85_out, not_86_out, not_87_out, not_88_out, not_89_out, not_90_out, not_91_out, not_92_out, F1, not_93_out);
  and and_16 (and_16_out, not_94_out, not_95_out, not_96_out, not_97_out, not_98_out, not_99_out, F5, not_100_out, not_101_out, not_102_out, F1, not_103_out);
  and and_17 (and_17_out, not_104_out, not_105_out, not_106_out, not_107_out, not_108_out, not_109_out, F5, not_110_out, not_111_out, F2, not_112_out, not_113_out);
  and and_18 (and_18_out, not_114_out, not_115_out, not_116_out, not_117_out, not_118_out, not_119_out, F5, not_120_out, not_121_out, F2, F1, F0);
  and and_19 (and_19_out, not_122_out, not_123_out, not_124_out, not_125_out, not_126_out, not_127_out, F5, not_128_out, F3, not_129_out, F1, not_130_out);
  and and_20 (and_20_out, not_131_out, not_132_out, OP3, OP2, not_133_out, not_134_out);
  and and_21 (and_21_out, not_135_out, not_136_out, OP3, not_137_out, OP1, not_138_out);
  and and_22 (and_22_out, not_139_out, not_140_out, not_141_out, OP2, OP1, OP0);
  and and_23 (and_23_out, not_142_out, not_143_out, not_144_out, not_145_out, not_146_out, not_147_out, F5, not_148_out, not_149_out, not_150_out, not_151_out, not_152_out);
  and and_24 (and_24_out, not_153_out, not_154_out, not_155_out, not_156_out, not_157_out, not_158_out, F5, not_159_out, not_160_out, not_161_out, not_162_out, F0);
  and and_25 (and_25_out, not_163_out, not_164_out, not_165_out, not_166_out, not_167_out, not_168_out, F5, not_169_out, not_170_out, not_171_out, F1, not_172_out);
  and and_26 (and_26_out, not_173_out, not_174_out, not_175_out, not_176_out, not_177_out, not_178_out, F5, not_179_out, not_180_out, F2, not_181_out, not_182_out);
  and and_27 (and_27_out, not_183_out, not_184_out, not_185_out, not_186_out, not_187_out, not_188_out, F5, not_189_out, F3, not_190_out, F1, F0);
  and and_28 (and_28_out, not_191_out, not_192_out, OP3, not_193_out, not_194_out, not_195_out);
  and and_29 (and_29_out, not_196_out, not_197_out, OP3, OP2, not_198_out, not_199_out);
  and and_30 (and_30_out, not_200_out, not_201_out, OP3, not_202_out, not_203_out, OP0);
  and and_31 (and_31_out, OP5, not_204_out, not_205_out, not_206_out, OP1, OP0);
  and and_32 (and_32_out, OP5, not_207_out, OP3, not_208_out, OP1, OP0);
  and and_33 (and_33_out, OP5, not_209_out, OP3, not_210_out, not_211_out, not_212_out);
  and and_34 (and_34_out, not_213_out, not_214_out, not_215_out, not_216_out, not_217_out, not_218_out, F5, not_219_out, not_220_out, F2, not_221_out, F0);
  and and_35 (and_35_out, not_222_out, not_223_out, not_224_out, not_225_out, not_226_out, not_227_out, F5, not_228_out, not_229_out, F2, F1, F0);
  and and_36 (and_36_out, not_230_out, not_231_out, not_232_out, not_233_out, not_234_out, not_235_out, F5, not_236_out, F3, not_237_out, F1, not_238_out);
  and and_37 (and_37_out, not_239_out, not_240_out, not_241_out, not_242_out, not_243_out, not_244_out, F5, not_245_out, F3, not_246_out, F1, F0);
  and and_38 (and_38_out, not_247_out, not_248_out, OP3, not_249_out, OP1, not_250_out);
  and and_39 (and_39_out, not_251_out, not_252_out, OP3, OP2, not_253_out, OP0);
  and and_40 (and_40_out, not_254_out, not_255_out, OP3, OP2, OP1, not_256_out);
  and and_41 (and_41_out, not_257_out, not_258_out, not_259_out, OP2, OP1, OP0);
  or or_1 (S1, and_15_out, and_16_out, and_17_out, and_18_out, and_19_out, and_20_out, and_21_out, and_22_out);
  or or_2 (S2, and_23_out, and_24_out, and_25_out, and_26_out, and_27_out, and_28_out, and_29_out, and_30_out, and_31_out, and_32_out, and_33_out);
  or or_3 (S3, and_34_out, and_35_out, and_36_out, and_37_out, and_38_out, and_39_out, and_40_out, and_41_out);
  or or_4 (S0, and_1_out, and_2_out, and_3_out, and_4_out, and_5_out, and_6_out, and_7_out, and_8_out, and_9_out, and_10_out, and_11_out, and_12_out, and_13_out, and_14_out);
endmodule

// 控制信号生成
module \控制信号自动生成  (
  input  OP0,
  input  OP1,
  input  OP2,
  input  OP3,
  input  OP4,
  input  OP5,
  input  F0,
  input  F1,
  input  F2,
  input  F3,
  input  F4,
  input  F5,
  output MemToReg,
  output MemWrite,
  output ALU_SRC,
  output RegWrite,
  output SysCALL,
  output SignedExt,
  output RegDst,
  output BEQ,
  output BNE,
  output JR,
  output JUMP,
  output JAL,
  output SLLV,
  output BGTZ,
  output SB
);

  wire and_2_out, and_3_out, and_4_out, and_5_out, and_6_out, and_7_out, and_8_out, and_9_out, and_10_out,
       and_11_out, and_12_out, and_13_out, and_14_out, and_15_out, and_16_out, and_17_out, and_18_out,
       and_19_out, and_20_out, and_21_out, and_23_out, and_24_out, and_25_out, and_26_out, and_27_out,
       and_28_out, and_29_out, and_30_out, and_31_out, and_32_out, and_36_out, and_37_out, not_1_out,
       not_2_out, not_3_out, not_4_out, not_5_out, not_6_out, not_7_out, not_8_out, not_9_out, not_10_out,
       not_11_out, not_12_out, not_13_out, not_14_out, not_15_out, not_16_out, not_17_out, not_18_out,
       not_19_out, not_20_out, not_21_out, not_22_out, not_23_out, not_24_out, not_25_out, not_26_out,
       not_27_out, not_28_out, not_29_out, not_30_out, not_31_out, not_32_out, not_33_out, not_34_out,
       not_35_out, not_36_out, not_37_out, not_38_out, not_39_out, not_40_out, not_41_out, not_42_out,
       not_43_out, not_44_out, not_45_out, not_46_out, not_47_out, not_48_out, not_49_out, not_50_out,
       not_51_out, not_52_out, not_53_out, not_54_out, not_55_out, not_56_out, not_57_out, not_58_out,
       not_59_out, not_60_out, not_61_out, not_62_out, not_63_out, not_64_out, not_65_out, not_66_out,
       not_67_out, not_68_out, not_69_out, not_70_out, not_71_out, not_72_out, not_73_out, not_74_out,
       not_75_out, not_76_out, not_77_out, not_78_out, not_79_out, not_80_out, not_81_out, not_82_out,
       not_83_out, not_84_out, not_85_out, not_86_out, not_87_out, not_88_out, not_89_out, not_90_out,
       not_91_out, not_92_out, not_93_out, not_94_out, not_95_out, not_96_out, not_97_out, not_98_out,
       not_99_out, not_100_out, not_101_out, not_102_out, not_103_out, not_104_out, not_105_out, not_106_out,
       not_107_out, not_108_out, not_109_out, not_110_out, not_111_out, not_112_out, not_113_out,
       not_114_out, not_115_out, not_116_out, not_117_out, not_118_out, not_119_out, not_120_out,
       not_121_out, not_122_out, not_123_out, not_124_out, not_125_out, not_126_out, not_127_out,
       not_128_out, not_129_out, not_130_out, not_131_out, not_132_out, not_133_out, not_134_out,
       not_135_out, not_136_out, not_137_out, not_138_out, not_139_out, not_140_out, not_141_out,
       not_142_out, not_143_out, not_144_out, not_145_out, not_146_out, not_147_out, not_148_out,
       not_149_out, not_150_out, not_151_out, not_152_out, not_153_out, not_154_out, not_155_out,
       not_156_out, not_157_out, not_158_out, not_159_out, not_160_out, not_161_out, not_162_out,
       not_163_out, not_164_out, not_165_out, not_166_out, not_167_out, not_168_out, not_169_out,
       not_170_out, not_171_out, not_172_out, not_173_out, not_174_out, not_175_out, not_176_out,
       not_177_out, not_178_out, not_179_out, not_180_out, not_181_out, not_182_out, not_183_out,
       not_184_out, not_185_out, not_186_out, not_187_out, not_188_out, not_189_out, not_190_out,
       not_191_out, not_192_out, not_193_out, not_194_out, not_195_out, not_196_out, not_197_out,
       not_198_out, not_199_out, not_200_out, not_201_out, not_202_out, not_203_out, not_204_out,
       not_205_out, not_206_out, not_207_out, not_208_out, not_209_out, not_210_out, not_211_out,
       not_212_out, not_213_out, not_214_out, not_215_out, not_216_out, not_217_out, not_218_out,
       not_219_out, not_220_out, not_221_out, not_222_out, not_223_out, not_224_out, not_225_out,
       not_226_out, not_227_out, not_228_out, not_229_out, not_230_out, not_231_out, not_232_out,
       not_233_out, not_234_out;

  not not_1 (not_1_out, OP2);
  not not_2 (not_2_out, OP3);
  not not_3 (not_3_out, OP4);
  not not_4 (not_4_out, OP0);
  not not_5 (not_5_out, OP1);
  not not_6 (not_6_out, OP2);
  not not_7 (not_7_out, OP4);
  not not_8 (not_8_out, OP2);
  not not_9 (not_9_out, OP4);
  not not_10 (not_10_out, OP5);
  not not_11 (not_11_out, OP4);
  not not_12 (not_12_out, OP2);
  not not_13 (not_13_out, OP1);
  not not_14 (not_14_out, OP0);
  not not_15 (not_15_out, OP5);
  not not_16 (not_16_out, OP4);
  not not_17 (not_17_out, OP1);
  not not_18 (not_18_out, OP0);
  not not_19 (not_19_out, OP5);
  not not_20 (not_20_out, OP4);
  not not_21 (not_21_out, OP2);
  not not_22 (not_22_out, OP1);
  not not_23 (not_23_out, OP5);
  not not_24 (not_24_out, OP4);
  not not_25 (not_25_out, OP2);
  not not_26 (not_26_out, OP0);
  not not_27 (not_27_out, OP5);
  not not_28 (not_28_out, OP4);
  not not_29 (not_29_out, OP1);
  not not_30 (not_30_out, OP4);
  not not_31 (not_31_out, OP3);
  not not_32 (not_32_out, OP2);
  not not_33 (not_33_out, OP4);
  not not_34 (not_34_out, OP2);
  not not_35 (not_35_out, OP5);
  not not_36 (not_36_out, OP4);
  not not_37 (not_37_out, OP0);
  not not_38 (not_38_out, OP4);
  not not_39 (not_39_out, OP2);
  not not_40 (not_40_out, OP1);
  not not_41 (not_41_out, OP0);
  not not_42 (not_42_out, OP0);
  not not_43 (not_43_out, OP1);
  not not_44 (not_44_out, OP2);
  not not_45 (not_45_out, OP4);
  not not_46 (not_46_out, OP5);
  not not_47 (not_47_out, F0);
  not not_48 (not_48_out, F1);
  not not_49 (not_49_out, F3);
  not not_50 (not_50_out, F4);
  not not_51 (not_51_out, OP0);
  not not_52 (not_52_out, OP1);
  not not_53 (not_53_out, OP2);
  not not_54 (not_54_out, OP4);
  not not_55 (not_55_out, OP5);
  not not_56 (not_56_out, F0);
  not not_57 (not_57_out, F2);
  not not_58 (not_58_out, F3);
  not not_59 (not_59_out, F4);
  not not_60 (not_60_out, OP0);
  not not_61 (not_61_out, OP1);
  not not_62 (not_62_out, OP2);
  not not_63 (not_63_out, OP4);
  not not_64 (not_64_out, OP5);
  not not_65 (not_65_out, F1);
  not not_66 (not_66_out, F3);
  not not_67 (not_67_out, F4);
  not not_68 (not_68_out, OP0);
  not not_69 (not_69_out, OP1);
  not not_70 (not_70_out, OP2);
  not not_71 (not_71_out, OP4);
  not not_72 (not_72_out, OP5);
  not not_73 (not_73_out, F2);
  not not_74 (not_74_out, F3);
  not not_75 (not_75_out, F4);
  not not_76 (not_76_out, F5);
  not not_77 (not_77_out, OP0);
  not not_78 (not_78_out, OP1);
  not not_79 (not_79_out, OP2);
  not not_80 (not_80_out, OP4);
  not not_81 (not_81_out, OP5);
  not not_82 (not_82_out, F2);
  not not_83 (not_83_out, F4);
  not not_84 (not_84_out, OP0);
  not not_85 (not_85_out, OP1);
  not not_86 (not_86_out, OP2);
  not not_87 (not_87_out, OP4);
  not not_88 (not_88_out, OP5);
  not not_89 (not_89_out, F3);
  not not_90 (not_90_out, F4);
  not not_91 (not_91_out, OP0);
  not not_92 (not_92_out, OP4);
  not not_93 (not_93_out, OP5);
  not not_94 (not_94_out, OP1);
  not not_95 (not_95_out, OP4);
  not not_96 (not_96_out, OP5);
  not not_97 (not_97_out, OP2);
  not not_98 (not_98_out, OP3);
  not not_99 (not_99_out, OP4);
  not not_100 (not_100_out, OP0);
  not not_101 (not_101_out, OP1);
  not not_102 (not_102_out, OP2);
  not not_103 (not_103_out, OP3);
  not not_104 (not_104_out, OP4);
  not not_105 (not_105_out, OP5);
  not not_106 (not_106_out, F0);
  not not_107 (not_107_out, F1);
  not not_108 (not_108_out, F4);
  not not_109 (not_109_out, F5);
  not not_110 (not_110_out, OP0);
  not not_111 (not_111_out, OP1);
  not not_112 (not_112_out, OP2);
  not not_113 (not_113_out, OP4);
  not not_114 (not_114_out, OP0);
  not not_115 (not_115_out, OP2);
  not not_116 (not_116_out, OP4);
  not not_117 (not_117_out, OP5);
  not not_118 (not_118_out, OP1);
  not not_119 (not_119_out, OP2);
  not not_120 (not_120_out, OP4);
  not not_121 (not_121_out, OP5);
  not not_122 (not_122_out, OP2);
  not not_123 (not_123_out, OP4);
  not not_124 (not_124_out, OP0);
  not not_125 (not_125_out, OP1);
  not not_126 (not_126_out, OP2);
  not not_127 (not_127_out, OP3);
  not not_128 (not_128_out, OP4);
  not not_129 (not_129_out, OP5);
  not not_130 (not_130_out, F0);
  not not_131 (not_131_out, F1);
  not not_132 (not_132_out, F3);
  not not_133 (not_133_out, F4);
  not not_134 (not_134_out, OP0);
  not not_135 (not_135_out, OP1);
  not not_136 (not_136_out, OP2);
  not not_137 (not_137_out, OP3);
  not not_138 (not_138_out, OP4);
  not not_139 (not_139_out, OP5);
  not not_140 (not_140_out, F0);
  not not_141 (not_141_out, F2);
  not not_142 (not_142_out, F3);
  not not_143 (not_143_out, F4);
  not not_144 (not_144_out, OP0);
  not not_145 (not_145_out, OP1);
  not not_146 (not_146_out, OP2);
  not not_147 (not_147_out, OP3);
  not not_148 (not_148_out, OP4);
  not not_149 (not_149_out, OP5);
  not not_150 (not_150_out, F1);
  not not_151 (not_151_out, F3);
  not not_152 (not_152_out, F4);
  not not_153 (not_153_out, OP0);
  not not_154 (not_154_out, OP1);
  not not_155 (not_155_out, OP2);
  not not_156 (not_156_out, OP3);
  not not_157 (not_157_out, OP4);
  not not_158 (not_158_out, OP5);
  not not_159 (not_159_out, F2);
  not not_160 (not_160_out, F3);
  not not_161 (not_161_out, F4);
  not not_162 (not_162_out, F5);
  not not_163 (not_163_out, OP0);
  not not_164 (not_164_out, OP1);
  not not_165 (not_165_out, OP2);
  not not_166 (not_166_out, OP3);
  not not_167 (not_167_out, OP4);
  not not_168 (not_168_out, OP5);
  not not_169 (not_169_out, F2);
  not not_170 (not_170_out, F4);
  not not_171 (not_171_out, OP0);
  not not_172 (not_172_out, OP1);
  not not_173 (not_173_out, OP2);
  not not_174 (not_174_out, OP3);
  not not_175 (not_175_out, OP4);
  not not_176 (not_176_out, OP5);
  not not_177 (not_177_out, F3);
  not not_178 (not_178_out, F4);
  not not_179 (not_179_out, OP0);
  not not_180 (not_180_out, OP1);
  not not_181 (not_181_out, OP3);
  not not_182 (not_182_out, OP4);
  not not_183 (not_183_out, OP5);
  not not_184 (not_184_out, OP1);
  not not_185 (not_185_out, OP3);
  not not_186 (not_186_out, OP4);
  not not_187 (not_187_out, OP5);
  not not_188 (not_188_out, OP0);
  not not_189 (not_189_out, OP1);
  not not_190 (not_190_out, OP2);
  not not_191 (not_191_out, OP3);
  not not_192 (not_192_out, OP4);
  not not_193 (not_193_out, OP5);
  not not_194 (not_194_out, F0);
  not not_195 (not_195_out, F1);
  not not_196 (not_196_out, F2);
  not not_197 (not_197_out, F4);
  not not_198 (not_198_out, F5);
  not not_199 (not_199_out, OP0);
  not not_200 (not_200_out, OP2);
  not not_201 (not_201_out, OP3);
  not not_202 (not_202_out, OP4);
  not not_203 (not_203_out, OP5);
  not not_204 (not_204_out, F0);
  not not_205 (not_205_out, F1);
  not not_206 (not_206_out, F2);
  not not_207 (not_207_out, F4);
  not not_208 (not_208_out, F5);
  not not_209 (not_209_out, OP2);
  not not_210 (not_210_out, OP3);
  not not_211 (not_211_out, OP4);
  not not_212 (not_212_out, OP5);
  not not_213 (not_213_out, OP2);
  not not_214 (not_214_out, OP3);
  not not_215 (not_215_out, OP4);
  not not_216 (not_216_out, OP5);
  not not_217 (not_217_out, OP0);
  not not_218 (not_218_out, OP1);
  not not_219 (not_219_out, OP2);
  not not_220 (not_220_out, OP3);
  not not_221 (not_221_out, OP4);
  not not_222 (not_222_out, OP5);
  not not_223 (not_223_out, F0);
  not not_224 (not_224_out, F1);
  not not_225 (not_225_out, F3);
  not not_226 (not_226_out, F4);
  not not_227 (not_227_out, F5);
  not not_228 (not_228_out, OP3);
  not not_229 (not_229_out, OP4);
  not not_230 (not_230_out, OP5);
  not not_231 (not_231_out, OP0);
  not not_232 (not_232_out, OP1);
  not not_233 (not_233_out, OP2);
  not not_234 (not_234_out, OP4);
  and and_1 (MemToReg, OP0, OP1, not_1_out, not_2_out, not_3_out, OP5);
  and and_2 (and_2_out, not_4_out, not_5_out, not_6_out, OP3, not_7_out, OP5);
  and and_3 (and_3_out, OP0, OP1, not_8_out, OP3, not_9_out, OP5);
  and and_4 (and_4_out, not_10_out, not_11_out, OP3, not_12_out, not_13_out, not_14_out);
  and and_5 (and_5_out, not_15_out, not_16_out, OP3, OP2, not_17_out, not_18_out);
  and and_6 (and_6_out, not_19_out, not_20_out, OP3, not_21_out, not_22_out, OP0);
  and and_7 (and_7_out, not_23_out, not_24_out, OP3, not_25_out, OP1, not_26_out);
  and and_8 (and_8_out, not_27_out, not_28_out, OP3, OP2, not_29_out, OP0);
  and and_9 (and_9_out, OP5, not_30_out, not_31_out, not_32_out, OP1, OP0);
  and and_10 (and_10_out, OP5, not_33_out, OP3, not_34_out, OP1, OP0);
  and and_11 (and_11_out, not_35_out, not_36_out, OP3, OP2, OP1, not_37_out);
  and and_12 (and_12_out, OP5, not_38_out, OP3, not_39_out, not_40_out, not_41_out);
  and and_13 (and_13_out, not_42_out, not_43_out, not_44_out, not_45_out, not_46_out, not_47_out, not_48_out, not_49_out, not_50_out);
  and and_14 (and_14_out, not_51_out, not_52_out, not_53_out, not_54_out, not_55_out, not_56_out, not_57_out, not_58_out, not_59_out);
  and and_15 (and_15_out, not_60_out, not_61_out, not_62_out, not_63_out, not_64_out, not_65_out, not_66_out, not_67_out, F5);
  and and_16 (and_16_out, not_68_out, not_69_out, not_70_out, not_71_out, not_72_out, F1, not_73_out, not_74_out, not_75_out, not_76_out);
  and and_17 (and_17_out, not_77_out, not_78_out, not_79_out, not_80_out, not_81_out, F1, not_82_out, F3, not_83_out, F5);
  and and_18 (and_18_out, not_84_out, not_85_out, not_86_out, not_87_out, not_88_out, F0, F2, not_89_out, not_90_out, F5);
  and and_19 (and_19_out, not_91_out, OP3, not_92_out, not_93_out);
  and and_20 (and_20_out, not_94_out, OP3, not_95_out, not_96_out);
  and and_21 (and_21_out, OP0, OP1, not_97_out, not_98_out, not_99_out);
  and and_22 (SysCALL, not_100_out, not_101_out, not_102_out, not_103_out, not_104_out, not_105_out, not_106_out, not_107_out, F2, F3, not_108_out, not_109_out);
  and and_23 (and_23_out, not_110_out, not_111_out, not_112_out, OP3, not_113_out);
  and and_24 (and_24_out, not_114_out, not_115_out, OP3, not_116_out, not_117_out);
  and and_25 (and_25_out, not_118_out, not_119_out, OP3, not_120_out, not_121_out);
  and and_26 (and_26_out, OP0, OP1, not_122_out, not_123_out, OP5);
  and and_27 (and_27_out, not_124_out, not_125_out, not_126_out, not_127_out, not_128_out, not_129_out, not_130_out, not_131_out, not_132_out, not_133_out);
  and and_28 (and_28_out, not_134_out, not_135_out, not_136_out, not_137_out, not_138_out, not_139_out, not_140_out, not_141_out, not_142_out, not_143_out);
  and and_29 (and_29_out, not_144_out, not_145_out, not_146_out, not_147_out, not_148_out, not_149_out, not_150_out, not_151_out, not_152_out, F5);
  and and_30 (and_30_out, not_153_out, not_154_out, not_155_out, not_156_out, not_157_out, not_158_out, F1, not_159_out, not_160_out, not_161_out, not_162_out);
  and and_31 (and_31_out, not_163_out, not_164_out, not_165_out, not_166_out, not_167_out, not_168_out, F1, not_169_out, F3, not_170_out, F5);
  and and_32 (and_32_out, not_171_out, not_172_out, not_173_out, not_174_out, not_175_out, not_176_out, F0, F2, not_177_out, not_178_out, F5);
  and and_33 (BEQ, not_179_out, not_180_out, OP2, not_181_out, not_182_out, not_183_out);
  and and_34 (BNE, OP0, not_184_out, OP2, not_185_out, not_186_out, not_187_out);
  and and_35 (JR, not_188_out, not_189_out, not_190_out, not_191_out, not_192_out, not_193_out, not_194_out, not_195_out, not_196_out, F3, not_197_out, not_198_out);
  and and_36 (and_36_out, not_199_out, not_200_out, not_201_out, not_202_out, not_203_out, not_204_out, not_205_out, not_206_out, F3, not_207_out, not_208_out);
  and and_37 (and_37_out, OP1, not_209_out, not_210_out, not_211_out, not_212_out);
  and and_38 (JAL, OP0, OP1, not_213_out, not_214_out, not_215_out, not_216_out);
  and and_39 (SLLV, not_217_out, not_218_out, not_219_out, not_220_out, not_221_out, not_222_out, not_223_out, not_224_out, F2, not_225_out, not_226_out, not_227_out);
  and and_40 (BGTZ, OP0, OP1, OP2, not_228_out, not_229_out, not_230_out);
  and and_41 (SB, not_231_out, not_232_out, not_233_out, OP3, not_234_out, OP5);
  or or_1 (MemWrite, and_2_out, and_3_out);
  or or_2 (ALU_SRC, and_4_out, and_5_out, and_6_out, and_7_out, and_8_out, and_9_out, and_10_out, and_11_out, and_12_out);
  or or_3 (RegWrite, and_13_out, and_14_out, and_15_out, and_16_out, and_17_out, and_18_out, and_19_out, and_20_out, and_21_out);
  or or_4 (SignedExt, and_23_out, and_24_out, and_25_out, and_26_out);
  or or_5 (RegDst, and_27_out, and_28_out, and_29_out, and_30_out, and_31_out, and_32_out);
  or or_6 (JUMP, and_36_out, and_37_out);
endmodule

// ALU
module MIPS_ALU (
  input  [4:0] shamt,
  input  [31:0] X,
  input  [31:0] Y,
  input  [3:0] AluOP,
  output Equal,
  output [31:0] Result,
  output [31:0] Result_2
);

  wire [0:0] comparator_1_lt, comparator_2_lt;
  wire [31:0] adder_1_out, AND_out, divider_1_out, divider_1_rem, multiplier_1_cout, multiplier_1_out,
       NOR_out, OR_out, shifter_1_out, shifter_2_out, shifter_3_out, subtractor_1_out, XOR_out;

  assign AND_out = X & Y;  // AND_Gate AND, 32 bits wide
  assign OR_out = X | Y;  // OR_Gate OR, 32 bits wide
  Shifter #(.width(32), .shift("ll")) shifter_1 (.in(Y), .\dist (shamt), .out(shifter_1_out));
  Shifter #(.width(32), .shift("ar")) shifter_2 (.in(Y), .\dist (shamt), .out(shifter_2_out));
  Shifter #(.width(32), .shift("lr")) shifter_3 (.in(Y), .\dist (shamt), .out(shifter_3_out));
  Multiplier #(.width(32)) multiplier_1 (.a(X), .b(Y), .out(multiplier_1_out), .cout(multiplier_1_cout));  // open: cin
  Divider #(.width(32)) divider_1 (.a(X), .b(Y), .out(divider_1_out), .rem(divider_1_rem));  // open: upper
  Adder #(.width(32)) adder_1 (.a(X), .b(Y), .out(adder_1_out));  // open: cin, cout
  Subtractor #(.width(32)) subtractor_1 (.a(X), .b(Y), .out(subtractor_1_out));  // open: bin, bout
  assign XOR_out = X ^ Y;  // XOR_Gate XOR, 32 bits wide
  assign NOR_out = ~(X | Y);  // NOR_Gate NOR, 32 bits wide
  Comparator #(.width(32), .mode("twosComplement")) comparator_1 (
    .a(X), .b(Y), .eq(Equal), .lt(comparator_1_lt[0]));  // open: gt
  Comparator #(.width(32), .mode("unsigned")) comparator_2 (.a(X), .b(Y), .lt(comparator_2_lt[0]));  // open: gt, eq
  Multiplexer #(.select(4), .width(32), .disabled("Z"), .enable("false")) multiplexer_1 (
    .in0(shifter_1_out), .in1(shifter_2_out), .in2(shifter_3_out), .in3(multiplier_1_out),
    .in4(divider_1_out), .in5(adder_1_out), .in6(subtractor_1_out), .in7(AND_out), .in8(OR_out),
    .in9(XOR_out), .in10(NOR_out), .in11({{31{1'b0}}, comparator_1_lt[0]}),
    .in12({{31{1'b0}}, comparator_2_lt[0]}), .in13({32{1'b0}}), .in14({32{1'b0}}), .in15({32{1'b0}}),
    .out(Result), .sel(AluOP));
  Multiplexer #(.select(4), .width(32), .disabled("Z"), .enable("false")) multiplexer_2 (
    .in0({32{1'b0}}), .in1({32{1'b0}}), .in2({32{1'b0}}), .in3(multiplier_1_cout), .in4(divider_1_rem),
    .in5({32{1'b0}}), .in6({32{1'b0}}), .in7({32{1'b0}}), .in8({32{1'b0}}), .in9({32{1'b0}}),
    .in10({32{1'b0}}), .in11({32{1'b0}}), .in12({32{1'b0}}), .in13({32{1'b0}}), .in14({32{1'b0}}),
    .in15({32{1'b0}}), .out(Result_2), .sel(AluOP));

  // Other names for the same wires on the sheet: Result2[31:0] = Result_2; S[3:0] = AluOP

  // Notes on the sheet:
  //   不要改变此引脚区域内容，也不要改变ALU封装形式
  //   输入引脚
  //   输出引脚
endmodule

module MIPS_Regifile (
  input  [31:0] Din,
  input  Clk,
  input  WE,
  input  [4:0] R1_num,
  input  [4:0] W_num,
  input  [4:0] R2_num,
  output [31:0] R1,
  output [31:0] R2
);

  // RegisterFile registerfile_1: pin names not known; wires that end beside it: Din, Clk, WE, W_num, R1_num, R2_num, R1, R2
endmodule

module \理想流水线  (
  output RegWrite,
  output MemWrite,
  output [31:0] IF_PC,
  output [31:0] ID_PC,
  output [31:0] EX_PC,
  output [31:0] M_PC,
  output [31:0] WB_PC,
  output [31:0] RDin,
  output [31:0] MDin,
  output [31:0] LedData
);

  wire and_3_out, and_4_out, and_5_out, Beq, BGTZ, Bne, BranchTaken, CLK, clock_1_out, clock_2_out,
       comparator_1_eq, comparator_1_lt, comparator_2_eq, comparator_3_gt, d_ff_1_q, En, Equal,
       ex_mem_1_jal_2, ex_mem_1_memtoreg_2, ex_mem_1_regwrite_2, ex_mem_1_syscall_2, Go, Halt,
       id_ex_1_alusrcb_2, id_ex_1_jal_2, id_ex_1_memtoreg_2, id_ex_1_memwrite_2, id_ex_1_regwrite_2,
       id_ex_1_sb_2, id_ex_1_syscall_2, IR1, IR2, IR3, JAL, LED_EN, MemToReg, nand_1_out, not_1_out, RegDst,
       RST, SB, SignedExt, SLLV, Syscall, W1, W2, W3, \单周期硬布线控制器_1_alu_src , \单周期硬布线控制器_1_beq ,
       \单周期硬布线控制器_1_bgtz , \单周期硬布线控制器_1_bne , \单周期硬布线控制器_1_jal , \单周期硬布线控制器_1_memtoreg ,
       \单周期硬布线控制器_1_memwrite , \单周期硬布线控制器_1_regwrite , \单周期硬布线控制器_1_sb , \单周期硬布线控制器_1_signedext ,
       \单周期硬布线控制器_1_sllv , \单周期硬布线控制器_1_syscall ;
  wire [3:0] id_ex_1_aluop_2, \单周期硬布线控制器_1_alu_op ;
  wire [4:0] ex_mem_1_writereg_num_2, id_ex_1_writereg_num_2, multiplexer_2_out, multiplexer_3_out,
       multiplexer_4_out, multiplexer_7_out, W_num;
  wire [12:0] CNT_num;
  wire [15:0] \LoadUse次数 , \总周期数 , \插入气泡数 , \无条件分支数 , \条件分支成功数 ;
  wire [27:0] id_ex_1_pc_4_2;
  wire [31:0] A0, adder_1_out, bit_extender_1_out, bit_extender_2_out, BranchAddr, EX_IR, ex_mem_1_result_2,
       GPRrs, GPRrt, id_ex_1_rt_2, ID_IR, if_id_1_pc_4_2, IF_IR, JRAddr, MEM_IR, mem_wb_1_memdata_2,
       mem_wb_1_result_2, mips_alu_1_result, multiplexer_1_out, multiplexer_5_out, multiplexer_6_out,
       multiplexer_9_out, PC_4, ram_1_data, shifter_1_out, WB_IR, \按字节存储电路_1_ddata ;
  wire [31:28] JMPAddr;

  Button \u_总复位  (.out(RST));
  Button _1 (.out(IR1));
  Button _2 (.out(IR2));
  Button _3 (.out(IR3));
  // Probe on \总周期数 
  // Probe on \总周期数 
  Button \u_继续运行  (.out(Go));
  LED #(.active("true")) led_1 (.in(W1));
  LED #(.active("true")) led_2 (.in(W2));
  LED #(.active("true")) led_3 (.in(W3));
  Hex_Digit_Display hex_digit_display_1 (.value(LedData[31:28]));  // open: dp
  // Probe on IF_PC[19:0]
  // Mips_Probe mips_probe_1: pin names not known; wires that end beside it: IF_IR
  not not_1 (not_1_out, Halt);
  or or_1 (En, not_1_out, Go);
  Multiplexer #(.select(1), .width(32), .disabled("Z"), .enable("false")) multiplexer_1 (
    .in0(adder_1_out), .in1(BranchAddr), .out(multiplexer_1_out), .sel(BranchTaken));
  Hex_Digit_Display hex_digit_display_2 (.value(LedData[27:24]));  // open: dp
  Hex_Digit_Display hex_digit_display_3 (.value(LedData[23:20]));  // open: dp
  // Probe on ID_PC[19:0]
  // Mips_Probe mips_probe_2: pin names not known; wires that end beside it: ID_IR
  Register #(.width(32), .trigger("rising"), .Select("low")) PC (
    .D(multiplexer_1_out), .en(En), .Q(IF_PC), .clk(CLK), .clr(RST));
  Hex_Digit_Display hex_digit_display_4 (.value(LedData[19:16]));  // open: dp
  Hex_Digit_Display hex_digit_display_5 (.value(LedData[15:12]));  // open: dp
  Hex_Digit_Display hex_digit_display_6 (.value(LedData[11:8]));  // open: dp
  Hex_Digit_Display hex_digit_display_7 (.value(LedData[7:4]));  // open: dp
  Clock #(.highDuration(1), .lowDuration(1)) clock_1 (.out(clock_1_out));
  // Probe on EX_PC[19:0]
  // Mips_Probe mips_probe_3: pin names not known; wires that end beside it: clock_1_out, EX_IR, CLK
  Counter #(.width(16), .max('hffff), .ongoal("wrap"), .trigger("rising"), .behavior("new")) counter_1 (
    .count(En), .Q(\总周期数 ), .clk(CLK), .clr(RST));  // open: load, D, carry, preset, down
  Adder #(.width(32)) adder_1 (.a(IF_PC), .b(32'h4), .out(adder_1_out), .cin(1'b0));  // open: cout
  Hex_Digit_Display hex_digit_display_8 (.value(LedData[3:0]));  // open: dp
  ROM #(.addrWidth(10), .dataWidth(32), .Select("high")) rom_1 (.addr(IF_PC[11:2]), .data(IF_IR));
  // Probe on \总周期数 
  // Probe on M_PC[19:0]
  // Mips_Probe mips_probe_4: pin names not known; wires that end beside it: MEM_IR
  IF_ID if_id_1 (
    .PC(IF_PC), .IR(IF_IR), .PC_4(adder_1_out), .PC_2(ID_PC), .IR_2(ID_IR), .PC_4_2(if_id_1_pc_4_2),
    .Clk(CLK), .\异步清0 (RST), .EN(En));  // open: PredictJump_2, 同步清0, PredictJump
  // Probe on \总周期数 
  // Probe on \无条件分支数 
  // Probe on \条件分支成功数 
  // Probe on \插入气泡数 
  // Probe on \LoadUse次数 
  // Mips_Probe mips_probe_5: pin names not known; wires that end beside it: ID_IR
  // Probe on IF_PC[11:0]
  // Probe on WB_PC[19:0]
  // Mips_Probe mips_probe_6: pin names not known; wires that end beside it: WB_IR
  // Probe on EX_PC[11:0]
  // Probe on ID_PC[11:0]
  D_Flip_Flop #(.trigger("high"), .Pre_Clr_Positions("LEGACY"), .NegatePresetClear("false"), .enable("true"), .NewFFLayout("false")) d_ff_1 (.Q(d_ff_1_q));  // open: clk, D, Qn, preset, en, reset
  Multiplexer #(.select(1), .width(5), .disabled("Z"), .enable("false")) multiplexer_2 (
    .in0(ID_IR[20:16]), .in1(ID_IR[15:11]), .out(multiplexer_2_out), .sel(RegDst));
  // Probe on M_PC[11:0]
  // Probe on 13'h12
  Multiplexer #(.select(1), .width(5), .disabled("Z"), .enable("false")) multiplexer_3 (
    .in0(ID_IR[25:21]), .in1(5'b00010), .out(multiplexer_3_out), .sel(Syscall));
  Multiplexer #(.select(1), .width(5), .disabled("Z"), .enable("false")) multiplexer_4 (
    .in0(ID_IR[20:16]), .in1(5'b00100), .out(multiplexer_4_out), .sel(Syscall));
  // Probe on WB_PC[11:0]
  Comparator #(.width(13), .mode("twosComplement")) comparator_1 (
    .a(CNT_num), .b(13'h12), .eq(comparator_1_eq), .lt(comparator_1_lt));  // open: gt
  Clock #(.highDuration(1), .lowDuration(1)) clock_2 (.out(clock_2_out));
  \单周期硬布线控制器  \u_单周期硬布线控制器_1  (
    .Func(ID_IR[5:0]), .OP(ID_IR[31:26]), .ALU_OP(\单周期硬布线控制器_1_alu_op ), .MemToReg(\单周期硬布线控制器_1_memtoreg ),
    .MemWrite(\单周期硬布线控制器_1_memwrite ), .ALU_SRC(\单周期硬布线控制器_1_alu_src ), .RegWrite(\单周期硬布线控制器_1_regwrite ),
    .SysCALL(\单周期硬布线控制器_1_syscall ), .SignedExt(\单周期硬布线控制器_1_signedext ), .RegDst(RegDst),
    .Beq(\单周期硬布线控制器_1_beq ), .JAL(\单周期硬布线控制器_1_jal ), .Bne(\单周期硬布线控制器_1_bne ), .SB(\单周期硬布线控制器_1_sb ),
    .BGTZ(\单周期硬布线控制器_1_bgtz ), .SLLV(\单周期硬布线控制器_1_sllv ));  // open: JR, JMP
  nand nand_1 (nand_1_out, d_ff_1_q, comparator_1_eq);
  Counter #(.width(13), .max('h1fff), .ongoal("stay"), .trigger("rising"), .behavior("old")) counter_2 (
    .count(comparator_1_lt), .Q(CNT_num), .clk(clock_2_out), .clr(RST));  // open: load, D, carry, preset
  fall_regfile fall_regfile_1 (
    .Din(RDin), .Clk(CLK), .R1(JRAddr), .R2(A0), .WE(RegWrite), .W_num(W_num), .R1_num(multiplexer_3_out),
    .R2_num(multiplexer_4_out));
  assign CLK = nand_1_out ? clock_2_out : 1'bz;  // Controlled_Buffer controlled_buffer_1
  Pull_Resistor #(.pull(1)) pull_resistor_1 (.node(CLK));
  ID_EX id_ex_1 (
    .SignEXt(\单周期硬布线控制器_1_signedext ), .Beq(\单周期硬布线控制器_1_beq ), .Bne(\单周期硬布线控制器_1_bne ),
    .MemToReg(\单周期硬布线控制器_1_memtoreg ), .MemWrite(\单周期硬布线控制器_1_memwrite ), .AluOP(\单周期硬布线控制器_1_alu_op ),
    .AluSrcB(\单周期硬布线控制器_1_alu_src ), .RegWrite(\单周期硬布线控制器_1_regwrite ), .PC(ID_PC), .IR(ID_IR), .RS(JRAddr),
    .RT(A0), .WriteReg_num(multiplexer_2_out), .PC_4(if_id_1_pc_4_2), .SignEXt_2(SignedExt), .Beq_2(Beq),
    .Bne_2(Bne), .MemToReg_2(id_ex_1_memtoreg_2), .MemWrite_2(id_ex_1_memwrite_2), .AluOP_2(id_ex_1_aluop_2),
    .AluSrcB_2(id_ex_1_alusrcb_2), .RegWrite_2(id_ex_1_regwrite_2), .PC_2(EX_PC), .IR_2(EX_IR), .RS_2(GPRrs),
    .RT_2(id_ex_1_rt_2), .WriteReg_num_2(id_ex_1_writereg_num_2), .PC_4_2({JMPAddr, id_ex_1_pc_4_2}),
    .Clk(CLK), .\异步清0 (RST), .JAL(\单周期硬布线控制器_1_jal ), .JAL_2(id_ex_1_jal_2), .EN(En),
    .BGTZ(\单周期硬布线控制器_1_bgtz ), .BGTZ_2(BGTZ), .SLLV(\单周期硬布线控制器_1_sllv ), .SLLV_2(SLLV),
    .SB(\单周期硬布线控制器_1_sb ), .SB_2(id_ex_1_sb_2), .syscall(\单周期硬布线控制器_1_syscall ), .syscall_2(id_ex_1_syscall_2));  // open: JMP, JR, JMP_2, JR_2, RT_F_2, RT_F, 同步清0, RS_F_2, RS_F, PredictJump, PredictJump_2
  assign bit_extender_1_out = {{16{1'b0}}, EX_IR[15:0]};  // Bit_Extender bit_extender_1
  assign bit_extender_2_out = {{16{EX_IR[15]}}, EX_IR[15:0]};  // Bit_Extender bit_extender_2
  Multiplexer #(.select(1), .width(32), .disabled("Z"), .enable("false")) multiplexer_5 (
    .in0(bit_extender_1_out), .in1(bit_extender_2_out), .out(multiplexer_5_out), .sel(SignedExt));
  Shifter #(.width(32), .shift("ll")) shifter_1 (.in(bit_extender_2_out), .\dist (5'b00010), .out(shifter_1_out));
  Multiplexer #(.select(1), .width(32), .disabled("Z"), .enable("false")) multiplexer_6 (
    .in0(id_ex_1_rt_2), .in1(multiplexer_5_out), .out(multiplexer_6_out), .sel(id_ex_1_alusrcb_2));
  Multiplexer #(.select(1), .width(5), .disabled("Z"), .enable("false")) multiplexer_7 (
    .in0(EX_IR[10:6]), .in1(GPRrs[4:0]), .out(multiplexer_7_out), .sel(SLLV));
  Adder #(.width(32)) adder_2 (
    .a(shifter_1_out), .b({JMPAddr, id_ex_1_pc_4_2}), .out(BranchAddr), .cin(1'b0));  // open: cout
  MIPS_ALU mips_alu_1 (
    .X(GPRrs), .Y(multiplexer_6_out), .AluOP(id_ex_1_aluop_2), .Equal(Equal), .Result(mips_alu_1_result),
    .shamt(multiplexer_7_out));  // open: Result_2
  EX_MEM ex_mem_1 (
    .MemToReg(id_ex_1_memtoreg_2), .RegWrite(id_ex_1_regwrite_2), .PC(EX_PC), .IR(EX_IR),
    .Result(mips_alu_1_result), .Writedata(id_ex_1_rt_2), .WriteReg_num(id_ex_1_writereg_num_2),
    .MemToReg_2(ex_mem_1_memtoreg_2), .RegWrite_2(ex_mem_1_regwrite_2), .PC_2(M_PC), .IR_2(MEM_IR),
    .Result_2(ex_mem_1_result_2), .Writedata_2(GPRrt), .WriteReg_num_2(ex_mem_1_writereg_num_2), .Clk(CLK),
    .Rst(RST), .MemWrite_2(MemWrite), .MemWrite(id_ex_1_memwrite_2), .JAL(id_ex_1_jal_2),
    .JAL_2(ex_mem_1_jal_2), .EN(En), .syscall_2(ex_mem_1_syscall_2), .syscall(id_ex_1_syscall_2),
    .SB(id_ex_1_sb_2), .SB_2(SB));  // open: JMP, JR, JMP_2, JR_2, R1_2, R1, 同步清0
  Comparator #(.width(32), .mode("twosComplement")) comparator_2 (
    .a(JRAddr), .b(32'ha), .eq(comparator_2_eq));  // open: gt, lt
  RAM #(.addrWidth(10), .dataWidth(32), .bus("separate"), .Select("high")) ram_1 (
    .addr(ex_mem_1_result_2[11:2]), .din(MDin), .data(ram_1_data), .str(MemWrite), .clk(CLK), .ld(1'b1),
    .clr(RST));  // open: sel
  and and_1 (Halt, Syscall, comparator_2_eq);
  and and_2 (LED_EN, ~comparator_2_eq, Syscall);  // AND_Gate
  \按字节存储电路  \u_按字节存储电路_1  (.cdata(GPRrt), .sel(ex_mem_1_result_2), .sdata(ram_1_data), .ddata(\按字节存储电路_1_ddata ));
  MEM_WB mem_wb_1 (
    .MemToReg(ex_mem_1_memtoreg_2), .RegWrite(ex_mem_1_regwrite_2), .PC(M_PC), .IR(MEM_IR),
    .Result(ex_mem_1_result_2), .Memdata(ram_1_data), .WriteReg_num(ex_mem_1_writereg_num_2),
    .MemToReg_2(MemToReg), .RegWrite_2(RegWrite), .PC_2(WB_PC), .IR_2(WB_IR), .Result_2(mem_wb_1_result_2),
    .Memdata_2(mem_wb_1_memdata_2), .WriteReg_num_2(W_num), .Clk(CLK), .Rst(RST), .JAL(ex_mem_1_jal_2),
    .JAL_2(JAL), .En(En), .syscall_2(Syscall), .syscall(ex_mem_1_syscall_2));  // open: JMP_2, JR_2, JMP, JR, 同步清0, R1_2, R1, R1_3, R2
  Multiplexer #(.select(1), .width(32), .disabled("Z"), .enable("false")) multiplexer_8 (
    .in0(GPRrt), .in1(\按字节存储电路_1_ddata ), .out(MDin), .sel(SB));
  Multiplexer #(.select(1), .width(32), .disabled("Z"), .enable("false")) multiplexer_9 (
    .in0(mem_wb_1_result_2), .in1(mem_wb_1_memdata_2), .out(multiplexer_9_out), .sel(MemToReg));
  Register #(.width(32), .trigger("rising"), .Select("low")) register_1 (
    .D(A0), .en(LED_EN), .Q(LedData), .clk(CLK));  // open: clr
  Multiplexer #(.select(1), .width(32), .disabled("Z"), .enable("false")) multiplexer_10 (
    .in0(multiplexer_9_out), .in1(PC_4), .out(RDin), .sel(JAL));
  // Probe on RDin
  Comparator #(.width(32), .mode("twosComplement")) comparator_3 (
    .a(GPRrs), .b({32{1'b0}}), .gt(comparator_3_gt));  // open: eq, lt
  and and_3 (and_3_out, Beq, Equal);
  and and_4 (and_4_out, ~Equal, Bne);  // AND_Gate
  and and_5 (and_5_out, comparator_3_gt, BGTZ);
  or or_2 (BranchTaken, and_3_out, and_4_out, and_5_out);

  // Other names for the same wires on the sheet: JMPAddr[27:2] = EX_IR[25:0]; shamt[4:0] = EX_IR[10:6];
  //   MEM_PC[31:0] = M_PC; PC[31:0] = IF_PC; V0[31:0] = JRAddr

  // Notes on the sheet:
  //   中断源
  //   时空图监测，可删除
  //   中断等待指示
  //   数码管输出
  //   指令存储器
  //   contents of rom_1 (hex, n*v repeats v):
  //   20100000 20110000 20120000 20130000 36100000 36310001 36520002 36730003 ae100000 ae110004 ae120008
  //   ae13000c 2002000a 20110000 20120000 20130000 c
  //   OP
  //   Func
  //   rs
  //   rt
  //   rd
  //   控制位
  //   流水调试日志用
  //   暂停节拍，不能为0
  //   SB
  //   JMP
  //   JR
  //   SignedExt
  //   SLLV
  //   OP
  //   Func
  //   Syscall
  //   BGTZ
  //   Beq
  //   Bne
  //   MemToReg
  //   MemWrite
  //   AluOP
  //   AluSrcB
  //   RegWrite
  //   JAL
  //   Regdst
  //   可计数暂停的时钟源
  //   shamt
  //   imm
  //   addr
  //   为方便自动评测，需要输出流水线各段保存的PC值，注意是PC不是PC+4，另外ID段寄存器写入信息，Mem段内存写入信息也要输出
  //   戳工具置1进入计数暂停模式，ctrl+k时钟自动运行到对应节拍暂停
  //   ctrl+k关闭时钟连续运行，将控制位置零，进入单步调试模式调试
  //   符号扩展
endmodule

module \重定向流水线  (
  output RegWrite,
  output MemWrite,
  output [31:0] IF_PC,
  output [31:0] ID_PC,
  output [31:0] EX_PC,
  output [31:0] M_PC,
  output [31:0] WB_PC,
  output [31:0] RDin,
  output [31:0] MDin,
  output [31:0] LedData
);

  wire and_1_out, and_2_out, and_4_out, and_5_out, and_6_out, and_7_out, Beq, BGTZ, Bne, BranchTaken, CLK,
       clock_1_out, clock_2_out, comparator_1_eq, comparator_1_lt, comparator_2_eq, comparator_3_gt, En,
       Equal, ex_mem_1_jal_2, ex_mem_1_memtoreg_2, ex_mem_1_syscall_2, EX_RegWrite, flush, Go, h_en, Halt,
       id_ex_1_alusrcb_2, id_ex_1_jal_2, id_ex_1_memwrite_2, id_ex_1_sb_2, id_ex_1_syscall_2, IR1, IR2, IR3,
       JAL, JMP, JR, MEM_RegWrite, MemRead, MemToReg, mips_probe_5_p3, nand_1_out, not_1_out, not_2_out,
       not_3_out, not_4_out, RegDst, RST, SB, SignedExt, SLLV, stall, Syscall, W1, W2, W3,
       \单周期硬布线控制器_1_alu_src , \单周期硬布线控制器_1_beq , \单周期硬布线控制器_1_bgtz , \单周期硬布线控制器_1_bne , \单周期硬布线控制器_1_jal ,
       \单周期硬布线控制器_1_jmp , \单周期硬布线控制器_1_jr , \单周期硬布线控制器_1_memtoreg , \单周期硬布线控制器_1_memwrite ,
       \单周期硬布线控制器_1_regwrite , \单周期硬布线控制器_1_sb , \单周期硬布线控制器_1_signedext , \单周期硬布线控制器_1_sllv ,
       \单周期硬布线控制器_1_syscall ;
  wire [1:0] id_ex_1_rs_f_2, id_ex_1_rt_f_2, RS_F, RT_F;
  wire [3:0] id_ex_1_aluop_2, \单周期硬布线控制器_1_alu_op ;
  wire [4:0] EX_W_num, MEM_W_num, mem_wb_1_writereg_num_2, multiplexer_2_out, multiplexer_3_out,
       multiplexer_4_out, multiplexer_9_out, W_num;
  wire [12:0] CNT_num;
  wire [15:0] \LoadUse次数 , \总周期数 , \插入气泡数 , \无条件分支数 , \条件分支成功数 ;
  wire [27:0] id_ex_1_pc_4_2;
  wire [31:0] A0, adder_1_out, adder_3_out, ALUresult, BAddr, bit_extender_1_out, bit_extender_2_out, EX_IR,
       ex_mem_1_r1_2, fall_regfile_1_r1, fall_regfile_1_r2, GPRrs, GPRrt, id_ex_1_rs_2, id_ex_1_rt_2, ID_IR,
       if_id_1_pc_4_2, IF_IR, MEM_IR, mem_wb_1_memdata_2, mem_wb_1_result_2, mips_alu_1_result,
       multiplexer_1_out, multiplexer_6_out, multiplexer_7_out, multiplexer_8_out, multiplexer_11_out,
       ram_1_data, shifter_1_out, V0, WB_IR, \按字节存储电路_1_ddata ;
  wire [31:28] JMPAddr;

  Button \u_总复位  (.out(RST));
  Button _1 (.out(IR1));
  Button _2 (.out(IR2));
  Button _3 (.out(IR3));
  // Probe on \总周期数 
  // Probe on \总周期数 
  Button \u_继续运行  (.out(Go));
  LED #(.active("true")) led_1 (.in(W1));
  LED #(.active("true")) led_2 (.in(W2));
  LED #(.active("true")) led_3 (.in(W3));
  not not_1 (not_1_out, Halt);
  not not_2 (not_2_out, stall);
  Counter #(.width(16), .max('hffff), .ongoal("wrap"), .trigger("rising"), .behavior("new")) counter_1 (
    .count(JMP), .Q(\无条件分支数 ), .clk(CLK), .clr(RST));  // open: load, D, carry, preset, down
  Hex_Digit_Display hex_digit_display_1 (.value(LedData[31:28]));  // open: dp
  // Probe on IF_PC[19:0]
  // Mips_Probe mips_probe_1: pin names not known; wires that end beside it: IF_IR
  and and_1 (and_1_out, not_1_out, not_2_out);
  Hex_Digit_Display hex_digit_display_2 (.value(LedData[23:20]));  // open: dp
  Hex_Digit_Display hex_digit_display_3 (.value(LedData[27:24]));  // open: dp
  // Probe on ID_PC[19:0]
  // Mips_Probe mips_probe_2: pin names not known; wires that end beside it: ID_IR
  or or_1 (En, and_1_out, Go);
  Hex_Digit_Display hex_digit_display_4 (.value(LedData[15:12]));  // open: dp
  Hex_Digit_Display hex_digit_display_5 (.value(LedData[19:16]));  // open: dp
  Multiplexer #(.select(3), .width(32), .disabled("Z"), .enable("false")) multiplexer_1 (
    .in0(adder_1_out), .in1(BAddr), .in3({JMPAddr, EX_IR[25:0], 2'b00}), .in7(GPRrs),
    .out(multiplexer_1_out), .sel({JR, JMP, BranchTaken}));  // open: in2, in4, in5, in6
  Hex_Digit_Display hex_digit_display_6 (.value(LedData[11:8]));  // open: dp
  Hex_Digit_Display hex_digit_display_7 (.value(LedData[7:4]));  // open: dp
  Clock #(.highDuration(1), .lowDuration(1)) clock_1 (.out(clock_1_out));
  // Probe on EX_PC[19:0]
  // Mips_Probe mips_probe_3: pin names not known; wires that end beside it: clock_1_out, EX_IR, CLK
  and and_2 (and_2_out, BranchTaken, ~JMP);  // AND_Gate
  Counter #(.width(16), .max('hffff), .ongoal("wrap"), .trigger("rising"), .behavior("new")) counter_2 (
    .count(and_2_out), .Q(\条件分支成功数 ), .clk(CLK), .clr(RST));  // open: load, D, carry, preset, down
  Hex_Digit_Display hex_digit_display_8 (.value(LedData[3:0]));  // open: dp
  Register #(.width(32), .trigger("rising"), .Select("low")) PC (
    .D(multiplexer_1_out), .en(En), .Q(IF_PC), .clk(CLK), .clr(RST));
  // Probe on \总周期数 
  // Probe on M_PC[19:0]
  // Mips_Probe mips_probe_4: pin names not known; wires that end beside it: MEM_IR
  not not_3 (not_3_out, Halt);
  Counter #(.width(16), .max('hffff), .ongoal("wrap"), .trigger("rising"), .behavior("new")) counter_3 (
    .count(not_3_out), .Q(\总周期数 ), .clk(CLK), .clr(RST));  // open: load, D, carry, preset, down
  // Probe on \总周期数 
  // Probe on \无条件分支数 
  // Probe on \条件分支成功数 
  // Probe on \插入气泡数 
  // Probe on \LoadUse次数 
  Adder #(.width(32)) adder_1 (.a(IF_PC), .b(32'h4), .out(adder_1_out), .cin(1'b0));  // open: cout
  // Probe on IF_PC[11:0]
  // Probe on WB_PC[19:0]
  // Mips_Probe mips_probe_5: pin names not known; wires that end beside it: stall, WB_IR, mips_probe_5_p3
  Counter #(.width(16), .max('hffff), .ongoal("wrap"), .trigger("rising"), .behavior("new")) counter_4 (
    .count(stall), .Q(\插入气泡数 ), .clk(CLK), .clr(RST));  // open: load, D, carry, preset, down
  ROM #(.addrWidth(10), .dataWidth(32), .Select("high")) rom_1 (.addr(IF_PC[11:2]), .data(IF_IR));
  // Probe on ID_PC[11:0]
  // Probe on EX_PC[11:0]
  IF_ID if_id_1 (
    .PC(IF_PC), .IR(IF_IR), .PC_4(adder_1_out), .PC_2(ID_PC), .IR_2(ID_IR), .PC_4_2(if_id_1_pc_4_2),
    .Clk(CLK), .\异步清0 (RST), .EN(En), .\同步清0 (BranchTaken));  // open: PredictJump_2, PredictJump
  // Probe on M_PC[11:0]
  D_Flip_Flop #(.trigger("high"), .Pre_Clr_Positions("LEGACY"), .NegatePresetClear("false"), .enable("true"), .NewFFLayout("false")) d_ff_1 (.Q(mips_probe_5_p3));  // open: clk, D, Qn, preset, en, reset
  // Probe on 13'h410
  // Mips_Probe mips_probe_6: pin names not known; wires that end beside it: ID_IR
  // Probe on WB_PC[11:0]
  Comparator #(.width(13), .mode("twosComplement")) comparator_1 (
    .a(CNT_num), .b(13'h410), .eq(comparator_1_eq), .lt(comparator_1_lt));  // open: gt
  Clock #(.highDuration(1), .lowDuration(1)) clock_2 (.out(clock_2_out));
  nand nand_1 (nand_1_out, mips_probe_5_p3, comparator_1_eq);
  Counter #(.width(13), .max('h1fff), .ongoal("stay"), .trigger("rising"), .behavior("old")) counter_5 (
    .count(comparator_1_lt), .Q(CNT_num), .clk(clock_2_out));  // open: load, D, carry, clr, preset
  Counter #(.width(16), .max('hffff), .ongoal("wrap"), .trigger("rising"), .behavior("new")) counter_6 (
    .count(stall), .Q(\LoadUse次数 ), .clk(CLK), .clr(RST));  // open: load, D, carry, preset, down
  Multiplexer #(.select(1), .width(5), .disabled("Z"), .enable("false")) multiplexer_2 (
    .in0(ID_IR[20:16]), .in1(ID_IR[15:11]), .out(multiplexer_2_out), .sel(RegDst));
  assign CLK = nand_1_out ? clock_2_out : 1'bz;  // Controlled_Buffer controlled_buffer_1
  Multiplexer #(.select(1), .width(5), .disabled("Z"), .enable("false")) multiplexer_3 (
    .in0(ID_IR[25:21]), .in1(5'b00010), .out(multiplexer_3_out), .sel(\单周期硬布线控制器_1_syscall ));
  Multiplexer #(.select(1), .width(5), .disabled("Z"), .enable("false")) multiplexer_4 (
    .in0(ID_IR[20:16]), .in1(5'b00100), .out(multiplexer_4_out), .sel(\单周期硬布线控制器_1_syscall ));
  Pull_Resistor #(.pull(1)) pull_resistor_1 (.node(CLK));
  \单周期硬布线控制器  \u_单周期硬布线控制器_1  (
    .Func(ID_IR[5:0]), .OP(ID_IR[31:26]), .ALU_OP(\单周期硬布线控制器_1_alu_op ), .MemToReg(\单周期硬布线控制器_1_memtoreg ),
    .MemWrite(\单周期硬布线控制器_1_memwrite ), .ALU_SRC(\单周期硬布线控制器_1_alu_src ), .RegWrite(\单周期硬布线控制器_1_regwrite ),
    .SysCALL(\单周期硬布线控制器_1_syscall ), .SignedExt(\单周期硬布线控制器_1_signedext ), .RegDst(RegDst),
    .JR(\单周期硬布线控制器_1_jr ), .JMP(\单周期硬布线控制器_1_jmp ), .Beq(\单周期硬布线控制器_1_beq ), .JAL(\单周期硬布线控制器_1_jal ),
    .Bne(\单周期硬布线控制器_1_bne ), .SB(\单周期硬布线控制器_1_sb ), .BGTZ(\单周期硬布线控制器_1_bgtz ), .SLLV(\单周期硬布线控制器_1_sllv ));
  fall_regfile fall_regfile_1 (
    .Din(RDin), .Clk(CLK), .R1(fall_regfile_1_r1), .R2(fall_regfile_1_r2), .WE(RegWrite), .W_num(W_num),
    .R1_num(multiplexer_3_out), .R2_num(multiplexer_4_out));
  not not_4 (not_4_out, Halt);
  or or_2 (h_en, not_4_out, Go);
  ID_EX id_ex_1 (
    .JMP(\单周期硬布线控制器_1_jmp ), .JR(\单周期硬布线控制器_1_jr ), .SignEXt(\单周期硬布线控制器_1_signedext ),
    .Beq(\单周期硬布线控制器_1_beq ), .Bne(\单周期硬布线控制器_1_bne ), .MemToReg(\单周期硬布线控制器_1_memtoreg ),
    .MemWrite(\单周期硬布线控制器_1_memwrite ), .AluOP(\单周期硬布线控制器_1_alu_op ), .AluSrcB(\单周期硬布线控制器_1_alu_src ),
    .RegWrite(\单周期硬布线控制器_1_regwrite ), .PC(ID_PC), .IR(ID_IR), .RS(fall_regfile_1_r1),
    .RT(fall_regfile_1_r2), .WriteReg_num(multiplexer_2_out), .PC_4(if_id_1_pc_4_2), .JMP_2(JMP), .JR_2(JR),
    .SignEXt_2(SignedExt), .Beq_2(Beq), .Bne_2(Bne), .MemToReg_2(MemRead), .MemWrite_2(id_ex_1_memwrite_2),
    .AluOP_2(id_ex_1_aluop_2), .AluSrcB_2(id_ex_1_alusrcb_2), .RegWrite_2(EX_RegWrite), .PC_2(EX_PC),
    .IR_2(EX_IR), .RS_2(id_ex_1_rs_2), .RT_2(id_ex_1_rt_2), .WriteReg_num_2(EX_W_num),
    .PC_4_2({JMPAddr, id_ex_1_pc_4_2}), .Clk(CLK), .\异步清0 (RST), .JAL(\单周期硬布线控制器_1_jal ),
    .JAL_2(id_ex_1_jal_2), .EN(h_en), .RT_F_2(id_ex_1_rt_f_2), .RT_F(RT_F), .\同步清0 (flush),
    .RS_F_2(id_ex_1_rs_f_2), .RS_F(RS_F), .BGTZ(\单周期硬布线控制器_1_bgtz ), .BGTZ_2(BGTZ),
    .SLLV(\单周期硬布线控制器_1_sllv ), .SLLV_2(SLLV), .SB(\单周期硬布线控制器_1_sb ), .SB_2(id_ex_1_sb_2),
    .syscall(\单周期硬布线控制器_1_syscall ), .syscall_2(id_ex_1_syscall_2));  // open: PredictJump, PredictJump_2
  assign bit_extender_1_out = {{16{1'b0}}, EX_IR[15:0]};  // Bit_Extender bit_extender_1
  assign bit_extender_2_out = {{16{EX_IR[15]}}, EX_IR[15:0]};  // Bit_Extender bit_extender_2
  Multiplexer #(.select(2), .width(32), .disabled("Z"), .enable("false")) multiplexer_5 (
    .in0(id_ex_1_rs_2), .in1(RDin), .in2(ALUresult), .out(GPRrs), .sel(id_ex_1_rs_f_2));  // open: in3
  Multiplexer #(.select(2), .width(32), .disabled("Z"), .enable("false")) multiplexer_6 (
    .in0(id_ex_1_rt_2), .in1(RDin), .in2(ALUresult), .out(multiplexer_6_out), .sel(id_ex_1_rt_f_2));  // open: in3
  Multiplexer #(.select(1), .width(32), .disabled("Z"), .enable("false")) multiplexer_7 (
    .in0(bit_extender_1_out), .in1(bit_extender_2_out), .out(multiplexer_7_out), .sel(SignedExt));
  \重定向相关处理逻辑  \u_重定向相关处理逻辑_1  (
    .Instr(ID_IR), .BranchTaken(BranchTaken), .MemRead(MemRead), .EX_W_num(EX_W_num),
    .EX_RegWrite(EX_RegWrite), .MEM_RegWrite(MEM_RegWrite), .MEM_W_num(MEM_W_num), .stall(stall),
    .flush(flush), .RS_F(RS_F), .RT_F(RT_F));
  Shifter #(.width(32), .shift("ll")) shifter_1 (.in(bit_extender_2_out), .\dist (5'b00010), .out(shifter_1_out));
  Multiplexer #(.select(1), .width(32), .disabled("Z"), .enable("false")) multiplexer_8 (
    .in0(multiplexer_6_out), .in1(multiplexer_7_out), .out(multiplexer_8_out), .sel(id_ex_1_alusrcb_2));
  Adder #(.width(32)) adder_2 (
    .a(shifter_1_out), .b({JMPAddr, id_ex_1_pc_4_2}), .out(BAddr), .cin(1'b0));  // open: cout
  MIPS_ALU mips_alu_1 (
    .X(GPRrs), .Y(multiplexer_8_out), .AluOP(id_ex_1_aluop_2), .Equal(Equal), .Result(mips_alu_1_result),
    .shamt(multiplexer_9_out));  // open: Result_2
  Multiplexer #(.select(1), .width(5), .disabled("Z"), .enable("false")) multiplexer_9 (
    .in0(EX_IR[10:6]), .in1(GPRrs[4:0]), .out(multiplexer_9_out), .sel(SLLV));
  Comparator #(.width(32), .mode("twosComplement")) comparator_2 (
    .a(V0), .b(32'ha), .eq(comparator_2_eq));  // open: gt, lt
  EX_MEM ex_mem_1 (
    .MemToReg(MemRead), .RegWrite(EX_RegWrite), .PC(EX_PC), .IR(EX_IR), .Result(mips_alu_1_result),
    .Writedata(multiplexer_6_out), .WriteReg_num(EX_W_num), .MemToReg_2(ex_mem_1_memtoreg_2),
    .RegWrite_2(MEM_RegWrite), .PC_2(M_PC), .IR_2(MEM_IR), .Result_2(ALUresult), .Writedata_2(GPRrt),
    .WriteReg_num_2(MEM_W_num), .Clk(CLK), .Rst(RST), .MemWrite_2(MemWrite), .MemWrite(id_ex_1_memwrite_2),
    .JAL(id_ex_1_jal_2), .JAL_2(ex_mem_1_jal_2), .EN(h_en), .R1_2(ex_mem_1_r1_2), .R1(GPRrs),
    .syscall_2(ex_mem_1_syscall_2), .syscall(id_ex_1_syscall_2), .SB(id_ex_1_sb_2), .SB_2(SB));  // open: JMP, JR, JMP_2, JR_2, 同步清0
  and and_3 (Halt, Syscall, comparator_2_eq);
  and and_4 (and_4_out, ~comparator_2_eq, Syscall);  // AND_Gate
  Register #(.width(32), .trigger("rising"), .Select("low")) register_1 (
    .D(A0), .en(and_4_out), .Q(LedData), .clk(CLK));  // open: clr
  RAM #(.addrWidth(10), .dataWidth(32), .bus("separate"), .Select("high")) ram_1 (
    .addr(ALUresult[11:2]), .din(MDin), .data(ram_1_data), .str(MemWrite), .clk(CLK), .ld(1'b1), .clr(RST));  // open: sel
  \按字节存储电路  \u_按字节存储电路_1  (.cdata(GPRrt), .sel(ALUresult), .sdata(ram_1_data), .ddata(\按字节存储电路_1_ddata ));
  MEM_WB mem_wb_1 (
    .MemToReg(ex_mem_1_memtoreg_2), .RegWrite(MEM_RegWrite), .PC(M_PC), .IR(MEM_IR), .Result(ALUresult),
    .Memdata(ram_1_data), .WriteReg_num(MEM_W_num), .MemToReg_2(MemToReg), .RegWrite_2(RegWrite),
    .PC_2(WB_PC), .IR_2(WB_IR), .Result_2(mem_wb_1_result_2), .Memdata_2(mem_wb_1_memdata_2),
    .WriteReg_num_2(mem_wb_1_writereg_num_2), .Clk(CLK), .Rst(RST), .JAL(ex_mem_1_jal_2), .JAL_2(JAL),
    .R1_2(V0), .R1(ex_mem_1_r1_2), .En(h_en), .syscall_2(Syscall), .syscall(ex_mem_1_syscall_2), .R1_3(A0),
    .R2(GPRrt));  // open: JMP_2, JR_2, JMP, JR, 同步清0
  Multiplexer #(.select(1), .width(32), .disabled("Z"), .enable("false")) multiplexer_10 (
    .in0(GPRrt), .in1(\按字节存储电路_1_ddata ), .out(MDin), .sel(SB));
  Multiplexer #(.select(1), .width(32), .disabled("Z"), .enable("false")) multiplexer_11 (
    .in0(mem_wb_1_result_2), .in1(mem_wb_1_memdata_2), .out(multiplexer_11_out), .sel(MemToReg));
  Multiplexer #(.select(1), .width(5), .disabled("Z"), .enable("false")) multiplexer_12 (
    .in0(mem_wb_1_writereg_num_2), .in1({5{1'b1}}), .out(W_num), .sel(JAL));
  // Probe on W_num
  and and_5 (and_5_out, Beq, Equal);
  and and_6 (and_6_out, ~Equal, Bne);  // AND_Gate
  Comparator #(.width(32), .mode("twosComplement")) comparator_3 (
    .a(GPRrs), .b({32{1'b0}}), .gt(comparator_3_gt));  // open: eq, lt
  and and_7 (and_7_out, comparator_3_gt, BGTZ);
  or or_3 (BranchTaken, and_5_out, and_6_out, and_7_out, JMP);
  Adder #(.width(32)) adder_3 (.a(WB_PC), .b(32'h4), .out(adder_3_out), .cin(1'b0));  // open: cout
  Multiplexer #(.select(1), .width(32), .disabled("Z"), .enable("false")) multiplexer_13 (
    .in0(multiplexer_11_out), .in1(adder_3_out), .out(RDin), .sel(JAL));
  // Probe on RDin

  // Other names for the same wires on the sheet: JMPAddr[27:2] = EX_IR[25:0]; shamt[4:0] = EX_IR[10:6];
  //   MEM_PC[31:0] = M_PC; PC[31:0] = IF_PC

  // Notes on the sheet:
  //   中断源
  //   时空图监测，可删除
  //   中断等待指示
  //   数码管输出
  //   指令存储器
  //   contents of rom_1 (hex, n*v repeats v):
  //   20110001 8000c05 20110001 20120002 20130003 8000c09 20110001 20120002 20130003 8000c0d 20110001
  //   20120002 20130003 8000c11 20110001 20120002 20130003 c000cf5 20100001 20110001 118fc0 112020
  //   20020022 c 118882 12200001 8000c15 112020 20020022 c 20110001 118880 112020 20020022 c 12200001
  //   8000c1f 20110001 118fc0 112020 20020022 c 1188c3 112020 20020022 c 118903 112020 20020022 c 118903
  //   112020 20020022 c 118903 112020 20020022 c 118903 112020 20020022 c 118903 112020 20020022 c 118903
  //   112020 20020022 c 118903 112020 20020022 c 20100001 109fc0 139fc3 8021 2012000c 24160003 26100001
  //   3210000f 20080008 20090001 139900 2709825 132020 20020022 c 1094022 1500fff9 22100001 2018000f
  //   2188024 108700 20080008 20090001 139902 2709825 132021 20020022 c 1094022 1500fff9 108702 2c9b022
  //   12c00001 8000c50 4020 1084027 84400 3508ffff 82021 20020022 c 2010ffff 20110000 ae300000 22100001
  //   22310004 ae300000 22100001 22310004 ae300000 22100001 22310004 ae300000 22100001 22310004 ae300000
  //   22100001 22310004 ae300000 22100001 22310004 ae300000 22100001 22310004 ae300000 22100001 22310004
  //   ae300000 22100001 22310004 ae300000 22100001 22310004 ae300000 22100001 22310004 ae300000 22100001
  //   22310004 ae300000 22100001 22310004 ae300000 22100001 22310004 ae300000 22100001 22310004 ae300000
  //   22100001 22310004 22100001 8020 2011003c 8e130000 8e340000 274402a 11000002 ae330000 ae140000
  //   2231fffc 1611fff8 102020 20020022 c 22100004 2011003c 1611fff2 2002000a c 20080001 20090003 20110876
  //   112020 20020022 c 200b0008 1118804 1318804 112020 20020022 c 216bffff 1560fff9 2002000a c 2008ffff
  //   20117777 112020 20020022 c 200b0010 3a31ffff 112020 20020022 c 216bffff 1560fffa 2002000a c 20090000
  //   200b0020 20110000 20120001 a1310000 112020 20020022 c 2328820 21290001 216bffff 1560fff8 200b0008
  //   20090000 8d310000 112020 20020022 c 21290004 216bffff 1560fff9 2002000a c 2011000f 112020 20020022 c
  //   2231ffff 1e20fffb 2002000a c 20100000 22100001 102020 20020022 c 22100002 102020 20020022 c 22100003
  //   102020 20020022 c 22100004 102020 20020022 c 22100005 102020 20020022 c 22100006 102020 20020022 c
  //   22100007 102020 20020022 c 22100008 102020 20020022 20020022 c 3e00008
  //   控制位
  //   流水调试日志用
  //   暂停节拍，不能为0
  //   戳工具置1进入计数暂停模式，ctrl+k时钟自动运行到对应节拍暂停
  //   ctrl+k关闭时钟连续运行，将控制位置零，进入单步调试模式调试
  //   OP
  //   Func
  //   rs
  //   rt
  //   rd
  //   可计数暂停的时钟源
  //   SB
  //   JMP
  //   JR
  //   SignedExt
  //   SLLV
  //   OP
  //   Func
  //   Syscall
  //   BGTZ
  //   Beq
  //   Bne
  //   MemToReg
  //   MemWrite
  //   AluOP
  //   AluSrcB
  //   RegWrite
  //   JAL
  //   Regdst
  //   为方便自动评测，需要输出流水线各段保存的PC值，注意是PC不是PC+4，另外ID段寄存器写入信息，Mem段内存写入信息也要输出
  //   shamt
  //   addr
  //   imm
  //   符号扩展
  //   WriteReg#
  //   ALUsrc
endmodule

module \气泡流水线  (
  output RegWrite,
  output MemWrite,
  output [31:0] IF_PC,
  output [31:0] ID_PC,
  output [31:0] EX_PC,
  output [31:0] M_PC,
  output [31:0] WB_PC,
  output [31:0] RDin,
  output [31:0] MDin,
  output [31:0] LedData
);

  wire and_1_out, and_2_out, and_4_out, and_5_out, and_6_out, and_7_out, Beq, BGTZ, Bne, BranchTaken, CLK,
       clock_1_out, clock_2_out, comparator_1_eq, comparator_1_lt, comparator_2_eq, comparator_3_gt,
       d_ff_1_q, En, Equal, ex_mem_1_jal_2, ex_mem_1_memtoreg_2, ex_mem_1_syscall_2, EX_RegWrite, flush, Go,
       h_en, Halt, id_ex_1_alusrcb_2, id_ex_1_jal_2, id_ex_1_memtoreg_2, id_ex_1_memwrite_2, id_ex_1_sb_2,
       id_ex_1_syscall_2, IR1, IR2, IR3, JAL, JMP, JR, MEM_RegWrite, MemToReg, nand_1_out, not_1_out,
       not_2_out, not_3_out, not_4_out, RegDst, RST, SB, SignedExt, SLLV, stall, Syscall, W1, W2, W3,
       \单周期硬布线控制器_1_alu_src , \单周期硬布线控制器_1_beq , \单周期硬布线控制器_1_bgtz , \单周期硬布线控制器_1_bne , \单周期硬布线控制器_1_jal ,
       \单周期硬布线控制器_1_jmp , \单周期硬布线控制器_1_jr , \单周期硬布线控制器_1_memtoreg , \单周期硬布线控制器_1_memwrite ,
       \单周期硬布线控制器_1_regwrite , \单周期硬布线控制器_1_sb , \单周期硬布线控制器_1_signedext , \单周期硬布线控制器_1_sllv ,
       \单周期硬布线控制器_1_syscall ;
  wire [3:0] id_ex_1_aluop_2, \单周期硬布线控制器_1_alu_op ;
  wire [4:0] EX_W_num, MEM_W_num, mem_wb_1_writereg_num_2, multiplexer_2_out, multiplexer_3_out,
       multiplexer_4_out, multiplexer_7_out, W_num;
  wire [12:0] CNT_num;
  wire [15:0] \LoadUse次数 , \总周期数 , \插入气泡数 , \无条件分支数 , \条件分支成功数 ;
  wire [27:0] id_ex_1_pc_4_2;
  wire [31:0] A0, adder_1_out, adder_3_out, BAddr, bit_extender_1_out, bit_extender_2_out, EX_IR,
       ex_mem_1_r1_2, ex_mem_1_result_2, fall_regfile_1_r1, fall_regfile_1_r2, GPRrs, GPRrt, id_ex_1_rt_2,
       ID_IR, if_id_1_pc_4_2, IF_IR, MEM_IR, mem_wb_1_memdata_2, mem_wb_1_result_2, mips_alu_1_result,
       multiplexer_1_out, multiplexer_5_out, multiplexer_6_out, multiplexer_9_out, ram_1_data, shifter_1_out,
       V0, WB_IR, \按字节存储电路_1_ddata ;
  wire [31:28] JMPAddr;

  Button \u_总复位  (.out(RST));
  Button _1 (.out(IR1));
  Button _2 (.out(IR2));
  Button _3 (.out(IR3));
  // Probe on \总周期数 
  // Probe on \总周期数 
  Button \u_继续运行  (.out(Go));
  LED #(.active("true")) led_1 (.in(W1));
  LED #(.active("true")) led_2 (.in(W2));
  LED #(.active("true")) led_3 (.in(W3));
  not not_1 (not_1_out, Halt);
  not not_2 (not_2_out, stall);
  Counter #(.width(16), .max('hffff), .ongoal("wrap"), .trigger("rising"), .behavior("new")) counter_1 (
    .count(JMP), .Q(\无条件分支数 ), .clk(CLK), .clr(RST));  // open: load, D, carry, preset, down
  Hex_Digit_Display hex_digit_display_1 (.value(LedData[31:28]));  // open: dp
  // Probe on IF_PC[19:0]
  // Mips_Probe mips_probe_1: pin names not known; wires that end beside it: IF_IR
  and and_1 (and_1_out, not_1_out, not_2_out);
  Hex_Digit_Display hex_digit_display_2 (.value(LedData[27:24]));  // open: dp
  Hex_Digit_Display hex_digit_display_3 (.value(LedData[23:20]));  // open: dp
  // Probe on ID_PC[19:0]
  // Mips_Probe mips_probe_2: pin names not known; wires that end beside it: ID_IR
  or or_1 (En, and_1_out, Go);
  Hex_Digit_Display hex_digit_display_4 (.value(LedData[19:16]));  // open: dp
  Hex_Digit_Display hex_digit_display_5 (.value(LedData[15:12]));  // open: dp
  Multiplexer #(.select(3), .width(32), .disabled("Z"), .enable("false")) multiplexer_1 (
    .in0(adder_1_out), .in1(BAddr), .in3({JMPAddr, EX_IR[25:0], 2'b00}), .in7(GPRrs),
    .out(multiplexer_1_out), .sel({JR, JMP, BranchTaken}));  // open: in2, in4, in5, in6
  Hex_Digit_Display hex_digit_display_6 (.value(LedData[11:8]));  // open: dp
  Hex_Digit_Display hex_digit_display_7 (.value(LedData[7:4]));  // open: dp
  Clock #(.highDuration(1), .lowDuration(1)) clock_1 (.out(clock_1_out));
  // Probe on EX_PC[19:0]
  // Mips_Probe mips_probe_3: pin names not known; wires that end beside it: clock_1_out, EX_IR, CLK
  and and_2 (and_2_out, BranchTaken, ~JMP);  // AND_Gate
  Counter #(.width(16), .max('hffff), .ongoal("wrap"), .trigger("rising"), .behavior("new")) counter_2 (
    .count(and_2_out), .Q(\条件分支成功数 ), .clk(CLK), .clr(RST));  // open: load, D, carry, preset, down
  Hex_Digit_Display hex_digit_display_8 (.value(LedData[3:0]));  // open: dp
  Register #(.width(32), .trigger("rising"), .Select("low")) PC (
    .D(multiplexer_1_out), .en(En), .Q(IF_PC), .clk(CLK), .clr(RST));
  // Probe on \总周期数 
  // Probe on M_PC[19:0]
  // Mips_Probe mips_probe_4: pin names not known; wires that end beside it: MEM_IR
  not not_3 (not_3_out, Halt);
  Counter #(.width(16), .max('hffff), .ongoal("wrap"), .trigger("rising"), .behavior("new")) counter_3 (
    .count(not_3_out), .Q(\总周期数 ), .clk(CLK), .clr(RST));  // open: load, D, carry, preset, down
  // Probe on \总周期数 
  // Probe on \无条件分支数 
  // Probe on \条件分支成功数 
  // Probe on \插入气泡数 
  // Probe on \LoadUse次数 
  Adder #(.width(32)) adder_1 (.a(IF_PC), .b(32'h4), .out(adder_1_out), .cin(1'b0));  // open: cout
  // Probe on IF_PC[11:0]
  // Probe on WB_PC[19:0]
  // Mips_Probe mips_probe_5: pin names not known; wires that end beside it: stall, WB_IR
  Counter #(.width(16), .max('hffff), .ongoal("wrap"), .trigger("rising"), .behavior("new")) counter_4 (
    .count(stall), .Q(\插入气泡数 ), .clk(CLK), .clr(RST));  // open: load, D, carry, preset, down
  ROM #(.addrWidth(10), .dataWidth(32), .Select("high")) rom_1 (.addr(IF_PC[11:2]), .data(IF_IR));
  // Probe on ID_PC[11:0]
  // Probe on EX_PC[11:0]
  IF_ID if_id_1 (
    .PC(IF_PC), .IR(IF_IR), .PC_4(adder_1_out), .PC_2(ID_PC), .IR_2(ID_IR), .PC_4_2(if_id_1_pc_4_2),
    .Clk(CLK), .\异步清0 (RST), .EN(En), .\同步清0 (BranchTaken));  // open: PredictJump_2, PredictJump
  // Probe on M_PC[11:0]
  D_Flip_Flop #(.trigger("high"), .Pre_Clr_Positions("LEGACY"), .NegatePresetClear("false"), .enable("true"), .NewFFLayout("false")) d_ff_1 (.Q(d_ff_1_q));  // open: clk, D, Qn, preset, en, reset
  // Probe on 13'he20
  // Mips_Probe mips_probe_6: pin names not known; wires that end beside it: ID_IR
  // Probe on WB_PC[11:0]
  Comparator #(.width(13), .mode("twosComplement")) comparator_1 (
    .a(CNT_num), .b(13'he20), .eq(comparator_1_eq), .lt(comparator_1_lt));  // open: gt
  Clock #(.highDuration(1), .lowDuration(1)) clock_2 (.out(clock_2_out));
  nand nand_1 (nand_1_out, d_ff_1_q, comparator_1_eq);
  Counter #(.width(13), .max('h1fff), .ongoal("stay"), .trigger("rising"), .behavior("old")) counter_5 (
    .count(comparator_1_lt), .Q(CNT_num), .clk(clock_2_out), .clr(RST));  // open: load, D, carry, preset
  Multiplexer #(.select(1), .width(5), .disabled("Z"), .enable("false")) multiplexer_2 (
    .in0(ID_IR[20:16]), .in1(ID_IR[15:11]), .out(multiplexer_2_out), .sel(RegDst));
  assign CLK = nand_1_out ? clock_2_out : 1'bz;  // Controlled_Buffer controlled_buffer_1
  Multiplexer #(.select(1), .width(5), .disabled("Z"), .enable("false")) multiplexer_3 (
    .in0(ID_IR[25:21]), .in1(5'b00010), .out(multiplexer_3_out), .sel(\单周期硬布线控制器_1_syscall ));
  Multiplexer #(.select(1), .width(5), .disabled("Z"), .enable("false")) multiplexer_4 (
    .in0(ID_IR[20:16]), .in1(5'b00100), .out(multiplexer_4_out), .sel(\单周期硬布线控制器_1_syscall ));
  Pull_Resistor #(.pull(1)) pull_resistor_1 (.node(CLK));
  \单周期硬布线控制器  \u_单周期硬布线控制器_1  (
    .Func(ID_IR[5:0]), .OP(ID_IR[31:26]), .ALU_OP(\单周期硬布线控制器_1_alu_op ), .MemToReg(\单周期硬布线控制器_1_memtoreg ),
    .MemWrite(\单周期硬布线控制器_1_memwrite ), .ALU_SRC(\单周期硬布线控制器_1_alu_src ), .RegWrite(\单周期硬布线控制器_1_regwrite ),
    .SysCALL(\单周期硬布线控制器_1_syscall ), .SignedExt(\单周期硬布线控制器_1_signedext ), .RegDst(RegDst),
    .JR(\单周期硬布线控制器_1_jr ), .JMP(\单周期硬布线控制器_1_jmp ), .Beq(\单周期硬布线控制器_1_beq ), .JAL(\单周期硬布线控制器_1_jal ),
    .Bne(\单周期硬布线控制器_1_bne ), .SB(\单周期硬布线控制器_1_sb ), .BGTZ(\单周期硬布线控制器_1_bgtz ), .SLLV(\单周期硬布线控制器_1_sllv ));
  fall_regfile fall_regfile_1 (
    .Din(RDin), .Clk(CLK), .R1(fall_regfile_1_r1), .R2(fall_regfile_1_r2), .WE(RegWrite), .W_num(W_num),
    .R1_num(multiplexer_3_out), .R2_num(multiplexer_4_out));
  // Probe on fall_regfile_1_r1
  not not_4 (not_4_out, Halt);
  or or_2 (h_en, not_4_out, Go);
  ID_EX id_ex_1 (
    .JMP(\单周期硬布线控制器_1_jmp ), .JR(\单周期硬布线控制器_1_jr ), .SignEXt(\单周期硬布线控制器_1_signedext ),
    .Beq(\单周期硬布线控制器_1_beq ), .Bne(\单周期硬布线控制器_1_bne ), .MemToReg(\单周期硬布线控制器_1_memtoreg ),
    .MemWrite(\单周期硬布线控制器_1_memwrite ), .AluOP(\单周期硬布线控制器_1_alu_op ), .AluSrcB(\单周期硬布线控制器_1_alu_src ),
    .RegWrite(\单周期硬布线控制器_1_regwrite ), .PC(ID_PC), .IR(ID_IR), .RS(fall_regfile_1_r1),
    .RT(fall_regfile_1_r2), .WriteReg_num(multiplexer_2_out), .PC_4(if_id_1_pc_4_2), .JMP_2(JMP), .JR_2(JR),
    .SignEXt_2(SignedExt), .Beq_2(Beq), .Bne_2(Bne), .MemToReg_2(id_ex_1_memtoreg_2),
    .MemWrite_2(id_ex_1_memwrite_2), .AluOP_2(id_ex_1_aluop_2), .AluSrcB_2(id_ex_1_alusrcb_2),
    .RegWrite_2(EX_RegWrite), .PC_2(EX_PC), .IR_2(EX_IR), .RS_2(GPRrs), .RT_2(id_ex_1_rt_2),
    .WriteReg_num_2(EX_W_num), .PC_4_2({JMPAddr, id_ex_1_pc_4_2}), .Clk(CLK), .\异步清0 (RST),
    .JAL(\单周期硬布线控制器_1_jal ), .JAL_2(id_ex_1_jal_2), .EN(h_en), .\同步清0 (flush), .BGTZ(\单周期硬布线控制器_1_bgtz ),
    .BGTZ_2(BGTZ), .SLLV(\单周期硬布线控制器_1_sllv ), .SLLV_2(SLLV), .SB(\单周期硬布线控制器_1_sb ), .SB_2(id_ex_1_sb_2),
    .syscall(\单周期硬布线控制器_1_syscall ), .syscall_2(id_ex_1_syscall_2));  // open: RT_F_2, RT_F, RS_F_2, RS_F, PredictJump, PredictJump_2
  assign bit_extender_1_out = {{16{1'b0}}, EX_IR[15:0]};  // Bit_Extender bit_extender_1
  assign bit_extender_2_out = {{16{EX_IR[15]}}, EX_IR[15:0]};  // Bit_Extender bit_extender_2
  Multiplexer #(.select(1), .width(32), .disabled("Z"), .enable("false")) multiplexer_5 (
    .in0(bit_extender_1_out), .in1(bit_extender_2_out), .out(multiplexer_5_out), .sel(SignedExt));
  Shifter #(.width(32), .shift("ll")) shifter_1 (.in(bit_extender_2_out), .\dist (5'b00010), .out(shifter_1_out));
  Multiplexer #(.select(1), .width(32), .disabled("Z"), .enable("false")) multiplexer_6 (
    .in0(id_ex_1_rt_2), .in1(multiplexer_5_out), .out(multiplexer_6_out), .sel(id_ex_1_alusrcb_2));
  Adder #(.width(32)) adder_2 (
    .a(shifter_1_out), .b({JMPAddr, id_ex_1_pc_4_2}), .out(BAddr), .cin(1'b0));  // open: cout
  \相关处理逻辑  \u_相关处理逻辑_1  (
    .Instr(ID_IR), .EX_RegWrite(EX_RegWrite), .EX_W_num(EX_W_num), .BranchTaken(BranchTaken),
    .MEM_RegWrite(MEM_RegWrite), .MEM_W_num(MEM_W_num), .stall(stall), .flush(flush));
  MIPS_ALU mips_alu_1 (
    .X(GPRrs), .Y(multiplexer_6_out), .AluOP(id_ex_1_aluop_2), .Equal(Equal), .Result(mips_alu_1_result),
    .shamt(multiplexer_7_out));  // open: Result_2
  Multiplexer #(.select(1), .width(5), .disabled("Z"), .enable("false")) multiplexer_7 (
    .in0(EX_IR[10:6]), .in1(GPRrs[4:0]), .out(multiplexer_7_out), .sel(SLLV));
  // Probe on {JMPAddr, EX_IR[25:0], 2'b00}
  // Probe on mips_alu_1_result
  Comparator #(.width(32), .mode("twosComplement")) comparator_2 (
    .a(V0), .b(32'ha), .eq(comparator_2_eq));  // open: gt, lt
  EX_MEM ex_mem_1 (
    .MemToReg(id_ex_1_memtoreg_2), .RegWrite(EX_RegWrite), .PC(EX_PC), .IR(EX_IR),
    .Result(mips_alu_1_result), .Writedata(id_ex_1_rt_2), .WriteReg_num(EX_W_num),
    .MemToReg_2(ex_mem_1_memtoreg_2), .RegWrite_2(MEM_RegWrite), .PC_2(M_PC), .IR_2(MEM_IR),
    .Result_2(ex_mem_1_result_2), .Writedata_2(GPRrt), .WriteReg_num_2(MEM_W_num), .Clk(CLK), .Rst(RST),
    .MemWrite_2(MemWrite), .MemWrite(id_ex_1_memwrite_2), .JAL(id_ex_1_jal_2), .JAL_2(ex_mem_1_jal_2),
    .EN(h_en), .R1_2(ex_mem_1_r1_2), .R1(GPRrs), .syscall_2(ex_mem_1_syscall_2), .syscall(id_ex_1_syscall_2),
    .SB(id_ex_1_sb_2), .SB_2(SB));  // open: JMP, JR, JMP_2, JR_2, 同步清0
  and and_3 (Halt, Syscall, comparator_2_eq);
  and and_4 (and_4_out, ~comparator_2_eq, Syscall);  // AND_Gate
  Register #(.width(32), .trigger("rising"), .Select("low")) register_1 (
    .D(A0), .en(and_4_out), .Q(LedData), .clk(CLK));  // open: clr
  // Probe on ex_mem_1_result_2
  RAM #(.addrWidth(10), .dataWidth(32), .bus("separate"), .Select("high")) ram_1 (
    .addr(ex_mem_1_result_2[11:2]), .din(MDin), .data(ram_1_data), .str(MemWrite), .clk(CLK), .ld(1'b1),
    .clr(RST));  // open: sel
  \按字节存储电路  \u_按字节存储电路_1  (.cdata(GPRrt), .sel(ex_mem_1_result_2), .sdata(ram_1_data), .ddata(\按字节存储电路_1_ddata ));
  MEM_WB mem_wb_1 (
    .MemToReg(ex_mem_1_memtoreg_2), .RegWrite(MEM_RegWrite), .PC(M_PC), .IR(MEM_IR),
    .Result(ex_mem_1_result_2), .Memdata(ram_1_data), .WriteReg_num(MEM_W_num), .MemToReg_2(MemToReg),
    .RegWrite_2(RegWrite), .PC_2(WB_PC), .IR_2(WB_IR), .Result_2(mem_wb_1_result_2),
    .Memdata_2(mem_wb_1_memdata_2), .WriteReg_num_2(mem_wb_1_writereg_num_2), .Clk(CLK), .Rst(RST),
    .JAL(ex_mem_1_jal_2), .JAL_2(JAL), .R1_2(V0), .R1(ex_mem_1_r1_2), .En(h_en), .syscall_2(Syscall),
    .syscall(ex_mem_1_syscall_2), .R1_3(A0), .R2(GPRrt));  // open: JMP_2, JR_2, JMP, JR, 同步清0
  Multiplexer #(.select(1), .width(32), .disabled("Z"), .enable("false")) multiplexer_8 (
    .in0(GPRrt), .in1(\按字节存储电路_1_ddata ), .out(MDin), .sel(SB));
  Multiplexer #(.select(1), .width(32), .disabled("Z"), .enable("false")) multiplexer_9 (
    .in0(mem_wb_1_result_2), .in1(mem_wb_1_memdata_2), .out(multiplexer_9_out), .sel(MemToReg));
  Multiplexer #(.select(1), .width(5), .disabled("Z"), .enable("false")) multiplexer_10 (
    .in0(mem_wb_1_writereg_num_2), .in1({5{1'b1}}), .out(W_num), .sel(JAL));
  // Probe on W_num
  and and_5 (and_5_out, Beq, Equal);
  and and_6 (and_6_out, ~Equal, Bne);  // AND_Gate
  Comparator #(.width(32), .mode("twosComplement")) comparator_3 (
    .a(GPRrs), .b({32{1'b0}}), .gt(comparator_3_gt));  // open: eq, lt
  and and_7 (and_7_out, comparator_3_gt, BGTZ);
  or or_3 (BranchTaken, and_5_out, and_6_out, and_7_out, JMP);
  Adder #(.width(32)) adder_3 (.a(WB_PC), .b(32'h4), .out(adder_3_out), .cin(1'b0));  // open: cout
  Multiplexer #(.select(1), .width(32), .disabled("Z"), .enable("false")) multiplexer_11 (
    .in0(multiplexer_9_out), .in1(adder_3_out), .out(RDin), .sel(JAL));
  // Probe on RDin

  // Other names for the same wires on the sheet: JMPAddr[27:2] = EX_IR[25:0]; shamt[4:0] = EX_IR[10:6];
  //   MEM_PC[31:0] = M_PC; PC[31:0] = IF_PC

  // Notes on the sheet:
  //   中断源
  //   时空图监测，可删除
  //   中断等待指示
  //   数码管输出
  //   指令存储器
  //   contents of rom_1 (hex, n*v repeats v):
  //   20110001 8000c05 20110001 20120002 20130003 8000c09 20110001 20120002 20130003 8000c0d 20110001
  //   20120002 20130003 8000c11 20110001 20120002 20130003 c000cf5 20100001 20110001 118fc0 112020
  //   20020022 c 118882 12200001 8000c15 112020 20020022 c 20110001 118880 112020 20020022 c 12200001
  //   8000c1f 20110001 118fc0 112020 20020022 c 1188c3 112020 20020022 c 118903 112020 20020022 c 118903
  //   112020 20020022 c 118903 112020 20020022 c 118903 112020 20020022 c 118903 112020 20020022 c 118903
  //   112020 20020022 c 118903 112020 20020022 c 20100001 109fc0 139fc3 8021 2012000c 24160003 26100001
  //   3210000f 20080008 20090001 139900 2709825 132020 20020022 c 1094022 1500fff9 22100001 2018000f
  //   2188024 108700 20080008 20090001 139902 2709825 132021 20020022 c 1094022 1500fff9 108702 2c9b022
  //   12c00001 8000c50 4020 1084027 84400 3508ffff 82021 20020022 c 2010ffff 20110000 ae300000 22100001
  //   22310004 ae300000 22100001 22310004 ae300000 22100001 22310004 ae300000 22100001 22310004 ae300000
  //   22100001 22310004 ae300000 22100001 22310004 ae300000 22100001 22310004 ae300000 22100001 22310004
  //   ae300000 22100001 22310004 ae300000 22100001 22310004 ae300000 22100001 22310004 ae300000 22100001
  //   22310004 ae300000 22100001 22310004 ae300000 22100001 22310004 ae300000 22100001 22310004 ae300000
  //   22100001 22310004 22100001 8020 2011003c 8e130000 8e340000 274402a 11000002 ae330000 ae140000
  //   2231fffc 1611fff8 102020 20020022 c 22100004 2011003c 1611fff2 2002000a c 20080001 20090003 20110876
  //   112020 20020022 c 200b0008 1118804 1318804 112020 20020022 c 216bffff 1560fff9 2002000a c 2008ffff
  //   20117777 112020 20020022 c 200b0010 3a31ffff 112020 20020022 c 216bffff 1560fffa 2002000a c 20090000
  //   200b0020 20110000 20120001 a1310000 112020 20020022 c 2328820 21290001 216bffff 1560fff8 200b0008
  //   20090000 8d310000 112020 20020022 c 21290004 216bffff 1560fff9 2002000a c 2011000f 112020 20020022 c
  //   2231ffff 1e20fffb 2002000a c 20100000 22100001 102020 20020022 c 22100002 102020 20020022 c 22100003
  //   102020 20020022 c 22100004 102020 20020022 c 22100005 102020 20020022 c 22100006 102020 20020022 c
  //   22100007 102020 20020022 c 22100008 102020 20020022 20020022 c 3e00008
  //   控制位
  //   流水调试日志用
  //   暂停节拍，不能为0
  //   戳工具置1进入计数暂停模式，ctrl+k时钟自动运行到对应节拍暂停
  //   ctrl+k关闭时钟连续运行，将控制位置零，进入单步调试模式调试
  //   OP
  //   Func
  //   rs
  //   rt
  //   rd
  //   可计数暂停的时钟源
  //   SB
  //   JMP
  //   JR
  //   SignedExt
  //   SLLV
  //   OP
  //   Func
  //   Syscall
  //   BGTZ
  //   Beq
  //   Bne
  //   MemToReg
  //   MemWrite
  //   AluOP
  //   AluSrcB
  //   RegWrite
  //   JAL
  //   Regdst
  //   为方便自动评测，需要输出流水线各段保存的PC值，注意是PC不是PC+4，另外ID段寄存器写入信息，Mem段内存写入信息也要输出
  //   shamt
  //   addr
  //   imm
  //   符号扩展
  //   WriteReg#
endmodule

module \中断按键参考电路  (
  input  \同步清零信号 ,
  output \与中断屏蔽位与 
);

  wire \_1号中断_out , and_1_out, clock_1_out, d_ff_1_q, or_1_out, or_2_out;

  Clock #(.highDuration(1), .lowDuration(1)) clock_1 (.out(clock_1_out));
  Button \_1号中断  (.out(\_1号中断_out ));
  or or_1 (or_1_out, \与中断屏蔽位与 , d_ff_1_q);
  LED #(.active("true")) \_1号中断等待指示灯  (.in(or_1_out));
  D_Flip_Flop #(.trigger("rising"), .Pre_Clr_Positions("LEGACY"), .NegatePresetClear("false"), .enable("true"), .NewFFLayout("false")) d_ff_1 (
    .clk(\_1号中断_out ), .D(1'b1), .Q(d_ff_1_q), .reset(\与中断屏蔽位与 ));  // open: Qn, preset, en
  or or_2 (or_2_out, d_ff_1_q, \与中断屏蔽位与 );
  and and_1 (and_1_out, or_2_out, ~\同步清零信号 );  // AND_Gate
  D_Flip_Flop #(.trigger("rising"), .Pre_Clr_Positions("LEGACY"), .NegatePresetClear("false"), .enable("true"), .NewFFLayout("false")) IR1 (
    .clk(clock_1_out), .D(and_1_out), .Q(\与中断屏蔽位与 ));  // open: Qn, preset, en, reset

  // Notes on the sheet:
  //   中断信号采样参考电路
  //   Reset 
endmodule
module \单周期MIPS_单级中断  (
  input  IR1,
  input  IR2,
  input  IR3,
  output RegWrite,
  output MemWrite,
  output [31:0] PC,
  output [31:0] IR,
  output [31:0] RDin,
  output [31:0] MDin,
  output [31:0] LedData
);

  wire AluSrcB, and_4_out, and_5_out, and_6_out, Beq, BGTZ, Bne, BranchTaken, CLK, clrA, clrB, clrC,
       comparator_2_eq, comparator_3_gt, En, Equal, eret, Go, Halt, \IE中断使能寄存器_q , Int, IR1_t, IR2_t, IR3_t,
       IRA, IRB, IRC, JAL, JMP, JR, LED_EN, MemToReg, not_1_out, or_5_out, or_6_out, RegDst, RST, SB,
       SignedExt, SLLV, Syscall, W1, W2, W3, \中断按键_1_与中断屏蔽位与 , \中断按键_2_与中断屏蔽位与 , \中断按键_3_与中断屏蔽位与 ;
  wire [1:0] priority_encoder_1_out, register_2_q;
  wire [3:0] AluOP;
  wire [4:0] multiplexer_5_out, multiplexer_6_out, multiplexer_7_out, multiplexer_8_out, multiplexer_11_out;
  wire [15:0] \总周期数 ;
  wire [27:0] PC_4;
  wire [31:0] A0, bit_extender_1_out, bit_extender_2_out, BranchAddr, GPRrs, Int_addr, mips_alu_1_result,
       multiplexer_1_out, multiplexer_2_out, multiplexer_3_out, multiplexer_9_out, multiplexer_10_out,
       multiplexer_12_out, ram_1_data, ret_addr, shifter_1_out, \按字节存储电路_1_ddata ;
  wire [31:28] JMPAddr;

  Clock #(.highDuration(1), .lowDuration(1)) clock_1 (.out(CLK));
  Button _1 (.out(IRA));
  Button _2 (.out(IRB));
  Button _3 (.out(IRC));
  Button \u_继续运行  (.out(Go));
  LED #(.active("true")) led_1 (.in(W1));
  LED #(.active("true")) led_2 (.in(W2));
  LED #(.active("true")) led_3 (.in(W3));
  Counter #(.width(16), .max('hffff), .ongoal("wrap"), .trigger("rising"), .behavior("new")) counter_1 (
    .count(En), .Q(\总周期数 ), .clk(CLK), .clr(RST));  // open: load, D, carry, preset, down
  Hex_Digit_Display hex_digit_display_1 (.value(LedData[31:28]));  // open: dp
  Hex_Digit_Display hex_digit_display_2 (.value(LedData[27:24]));  // open: dp
  Hex_Digit_Display hex_digit_display_3 (.value(LedData[23:20]));  // open: dp
  Multiplexer #(.select(3), .width(32), .disabled("Z"), .enable("false")) multiplexer_1 (
    .in0({JMPAddr, PC_4}), .in1(BranchAddr), .in2({JMPAddr, IR[25:0], 2'b00}), .in6(GPRrs),
    .out(multiplexer_1_out), .sel({JR, JMP, BranchTaken}));  // open: in3, in4, in5, in7
  Hex_Digit_Display hex_digit_display_4 (.value(LedData[19:16]));  // open: dp
  Hex_Digit_Display hex_digit_display_5 (.value(LedData[15:12]));  // open: dp
  Register #(.width(32), .trigger("rising"), .Select("low")) register_1 (
    .D(multiplexer_1_out), .en(Int), .Q(ret_addr), .clk(CLK));  // open: clr
  // Probe on Int_addr
  Hex_Digit_Display hex_digit_display_6 (.value(LedData[11:8]));  // open: dp
  Hex_Digit_Display hex_digit_display_7 (.value(LedData[7:4]));  // open: dp
  // Probe on \总周期数 
  Multiplexer #(.select(1), .width(32), .disabled("Z"), .enable("false")) multiplexer_2 (
    .in0(multiplexer_1_out), .in1(Int_addr), .out(multiplexer_2_out), .sel(Int));
  Multiplexer #(.select(1), .width(32), .disabled("Z"), .enable("false")) multiplexer_3 (
    .in0(multiplexer_2_out), .in1(ret_addr), .out(multiplexer_3_out), .sel(eret));
  Hex_Digit_Display hex_digit_display_8 (.value(LedData[3:0]));  // open: dp
  Register #(.width(32), .trigger("rising"), .Select("low")) u_PC (
    .D(multiplexer_3_out), .en(En), .Q(PC), .clk(CLK), .clr(RST));
  or or_1 (IR1_t, IR1, IRA);
  not not_1 (not_1_out, Halt);
  or or_2 (IR2_t, IR2, IRB);
  // Probe on IR
  or or_3 (En, not_1_out, Go);
  Adder #(.width(32)) adder_1 (.a(PC), .b(32'h4), .out({JMPAddr, PC_4}), .cin(1'b0));  // open: cout
  ROM #(.addrWidth(10), .dataWidth(32), .Select("high")) rom_1 (.addr(PC[11:2]), .data(IR));
  \中断按键  \u_中断按键_1  (.clk(CLK), .\中断源 (IRA), .\中断等待信号 (W1), .\与中断屏蔽位与 (\中断按键_1_与中断屏蔽位与 ), .\同步清零信号 (clrA));
  \中断按键  \u_中断按键_2  (.clk(CLK), .\中断源 (IRB), .\中断等待信号 (W2), .\与中断屏蔽位与 (\中断按键_2_与中断屏蔽位与 ), .\同步清零信号 (clrB));
  \中断按键  \u_中断按键_3  (.clk(CLK), .\中断源 (IRC), .\中断等待信号 (W3), .\与中断屏蔽位与 (\中断按键_3_与中断屏蔽位与 ), .\同步清零信号 (clrC));
  or or_4 (IR3_t, IR3, IRC);
  // Mips_Probe mips_probe_1: pin names not known; wires that end beside it: IR
  or or_5 (or_5_out, \中断按键_1_与中断屏蔽位与 , \中断按键_2_与中断屏蔽位与 , \中断按键_3_与中断屏蔽位与 );
  Comparator #(.width(32), .mode("twosComplement")) comparator_1 (.a(32'h42000018), .b(IR), .eq(eret));  // open: gt, lt
  Priority_Encoder #(.select(2), .disabled("Z")) priority_encoder_1 (
    .in1(\中断按键_1_与中断屏蔽位与 ), .in2(\中断按键_2_与中断屏蔽位与 ), .in3(\中断按键_3_与中断屏蔽位与 ), .out(priority_encoder_1_out));  // open: in0, gs, en_out, en_in
  or or_6 (or_6_out, eret, ~or_5_out);  // OR_Gate
  Multiplexer #(.select(2), .width(32), .disabled("Z"), .enable("false")) multiplexer_4 (
    .in1(32'h30ac), .in2(32'h3150), .in3(32'h31f4), .out(Int_addr), .sel(priority_encoder_1_out));  // open: in0
  Register #(.width(1), .trigger("rising"), .Select("low")) \IE中断使能寄存器  (
    .D(or_6_out), .Q(\IE中断使能寄存器_q ), .clk(CLK));  // open: en, clr
  and and_1 (Int, \IE中断使能寄存器_q , or_5_out);
  Register #(.width(2), .trigger("rising"), .Select("low")) register_2 (
    .D(priority_encoder_1_out), .en(Int), .Q(register_2_q), .clk(CLK));  // open: clr
  Button u_RST (.out(RST));
  Demultiplexer #(.select(2), .width(1), .tristate("false"), .disabled("Z"), .enable("false")) demultiplexer_1 (
    .out1(clrA), .out2(clrB), .out3(clrC), .in(eret), .sel(register_2_q));  // open: out0
  // Probe on register_2_q
  Multiplexer #(.select(1), .width(5), .disabled("Z"), .enable("false")) multiplexer_5 (
    .in0(IR[20:16]), .in1(IR[15:11]), .out(multiplexer_5_out), .sel(RegDst));
  assign bit_extender_1_out = {{16{1'b0}}, IR[15:0]};  // Bit_Extender bit_extender_1
  assign bit_extender_2_out = {{16{IR[15]}}, IR[15:0]};  // Bit_Extender bit_extender_2
  // Probe on multiplexer_6_out
  Multiplexer #(.select(1), .width(5), .disabled("Z"), .enable("false")) multiplexer_6 (
    .in0(IR[25:21]), .in1(5'b00010), .out(multiplexer_6_out), .sel(Syscall));
  Multiplexer #(.select(1), .width(5), .disabled("Z"), .enable("false")) multiplexer_7 (
    .in0(IR[20:16]), .in1(5'b00100), .out(multiplexer_7_out), .sel(Syscall));
  // Probe on multiplexer_7_out
  // Probe on multiplexer_8_out
  Multiplexer #(.select(1), .width(5), .disabled("Z"), .enable("false")) multiplexer_8 (
    .in0(multiplexer_5_out), .in1({5{1'b1}}), .out(multiplexer_8_out), .sel(JAL));
  Multiplexer #(.select(1), .width(32), .disabled("Z"), .enable("false")) multiplexer_9 (
    .in0(bit_extender_1_out), .in1(bit_extender_2_out), .out(multiplexer_9_out), .sel(SignedExt));
  // Probe on RDin
  Comparator #(.width(32), .mode("twosComplement")) comparator_2 (
    .a(GPRrs), .b(32'ha), .eq(comparator_2_eq));  // open: gt, lt
  // Probe on GPRrs
  MIPS_Regifile mips_regifile_1 (
    .Din(RDin), .Clk(CLK), .R1(GPRrs), .R2(A0), .WE(RegWrite), .W_num(multiplexer_8_out),
    .R1_num(multiplexer_6_out), .R2_num(multiplexer_7_out));
  Shifter #(.width(32), .shift("ll")) shifter_1 (.in(bit_extender_2_out), .\dist (5'b00010), .out(shifter_1_out));
  // Probe on multiplexer_10_out
  Multiplexer #(.select(1), .width(32), .disabled("Z"), .enable("false")) multiplexer_10 (
    .in0(A0), .in1(multiplexer_9_out), .out(multiplexer_10_out), .sel(AluSrcB));
  and and_2 (Halt, Syscall, comparator_2_eq);
  and and_3 (LED_EN, ~comparator_2_eq, Syscall);  // AND_Gate
  MIPS_ALU mips_alu_1 (
    .X(GPRrs), .Y(multiplexer_10_out), .AluOP(AluOP), .Equal(Equal), .Result(mips_alu_1_result),
    .shamt(multiplexer_11_out));  // open: Result_2
  Multiplexer #(.select(1), .width(5), .disabled("Z"), .enable("false")) multiplexer_11 (
    .in0(IR[10:6]), .in1(GPRrs[4:0]), .out(multiplexer_11_out), .sel(SLLV));
  Adder #(.width(32)) adder_2 (.a(shifter_1_out), .b({JMPAddr, PC_4}), .out(BranchAddr), .cin(1'b0));  // open: cout
  and and_4 (and_4_out, Beq, Equal);
  and and_5 (and_5_out, ~Equal, Bne);  // AND_Gate
  Comparator #(.width(32), .mode("twosComplement")) comparator_3 (
    .a(GPRrs), .b({32{1'b0}}), .gt(comparator_3_gt));  // open: eq, lt
  // Probe on mips_alu_1_result
  and and_6 (and_6_out, comparator_3_gt, BGTZ);
  or or_7 (BranchTaken, and_4_out, and_5_out, and_6_out);
  RAM #(.addrWidth(10), .dataWidth(32), .bus("separate"), .Select("high")) ram_1 (
    .addr(mips_alu_1_result[11:2]), .din(MDin), .data(ram_1_data), .str(MemWrite), .clk(CLK), .ld(1'b1));  // open: sel, clr
  \按字节存储电路  \u_按字节存储电路_1  (.cdata(A0), .sel(mips_alu_1_result), .sdata(ram_1_data), .ddata(\按字节存储电路_1_ddata ));
  \单周期硬布线控制器  \u_单周期硬布线控制器_1  (
    .Func(IR[5:0]), .OP(IR[31:26]), .ALU_OP(AluOP), .MemToReg(MemToReg), .MemWrite(MemWrite),
    .ALU_SRC(AluSrcB), .RegWrite(RegWrite), .SysCALL(Syscall), .SignedExt(SignedExt), .RegDst(RegDst),
    .JR(JR), .JMP(JMP), .Beq(Beq), .JAL(JAL), .Bne(Bne), .SB(SB), .BGTZ(BGTZ), .SLLV(SLLV));
  Multiplexer #(.select(1), .width(32), .disabled("Z"), .enable("false")) multiplexer_12 (
    .in0(mips_alu_1_result), .in1(ram_1_data), .out(multiplexer_12_out), .sel(MemToReg));
  Register #(.width(32), .trigger("rising"), .Select("low")) register_3 (
    .D(A0), .en(LED_EN), .Q(LedData), .clk(CLK));  // open: clr
  Multiplexer #(.select(1), .width(32), .disabled("Z"), .enable("false")) multiplexer_13 (
    .in0(multiplexer_12_out), .in1({JMPAddr, PC_4}), .out(RDin), .sel(JAL));
  Multiplexer #(.select(1), .width(32), .disabled("Z"), .enable("false")) multiplexer_14 (
    .in0(A0), .in1(\按字节存储电路_1_ddata ), .out(MDin), .sel(SB));
  // Probe on RDin

  // Other names for the same wires on the sheet: GPRrt[31:0] = A0; OP[5:0] = IR[31:26]; addr[25:0] = IR[25:0];
  //   Func[5:0] = IR[5:0]; imm[15:0] = IR[15:0]; JMPAddr[27:2] = IR[25:0]; shamt[4:0] = IR[10:6]; rd[4:0] = IR[15:11];
  //   rt[4:0] = IR[20:16]; rs[4:0] = IR[25:21]; PC_4[31:28] = JMPAddr; V0[31:0] = GPRrs

  // Notes on the sheet:
  //   中断源
  //   中断等待指示
  //   总复位信号应将除ROM以外所有存储组件全部清零
  //   数码管输出
  //   EPC寄存器
  //   数码管输出应该用寄存器锁存，否则显示数据只能一闪而过
  //   指令存储器
  //   contents of rom_1 (hex, n*v repeats v):
  //   201d07d0 20100001 109fc0 139fc3 8021 2012000c 24160008 26100001 3210000f 20080008 20090001 139900
  //   2709825 132020 20020022 c 1094022 1500fff9 22100001 2018000f 2188024 108700 20080008 20090001 139902
  //   2709825 132021 20020022 c 1094022 1500fff9 108702 2c9b022 12c00001 8000c07 4020 1084027 84400
  //   3508ffff 82021 20020022 c 8000c01 afa20000 23bd0004 afa40000 23bd0004 afb00000 23bd0004 afb30000
  //   23bd0004 afb40000 23bd0004 afb50000 23bd0004 afb60000 23bd0004 20160001 20140003 20150001 168020
  //   108100 2149825 132020 20020022 c 1600fffa 295a022 1680fff7 23bdfffc 8fb60000 23bdfffc 8fb50000
  //   23bdfffc 8fb40000 23bdfffc 8fb30000 23bdfffc 8fb00000 23bdfffc 8fa40000 23bdfffc 8fa20000 42000018
  //   afa20000 23bd0004 afa40000 23bd0004 afb00000 23bd0004 afb30000 23bd0004 afb40000 23bd0004 afb50000
  //   23bd0004 afb60000 23bd0004 20160002 20140003 20150001 168020 108100 2149825 132020 20020022 c
  //   1600fffa 295a022 1680fff7 23bdfffc 8fb60000 23bdfffc 8fb50000 23bdfffc 8fb40000 23bdfffc 8fb30000
  //   23bdfffc 8fb00000 23bdfffc 8fa40000 23bdfffc 8fa20000 42000018 afa20000 23bd0004 afa40000 23bd0004
  //   afb00000 23bd0004 afb30000 23bd0004 afb40000 23bd0004 afb50000 23bd0004 afb60000 23bd0004 20160003
  //   20140003 20150001 168020 108100 2149825 132020 20020022 c 1600fffa 295a022 1680fff7 23bdfffc
  //   8fb60000 23bdfffc 8fb50000 23bdfffc 8fb40000 23bdfffc 8fb30000 23bdfffc 8fb00000 23bdfffc 8fa40000
  //   23bdfffc 8fa20000 42000018
  //   OP
  //   Func
  //   rs
  //   指令字
  //   rt
  //   rd
  //   imm
  //   addr
  //   eret指令
  //   有中断
  //   中断程序入口地址
  //   为方便自动评测，需要输出PC，IR，寄存器堆写如数据RDin
  //   RAM写使能MemWrite、RAM写入数据MDin等信号
  //   中断请求
  //   符号扩展
  //   SB
  //   JMP
  //   JR
  //   SLLV
  //   OP
  //   Func
  //   BGTZ
  //   Beq
  //   Bne
  //   MemToReg
  //   MemWrite
  //   AluOP
  //   AluSrcB
  //   RegWrite
  //   JAL
  //   RegDst
  //   Syscall
endmodule

module \单周期MIPS_多级中断  (
  input  IR1,
  input  IR2,
  input  IR3,
  output RegWrite,
  output MemWrite,
  output [31:0] PC,
  output [31:0] IR,
  output [31:0] RDin,
  output [31:0] MDin,
  output [31:0] LedData
);

  wire AluSrcB, and_3_out, and_4_out, and_5_out, and_6_out, and_8_out, and_9_out, and_10_out, Beq, BGTZ, Bne,
       BranchTaken, CLK, clock_2_out, clrA, clrB, clrC, comparator_1_eq, comparator_2_eq, comparator_2_lt,
       comparator_3_eq, comparator_4_eq, comparator_5_eq, comparator_6_eq, comparator_7_eq, comparator_8_eq,
       comparator_9_eq, comparator_11_gt, d_ff_1_q, demultiplexer_1_out1, demultiplexer_1_out2,
       demultiplexer_1_out3, En, Equal, eret, Go, Halt, \IE中断使能寄存器_q , Int, IR1_t, IR2_t, IR3_t, IRA, IRB,
       IRC, JAL, JMP, JR, LED_EN, MemToReg, nand_1_out, not_1_out, or_4_out, or_5_out, or_7_out, or_8_out,
       or_9_out, or_10_out, or_11_out, RegDst, RST, SB, SignedExt, SLLV, Syscall, W1, W2, W3,
       \中断按键_1_与中断屏蔽位与 , \中断按键_2_与中断屏蔽位与 , \中断按键_3_与中断屏蔽位与 ;
  wire [1:0] ISR_2_q, ISR_3_q, ISR_q, multiplexer_10_out, multiplexer_15_out, newState, nowState;
  wire [2:0] multiplexer_4_out;
  wire [3:0] AluOP;
  wire [4:0] multiplexer_5_out, multiplexer_6_out, multiplexer_7_out, multiplexer_8_out, multiplexer_13_out;
  wire [12:0] CNT_num;
  wire [15:0] \总周期数 ;
  wire [27:0] PC_4;
  wire [31:0] A0, bit_extender_1_out, bit_extender_2_out, BranchAddr, epc_addr, GPRrs, Int_addr,
       mips_alu_1_result, multiplexer_2_out, multiplexer_3_out, multiplexer_9_out, multiplexer_12_out,
       multiplexer_16_out, ram_1_data, register_1_q, register_2_q, register_3_q, ret_addr, shifter_1_out,
       \按字节存储电路_1_ddata ;
  wire [31:28] JMPAddr;

  Clock #(.highDuration(1), .lowDuration(1)) clock_1 ();  // open: out
  Button _1 ();  // open: out
  Button _2 ();  // open: out
  Button _3 ();  // open: out
  Button \u_继续运行  (.out(Go));
  LED #(.active("true")) led_1 (.in(W1));
  LED #(.active("true")) led_2 (.in(W2));
  LED #(.active("true")) led_3 (.in(W3));
  Comparator #(.width(32), .mode("twosComplement")) comparator_1 (
    .a(GPRrs), .b(32'ha), .eq(comparator_1_eq));  // open: gt, lt
  Hex_Digit_Display hex_digit_display_1 (.value(LedData[31:28]));  // open: dp
  D_Flip_Flop #(.trigger("high"), .Pre_Clr_Positions("LEGACY"), .NegatePresetClear("false"), .enable("true"), .NewFFLayout("false")) d_ff_1 (.Q(d_ff_1_q));  // open: clk, D, Qn, preset, en, reset
  // Probe on 13'hca
  Hex_Digit_Display hex_digit_display_2 (.value(LedData[27:24]));  // open: dp
  Hex_Digit_Display hex_digit_display_3 (.value(LedData[23:20]));  // open: dp
  Comparator #(.width(13), .mode("twosComplement")) comparator_2 (
    .a(CNT_num), .b(13'hca), .eq(comparator_2_eq), .lt(comparator_2_lt));  // open: gt
  Clock #(.highDuration(1), .lowDuration(1)) clock_2 (.out(clock_2_out));
  and and_1 (Halt, Syscall, comparator_1_eq);
  and and_2 (LED_EN, ~comparator_1_eq, Syscall);  // AND_Gate
  \单周期硬布线控制器  \u_单周期硬布线控制器_1  (
    .Func(IR[5:0]), .OP(IR[31:26]), .ALU_OP(AluOP), .MemToReg(MemToReg), .MemWrite(MemWrite),
    .ALU_SRC(AluSrcB), .RegWrite(RegWrite), .SysCALL(Syscall), .SignedExt(SignedExt), .RegDst(RegDst),
    .JR(JR), .JMP(JMP), .Beq(Beq), .JAL(JAL), .Bne(Bne), .SB(SB), .BGTZ(BGTZ), .SLLV(SLLV));
  Hex_Digit_Display hex_digit_display_4 (.value(LedData[15:12]));  // open: dp
  Hex_Digit_Display hex_digit_display_5 (.value(LedData[19:16]));  // open: dp
  nand nand_1 (nand_1_out, d_ff_1_q, comparator_2_eq);
  Counter #(.width(13), .max('h1fff), .ongoal("stay"), .trigger("rising"), .behavior("old")) counter_1 (
    .count(comparator_2_lt), .Q(CNT_num), .clk(clock_2_out));  // open: load, D, carry, clr, preset
  Hex_Digit_Display hex_digit_display_6 (.value(LedData[7:4]));  // open: dp
  Hex_Digit_Display hex_digit_display_7 (.value(LedData[11:8]));  // open: dp
  // Probe on \总周期数 
  assign CLK = nand_1_out ? clock_2_out : 1'bz;  // Controlled_Buffer controlled_buffer_1
  Hex_Digit_Display hex_digit_display_8 (.value(LedData[3:0]));  // open: dp
  Pull_Resistor #(.pull(1)) pull_resistor_1 (.node(CLK));
  Multiplexer #(.select(3), .width(32), .disabled("Z"), .enable("false")) multiplexer_1 (
    .in0({JMPAddr, PC_4}), .in1(BranchAddr), .in2({JMPAddr, IR[25:0], 2'b00}), .in6(GPRrs), .out(ret_addr),
    .sel({JR, JMP, BranchTaken}));  // open: in3, in4, in5, in7
  or or_1 (IR1_t, IR1, IRA);
  // Probe on Int_addr
  or or_2 (IR2_t, IR2, IRB);
  Multiplexer #(.select(1), .width(32), .disabled("Z"), .enable("false")) multiplexer_2 (
    .in0(ret_addr), .in1(Int_addr), .out(multiplexer_2_out), .sel(Int));
  Multiplexer #(.select(1), .width(32), .disabled("Z"), .enable("false")) multiplexer_3 (
    .in0(multiplexer_2_out), .in1(epc_addr), .out(multiplexer_3_out), .sel(eret));
  Comparator #(.width(16), .mode("twosComplement")) comparator_3 (
    .a(16'h258), .b(\总周期数 ), .eq(comparator_3_eq));  // open: gt, lt
  Comparator #(.width(16), .mode("twosComplement")) comparator_4 (
    .a(\总周期数 ), .b(16'h1), .eq(comparator_4_eq));  // open: gt, lt
  Comparator #(.width(16), .mode("twosComplement")) comparator_5 (
    .a(\总周期数 ), .b(16'h4), .eq(comparator_5_eq));  // open: gt, lt
  Comparator #(.width(16), .mode("twosComplement")) comparator_6 (
    .a(\总周期数 ), .b(16'h7), .eq(comparator_6_eq));  // open: gt, lt
  Comparator #(.width(16), .mode("twosComplement")) comparator_7 (
    .a(\总周期数 ), .b(16'h241), .eq(comparator_7_eq));  // open: gt, lt
  or or_3 (IR3_t, IR3, IRC);
  or or_4 (or_4_out, comparator_3_eq, comparator_4_eq);
  assign IRA = or_4_out ? ~CLK : 1'bz;  // Controlled_Inverter controlled_inverter_1
  assign IRB = comparator_5_eq ? ~CLK : 1'bz;  // Controlled_Inverter controlled_inverter_2
  or or_5 (or_5_out, comparator_6_eq, comparator_7_eq);
  assign IRC = or_5_out ? ~CLK : 1'bz;  // Controlled_Inverter controlled_inverter_3
  // Probe on PC
  Register #(.width(32), .trigger("rising"), .Select("low")) u_PC (
    .D(multiplexer_3_out), .en(En), .Q(PC), .clk(CLK), .clr(RST));
  Pull_Resistor #(.pull(0)) pull_resistor_2 (.node(IRA));
  Pull_Resistor #(.pull(0)) pull_resistor_3 (.node(IRB));
  Pull_Resistor #(.pull(0)) pull_resistor_4 (.node(IRC));
  // Probe on IR
  not not_1 (not_1_out, Halt);
  Adder #(.width(32)) adder_1 (.a(PC), .b(32'h4), .out({JMPAddr, PC_4}), .cin(1'b0));  // open: cout
  or or_6 (En, not_1_out, Go);
  // Mips_Probe mips_probe_1: pin names not known; wires that end beside it: IR
  ROM #(.addrWidth(10), .dataWidth(32), .Select("high")) rom_1 (.addr(PC[11:2]), .data(IR));
  Counter #(.width(16), .max('hffff), .ongoal("wrap"), .trigger("rising"), .behavior("new")) counter_2 (
    .count(En), .Q(\总周期数 ), .clk(CLK), .clr(RST));  // open: load, D, carry, preset, down
  \中断按键  \u_中断按键_1  (.clk(CLK), .\中断源 (IRA), .\中断等待信号 (W1), .\与中断屏蔽位与 (\中断按键_1_与中断屏蔽位与 ), .\同步清零信号 (clrA));
  \中断按键  \u_中断按键_2  (.clk(CLK), .\中断源 (IRB), .\中断等待信号 (W2), .\与中断屏蔽位与 (\中断按键_2_与中断屏蔽位与 ), .\同步清零信号 (clrB));
  \中断按键  \u_中断按键_3  (.clk(CLK), .\中断源 (IRC), .\中断等待信号 (W3), .\与中断屏蔽位与 (\中断按键_3_与中断屏蔽位与 ), .\同步清零信号 (clrC));
  // Probe on \总周期数 
  Multiplexer #(.select(2), .width(3), .disabled("Z"), .enable("false")) multiplexer_4 (
    .in0(3'b111), .in1(3'b110), .in2(3'b100), .in3(3'b000), .out(multiplexer_4_out), .sel(nowState));
  Button u_RST (.out(RST));
  and and_3 (and_3_out, \中断按键_1_与中断屏蔽位与 , multiplexer_4_out[0]);
  and and_4 (and_4_out, \中断按键_2_与中断屏蔽位与 , multiplexer_4_out[1]);
  and and_5 (and_5_out, \中断按键_3_与中断屏蔽位与 , multiplexer_4_out[2]);
  Comparator #(.width(32), .mode("twosComplement")) comparator_8 (
    .a(32'h40800000), .b(IR), .eq(comparator_8_eq));  // open: gt, lt
  Comparator #(.width(32), .mode("twosComplement")) comparator_9 (
    .a(32'h40000000), .b(IR), .eq(comparator_9_eq));  // open: gt, lt
  Comparator #(.width(32), .mode("twosComplement")) comparator_10 (
    .a(32'h42000018), .b(IR), .eq(eret));  // open: gt, lt
  or or_7 (or_7_out, \中断按键_1_与中断屏蔽位与 , \中断按键_2_与中断屏蔽位与 , \中断按键_3_与中断屏蔽位与 );
  Multiplexer #(.select(1), .width(5), .disabled("Z"), .enable("false")) multiplexer_5 (
    .in0(IR[20:16]), .in1(IR[15:11]), .out(multiplexer_5_out), .sel(RegDst));
  assign bit_extender_1_out = {{16{1'b0}}, IR[15:0]};  // Bit_Extender bit_extender_1
  assign bit_extender_2_out = {{16{IR[15]}}, IR[15:0]};  // Bit_Extender bit_extender_2
  or or_8 (or_8_out, eret, ~or_7_out);  // OR_Gate
  // Probe on multiplexer_6_out
  Multiplexer #(.select(1), .width(5), .disabled("Z"), .enable("false")) multiplexer_6 (
    .in0(IR[25:21]), .in1(5'b00010), .out(multiplexer_6_out), .sel(Syscall));
  Multiplexer #(.select(1), .width(5), .disabled("Z"), .enable("false")) multiplexer_7 (
    .in0(IR[20:16]), .in1(5'b00100), .out(multiplexer_7_out), .sel(Syscall));
  // Probe on multiplexer_7_out
  // Probe on multiplexer_8_out
  Multiplexer #(.select(1), .width(5), .disabled("Z"), .enable("false")) multiplexer_8 (
    .in0(multiplexer_5_out), .in1({5{1'b1}}), .out(multiplexer_8_out), .sel(JAL));
  Multiplexer #(.select(1), .width(32), .disabled("Z"), .enable("false")) multiplexer_9 (
    .in0(bit_extender_1_out), .in1(bit_extender_2_out), .out(multiplexer_9_out), .sel(SignedExt));
  or or_9 (or_9_out, or_8_out, comparator_9_eq);
  or or_10 (or_10_out, and_3_out, and_4_out, and_5_out);
  // Probe on RDin
  and and_6 (and_6_out, ~comparator_8_eq, or_9_out);  // AND_Gate
  Priority_Encoder #(.select(2), .disabled("Z")) priority_encoder_1 (
    .in0(1'b1), .in1(and_3_out), .in2(and_4_out), .in3(and_5_out), .out(newState));  // open: gs, en_out, en_in
  // Probe on GPRrs
  MIPS_Regifile mips_regifile_1 (
    .Din(RDin), .Clk(CLK), .R1(GPRrs), .R2(A0), .WE(RegWrite), .W_num(multiplexer_8_out),
    .R1_num(multiplexer_6_out), .R2_num(multiplexer_7_out));
  Shifter #(.width(32), .shift("ll")) shifter_1 (.in(bit_extender_2_out), .\dist (5'b00010), .out(shifter_1_out));
  Register #(.width(1), .trigger("rising"), .Select("low")) \IE中断使能寄存器  (
    .D(and_6_out), .Q(\IE中断使能寄存器_q ), .clk(CLK));  // open: en, clr
  // Probe on newState
  Multiplexer #(.select(1), .width(2), .disabled("Z"), .enable("false")) multiplexer_10 (
    .in0(newState), .in1(multiplexer_15_out), .out(multiplexer_10_out), .sel(eret));
  or or_11 (or_11_out, Int, eret);
  Multiplexer #(.select(2), .width(32), .disabled("Z"), .enable("false")) multiplexer_11 (
    .in1(32'h30ac), .in2(32'h3158), .in3(32'h3204), .out(Int_addr), .sel(multiplexer_10_out));  // open: in0
  // Probe on multiplexer_12_out
  Multiplexer #(.select(1), .width(32), .disabled("Z"), .enable("false")) multiplexer_12 (
    .in0(A0), .in1(multiplexer_9_out), .out(multiplexer_12_out), .sel(AluSrcB));
  Demultiplexer #(.select(2), .width(1), .tristate("false"), .disabled("Z"), .enable("false")) demultiplexer_1 (
    .out1(demultiplexer_1_out1), .out2(demultiplexer_1_out2), .out3(demultiplexer_1_out3), .in(Int),
    .sel(newState));  // open: out0
  Demultiplexer #(.select(2), .width(1), .tristate("false"), .disabled("Z"), .enable("false")) demultiplexer_2 (
    .out1(clrA), .out2(clrB), .out3(clrC), .in(eret), .sel(nowState));  // open: out0
  and and_7 (Int, \IE中断使能寄存器_q , or_10_out);
  Register #(.width(2), .trigger("rising"), .Select("low")) \u_中断源  (
    .D(multiplexer_10_out), .en(or_11_out), .Q(nowState), .clk(CLK));  // open: clr
  and and_8 (and_8_out, Beq, Equal);
  and and_9 (and_9_out, ~Equal, Bne);  // AND_Gate
  Comparator #(.width(32), .mode("twosComplement")) comparator_11 (
    .a(GPRrs), .b({32{1'b0}}), .gt(comparator_11_gt));  // open: eq, lt
  MIPS_ALU mips_alu_1 (
    .X(GPRrs), .Y(multiplexer_12_out), .AluOP(AluOP), .Equal(Equal), .Result(mips_alu_1_result),
    .shamt(multiplexer_13_out));  // open: Result_2
  Multiplexer #(.select(1), .width(5), .disabled("Z"), .enable("false")) multiplexer_13 (
    .in0(IR[10:6]), .in1(GPRrs[4:0]), .out(multiplexer_13_out), .sel(SLLV));
  Adder #(.width(32)) adder_2 (.a(shifter_1_out), .b({JMPAddr, PC_4}), .out(BranchAddr), .cin(1'b0));  // open: cout
  // Probe on nowState
  and and_10 (and_10_out, comparator_11_gt, BGTZ);
  // Probe on mips_alu_1_result
  or or_12 (BranchTaken, and_8_out, and_9_out, and_10_out);
  Register #(.width(32), .trigger("rising"), .Select("low")) register_1 (
    .D(ret_addr), .en(demultiplexer_1_out1), .Q(register_1_q), .clk(CLK));  // open: clr
  Register #(.width(32), .trigger("rising"), .Select("low")) register_2 (
    .D(ret_addr), .en(demultiplexer_1_out2), .Q(register_2_q), .clk(CLK));  // open: clr
  Register #(.width(32), .trigger("rising"), .Select("low")) register_3 (
    .D(ret_addr), .en(demultiplexer_1_out3), .Q(register_3_q), .clk(CLK));  // open: clr
  Register #(.width(2), .trigger("rising"), .Select("low")) ISR (
    .D(nowState), .en(demultiplexer_1_out1), .Q(ISR_q), .clk(CLK));  // open: clr
  Register #(.width(2), .trigger("rising"), .Select("low")) ISR_2 (
    .D(nowState), .en(demultiplexer_1_out2), .Q(ISR_2_q), .clk(CLK));  // open: clr
  Register #(.width(2), .trigger("rising"), .Select("low")) ISR_3 (
    .D(nowState), .en(demultiplexer_1_out3), .Q(ISR_3_q), .clk(CLK));  // open: clr
  // Probe on register_1_q
  RAM #(.addrWidth(10), .dataWidth(32), .bus("separate"), .Select("high")) ram_1 (
    .addr(mips_alu_1_result[11:2]), .din(MDin), .data(ram_1_data), .str(MemWrite), .clk(CLK), .ld(1'b1));  // open: sel, clr
  Multiplexer #(.select(2), .width(32), .disabled("Z"), .enable("false")) multiplexer_14 (
    .in1(register_1_q), .in2(register_2_q), .in3(register_3_q), .out(epc_addr), .sel(nowState));  // open: in0
  // Probe on register_3_q
  \按字节存储电路  \u_按字节存储电路_1  (.cdata(A0), .sel(mips_alu_1_result), .sdata(ram_1_data), .ddata(\按字节存储电路_1_ddata ));
  // Probe on epc_addr
  Multiplexer #(.select(2), .width(2), .disabled("Z"), .enable("false")) multiplexer_15 (
    .in1(ISR_q), .in2(ISR_2_q), .in3(ISR_3_q), .out(multiplexer_15_out), .sel(nowState));  // open: in0
  Register #(.width(32), .trigger("rising"), .Select("low")) register_4 (
    .D(A0), .en(LED_EN), .Q(LedData), .clk(CLK));  // open: clr
  Multiplexer #(.select(1), .width(32), .disabled("Z"), .enable("false")) multiplexer_16 (
    .in0(mips_alu_1_result), .in1(ram_1_data), .out(multiplexer_16_out), .sel(MemToReg));
  Multiplexer #(.select(1), .width(32), .disabled("Z"), .enable("false")) multiplexer_17 (
    .in0(multiplexer_16_out), .in1({JMPAddr, PC_4}), .out(RDin), .sel(JAL));
  Multiplexer #(.select(1), .width(32), .disabled("Z"), .enable("false")) multiplexer_18 (
    .in0(A0), .in1(\按字节存储电路_1_ddata ), .out(MDin), .sel(SB));
  // Probe on RDin

  // Other names for the same wires on the sheet: GPRrt[31:0] = A0; OP[5:0] = IR[31:26]; addr[25:0] = IR[25:0];
  //   Func[5:0] = IR[5:0]; imm[15:0] = IR[15:0]; JMPAddr[27:2] = IR[25:0]; shamt[4:0] = IR[10:6]; rd[4:0] = IR[15:11];
  //   rt[4:0] = IR[20:16]; rs[4:0] = IR[25:21]; PC_4[31:28] = JMPAddr; V0[31:0] = GPRrs

  // Notes on the sheet:
  //   中断源
  //   中断等待指示
  //   总复位信号应将除ROM以外所有存储组件全部清零
  //   控制位
  //   暂停节拍，不能为0
  //   SB
  //   JMP
  //   JR
  //   SLLV
  //   OP
  //   Func
  //   用这个时钟源需要去掉电路中的其他时钟源
  //   戳工具置1进入计数暂停模式，ctrl+k时钟自动运行到对应节拍暂停
  //   ctrl+k关闭时钟连续运行，将控制位置零，进入单步调试模式调试
  //   BGTZ
  //   Beq
  //   Bne
  //   MemToReg
  //   MemWrite
  //   AluOP
  //   AluSrcB
  //   RegWrite
  //   JAL
  //   RegDst
  //   Syscall
  //   数码管输出
  //   数码管输出应该用寄存器锁存，否则显示数据只能一闪而过
  //   可计数暂停的时钟源
  //   多级中断测试信号模拟器
  //   为方便自动评测，需要输出PC，IR，寄存器堆写如数据RDin
  //   指令存储器
  //   RAM写使能MemWrite、RAM写入数据MDin等信号
  //   指令字
  //   contents of rom_1 (hex, n*v repeats v):
  //   201d07d0 20100001 109fc0 139fc3 8021 2012000c 24160008 26100001 3210000f 20080008 20090001 139900
  //   2709825 132020 20020022 c 1094022 1500fff9 22100001 2018000f 2188024 108700 20080008 20090001 139902
  //   2709825 132021 20020022 c 1094022 1500fff9 108702 2c9b022 12c00001 8000c07 4020 1084027 84400
  //   3508ffff 82021 20020022 c 8000c01 afa20000 23bd0004 afa40000 23bd0004 afb00000 23bd0004 afb30000
  //   23bd0004 afb40000 23bd0004 afb50000 23bd0004 afb60000 23bd0004 40000000 20160001 20140003 20150001
  //   168020 108100 2149825 132020 20020022 c 1600fffa 295a022 1680fff7 40800000 23bdfffc 8fb60000
  //   23bdfffc 8fb50000 23bdfffc 8fb40000 23bdfffc 8fb30000 23bdfffc 8fb00000 23bdfffc 8fa40000 23bdfffc
  //   8fa20000 42000018 afa20000 23bd0004 afa40000 23bd0004 afb00000 23bd0004 afb30000 23bd0004 afb40000
  //   23bd0004 afb50000 23bd0004 afb60000 23bd0004 40000000 20160002 20140003 20150001 168020 108100
  //   2149825 132020 20020022 c 1600fffa 295a022 1680fff7 40800000 23bdfffc 8fb60000 23bdfffc 8fb50000
  //   23bdfffc 8fb40000 23bdfffc 8fb30000 23bdfffc 8fb00000 23bdfffc 8fa40000 23bdfffc 8fa20000 42000018
  //   afa20000 23bd0004 afa40000 23bd0004 afb00000 23bd0004 afb30000 23bd0004 afb40000 23bd0004 afb50000
  //   23bd0004 afb60000 23bd0004 40000000 20160003 20140003 20150001 168020 108100 2149825 132020 20020022
  //   c 1600fffa 295a022 1680fff7 40800000 23bdfffc 8fb60000 23bdfffc 8fb50000 23bdfffc 8fb40000 23bdfffc
  //   8fb30000 23bdfffc 8fb00000 23bdfffc 8fa40000 23bdfffc 8fa20000 42000018
  //   OP
  //   Func
  //   rs
  //   rt
  //   rd
  //   imm
  //   addr
  //   mtco关中断
  //   mfco开中断
  //   eret指令
  //   有中断
  //   符号扩展
  //   中断程序入口地址
  //   中断请求
  //   EPC寄存器
endmodule

module \封装正确性测试  (
);

  wire IR1, IR2, IR3, MemW, RegW;
  wire [31:0] EX_PC, ID_PC, IF_PC, IR, LED, MDin, MDinr, MEM_PC, PC, RDin, RDinr, WB_PC;

  \单周期MIPS  \u_单周期mips_1  (
    .IR1(IR1), .IR2(IR2), .IR3(IR3), .RegWrite(RegW), .MemWrite(MemW), .PC(PC), .IR(IR), .RDin(RDin),
    .MDin(MDin), .LedData(LED));
  \气泡流水线  \u_气泡流水线_1  (
    .RegWrite(RegW), .MemWrite(MemW), .IF_PC(IF_PC), .ID_PC(ID_PC), .EX_PC(EX_PC), .M_PC(MEM_PC),
    .WB_PC(WB_PC), .RDin(RDinr), .MDin(MDinr), .LedData(LED));
  \单周期MIPS_单级中断  \u_单周期mips_单级中断_1  (
    .IR1(IR1), .IR2(IR2), .IR3(IR3), .RegWrite(RegW), .MemWrite(MemW), .PC(PC), .IR(IR), .RDin(RDin),
    .MDin(MDin), .LedData(LED));
  \理想流水线  \u_理想流水线_1  (
    .RegWrite(RegW), .MemWrite(MemW), .IF_PC(IF_PC), .ID_PC(ID_PC), .EX_PC(EX_PC), .M_PC(MEM_PC),
    .WB_PC(WB_PC), .RDin(RDinr), .MDin(MDinr), .LedData(LED));
  \重定向流水线  \u_重定向流水线_1  (
    .RegWrite(RegW), .MemWrite(MemW), .IF_PC(IF_PC), .ID_PC(ID_PC), .EX_PC(EX_PC), .M_PC(MEM_PC),
    .WB_PC(WB_PC), .RDin(RDinr), .MDin(MDinr), .LedData(LED));
  \单周期MIPS_多级中断  \u_单周期mips_多级中断_1  (
    .IR1(IR1), .IR2(IR2), .IR3(IR3), .RegWrite(RegW), .MemWrite(MemW), .PC(PC), .IR(IR), .RDin(RDin),
    .MDin(MDin), .LedData(LED));

  // Notes on the sheet:
  //   单周期封装测试
  //   气泡流水封装测试
  //   单周期+单级中断封装测试
  //   请检查上面封装有无位宽不匹配，引脚标签是否和连接的标签相对应，否则无法在educoder平台上正确测试
  //   理想流水封装测试
  //   重定向流水封装测试
  //   单周期+多级中断封装测试
endmodule

module IF_ID (
  input  [31:0] PC,
  input  [31:0] IR,
  input  [31:0] PC_4,
  input  PredictJump,
  input  EN,
  input  Clk,
  input  \异步清0 ,
  input  \同步清0 ,
  output [31:0] PC_2,
  output [31:0] IR_2,
  output [31:0] PC_4_2,
  output PredictJump_2
);

  wire multiplexer_4_out, pull_resistor_2_node;
  wire [31:0] multiplexer_1_out, multiplexer_2_out, multiplexer_3_out;

  Pull_Resistor #(.pull(0)) pull_resistor_1 (.node(\同步清0 ));
  Multiplexer #(.select(1), .width(32), .disabled("Z"), .enable("false")) multiplexer_1 (
    .in0(PC), .in1({32{1'b0}}), .out(multiplexer_1_out), .sel(\同步清0 ));
  Multiplexer #(.select(1), .width(32), .disabled("Z"), .enable("false")) multiplexer_2 (
    .in0(IR), .in1({32{1'b0}}), .out(multiplexer_2_out), .sel(\同步清0 ));
  Multiplexer #(.select(1), .width(32), .disabled("Z"), .enable("false")) multiplexer_3 (
    .in0(PC_4), .in1({32{1'b0}}), .out(multiplexer_3_out), .sel(\同步清0 ));
  Pull_Resistor #(.pull(0)) pull_resistor_2 (.node(pull_resistor_2_node));
  Multiplexer #(.select(1), .width(1), .disabled("Z"), .enable("false")) multiplexer_4 (
    .in0(PredictJump), .in1(1'b0), .out(multiplexer_4_out), .sel(\同步清0 ));
  or or_1 (pull_resistor_2_node, \同步清0 , EN);
  Register #(.width(32), .trigger("rising"), .Select("low")) register_1 (
    .D(multiplexer_1_out), .en(pull_resistor_2_node), .Q(PC_2), .clk(Clk), .clr(\异步清0 ));
  Register #(.width(32), .trigger("rising"), .Select("low")) register_2 (
    .D(multiplexer_2_out), .en(pull_resistor_2_node), .Q(IR_2), .clk(Clk), .clr(\异步清0 ));
  Register #(.width(32), .trigger("rising"), .Select("low")) register_3 (
    .D(multiplexer_3_out), .en(pull_resistor_2_node), .Q(PC_4_2), .clk(Clk), .clr(\异步清0 ));
  Register #(.width(1), .trigger("rising"), .Select("low")) register_4 (
    .D(multiplexer_4_out), .en(pull_resistor_2_node), .Q(PredictJump_2), .clk(Clk), .clr(\异步清0 ));

  // Other names for the same wires on the sheet: reset = \同步清0 
endmodule

module ID_EX (
  input  syscall,
  input  SB,
  input  SLLV,
  input  BGTZ,
  input  JMP,
  input  JR,
  input  SignEXt,
  input  Beq,
  input  Bne,
  input  MemToReg,
  input  MemWrite,
  input  [3:0] AluOP,
  input  AluSrcB,
  input  RegWrite,
  input  JAL,
  input  [1:0] RS_F,
  input  [31:0] PC,
  input  [31:0] IR,
  input  [31:0] RS,
  input  [31:0] RT,
  input  [4:0] WriteReg_num,
  input  [1:0] RT_F,
  input  [31:0] PC_4,
  input  PredictJump,
  input  \同步清0 ,
  input  EN,
  input  Clk,
  input  \异步清0 ,
  output syscall_2,
  output SB_2,
  output SLLV_2,
  output BGTZ_2,
  output JMP_2,
  output JR_2,
  output SignEXt_2,
  output Beq_2,
  output Bne_2,
  output MemToReg_2,
  output MemWrite_2,
  output [3:0] AluOP_2,
  output AluSrcB_2,
  output RegWrite_2,
  output JAL_2,
  output [1:0] RS_F_2,
  output [31:0] PC_2,
  output [31:0] IR_2,
  output [31:0] RS_2,
  output [31:0] RT_2,
  output [4:0] WriteReg_num_2,
  output [1:0] RT_F_2,
  output [31:0] PC_4_2,
  output PredictJump_2
);

  wire multiplexer_1_out, multiplexer_2_out, multiplexer_3_out, multiplexer_4_out, multiplexer_5_out,
       multiplexer_6_out, multiplexer_7_out, multiplexer_8_out, multiplexer_9_out, multiplexer_10_out,
       multiplexer_11_out, multiplexer_13_out, multiplexer_14_out, multiplexer_15_out, multiplexer_24_out;
  wire [1:0] multiplexer_16_out, multiplexer_22_out;
  wire [3:0] multiplexer_12_out;
  wire [4:0] multiplexer_21_out;
  wire [31:0] multiplexer_17_out, multiplexer_18_out, multiplexer_19_out, multiplexer_20_out,
       multiplexer_23_out;

  Pull_Resistor #(.pull(0)) pull_resistor_1 (.node(EN));
  Multiplexer #(.select(1), .width(1), .disabled("Z"), .enable("false")) multiplexer_1 (
    .in0(syscall), .in1(1'b0), .out(multiplexer_1_out), .sel(\同步清0 ));
  Multiplexer #(.select(1), .width(1), .disabled("Z"), .enable("false")) multiplexer_2 (
    .in0(SB), .in1(1'b0), .out(multiplexer_2_out), .sel(\同步清0 ));
  Multiplexer #(.select(1), .width(1), .disabled("Z"), .enable("false")) multiplexer_3 (
    .in0(SLLV), .in1(1'b0), .out(multiplexer_3_out), .sel(\同步清0 ));
  Multiplexer #(.select(1), .width(1), .disabled("Z"), .enable("false")) multiplexer_4 (
    .in0(BGTZ), .in1(1'b0), .out(multiplexer_4_out), .sel(\同步清0 ));
  Multiplexer #(.select(1), .width(1), .disabled("Z"), .enable("false")) multiplexer_5 (
    .in0(JMP), .in1(1'b0), .out(multiplexer_5_out), .sel(\同步清0 ));
  Multiplexer #(.select(1), .width(1), .disabled("Z"), .enable("false")) multiplexer_6 (
    .in0(JR), .in1(1'b0), .out(multiplexer_6_out), .sel(\同步清0 ));
  Multiplexer #(.select(1), .width(1), .disabled("Z"), .enable("false")) multiplexer_7 (
    .in0(SignEXt), .in1(1'b0), .out(multiplexer_7_out), .sel(\同步清0 ));
  Multiplexer #(.select(1), .width(1), .disabled("Z"), .enable("false")) multiplexer_8 (
    .in0(Beq), .in1(1'b0), .out(multiplexer_8_out), .sel(\同步清0 ));
  Multiplexer #(.select(1), .width(1), .disabled("Z"), .enable("false")) multiplexer_9 (
    .in0(Bne), .in1(1'b0), .out(multiplexer_9_out), .sel(\同步清0 ));
  Multiplexer #(.select(1), .width(1), .disabled("Z"), .enable("false")) multiplexer_10 (
    .in0(MemToReg), .in1(1'b0), .out(multiplexer_10_out), .sel(\同步清0 ));
  Multiplexer #(.select(1), .width(1), .disabled("Z"), .enable("false")) multiplexer_11 (
    .in0(MemWrite), .in1(1'b0), .out(multiplexer_11_out), .sel(\同步清0 ));
  Multiplexer #(.select(1), .width(4), .disabled("Z"), .enable("false")) multiplexer_12 (
    .in0(AluOP), .in1(4'b0000), .out(multiplexer_12_out), .sel(\同步清0 ));
  Multiplexer #(.select(1), .width(1), .disabled("Z"), .enable("false")) multiplexer_13 (
    .in0(AluSrcB), .in1(1'b0), .out(multiplexer_13_out), .sel(\同步清0 ));
  Multiplexer #(.select(1), .width(1), .disabled("Z"), .enable("false")) multiplexer_14 (
    .in0(RegWrite), .in1(1'b0), .out(multiplexer_14_out), .sel(\同步清0 ));
  Multiplexer #(.select(1), .width(1), .disabled("Z"), .enable("false")) multiplexer_15 (
    .in0(JAL), .in1(1'b0), .out(multiplexer_15_out), .sel(\同步清0 ));
  Multiplexer #(.select(1), .width(2), .disabled("Z"), .enable("false")) multiplexer_16 (
    .in0(RS_F), .in1(2'b00), .out(multiplexer_16_out), .sel(\同步清0 ));
  Multiplexer #(.select(1), .width(32), .disabled("Z"), .enable("false")) multiplexer_17 (
    .in0(PC), .in1({32{1'b0}}), .out(multiplexer_17_out), .sel(\同步清0 ));
  Multiplexer #(.select(1), .width(32), .disabled("Z"), .enable("false")) multiplexer_18 (
    .in0(IR), .in1({32{1'b0}}), .out(multiplexer_18_out), .sel(\同步清0 ));
  Multiplexer #(.select(1), .width(32), .disabled("Z"), .enable("false")) multiplexer_19 (
    .in0(RS), .in1({32{1'b0}}), .out(multiplexer_19_out), .sel(\同步清0 ));
  Multiplexer #(.select(1), .width(32), .disabled("Z"), .enable("false")) multiplexer_20 (
    .in0(RT), .in1({32{1'b0}}), .out(multiplexer_20_out), .sel(\同步清0 ));
  Multiplexer #(.select(1), .width(5), .disabled("Z"), .enable("false")) multiplexer_21 (
    .in0(WriteReg_num), .in1({5{1'b0}}), .out(multiplexer_21_out), .sel(\同步清0 ));
  Multiplexer #(.select(1), .width(2), .disabled("Z"), .enable("false")) multiplexer_22 (
    .in0(RT_F), .in1(2'b00), .out(multiplexer_22_out), .sel(\同步清0 ));
  Multiplexer #(.select(1), .width(32), .disabled("Z"), .enable("false")) multiplexer_23 (
    .in0(PC_4), .in1({32{1'b0}}), .out(multiplexer_23_out), .sel(\同步清0 ));
  Multiplexer #(.select(1), .width(1), .disabled("Z"), .enable("false")) multiplexer_24 (
    .in0(PredictJump), .in1(1'b0), .out(multiplexer_24_out), .sel(\同步清0 ));
  Register #(.width(1), .trigger("rising"), .Select("low")) register_1 (
    .D(multiplexer_1_out), .en(EN), .Q(syscall_2), .clk(Clk), .clr(\异步清0 ));
  Register #(.width(1), .trigger("rising"), .Select("low")) register_2 (
    .D(multiplexer_2_out), .en(EN), .Q(SB_2), .clk(Clk), .clr(\异步清0 ));
  Register #(.width(1), .trigger("rising"), .Select("low")) register_3 (
    .D(multiplexer_3_out), .en(EN), .Q(SLLV_2), .clk(Clk), .clr(\异步清0 ));
  Register #(.width(1), .trigger("rising"), .Select("low")) register_4 (
    .D(multiplexer_4_out), .en(EN), .Q(BGTZ_2), .clk(Clk), .clr(\异步清0 ));
  Register #(.width(1), .trigger("rising"), .Select("low")) register_5 (
    .D(multiplexer_5_out), .en(EN), .Q(JMP_2), .clk(Clk), .clr(\异步清0 ));
  Register #(.width(1), .trigger("rising"), .Select("low")) register_6 (
    .D(multiplexer_6_out), .en(EN), .Q(JR_2), .clk(Clk), .clr(\异步清0 ));
  Register #(.width(1), .trigger("rising"), .Select("low")) register_7 (
    .D(multiplexer_7_out), .en(EN), .Q(SignEXt_2), .clk(Clk), .clr(\异步清0 ));
  Register #(.width(1), .trigger("rising"), .Select("low")) register_8 (
    .D(multiplexer_8_out), .en(EN), .Q(Beq_2), .clk(Clk), .clr(\异步清0 ));
  Register #(.width(1), .trigger("rising"), .Select("low")) register_9 (
    .D(multiplexer_9_out), .en(EN), .Q(Bne_2), .clk(Clk), .clr(\异步清0 ));
  Register #(.width(1), .trigger("rising"), .Select("low")) register_10 (
    .D(multiplexer_10_out), .en(EN), .Q(MemToReg_2), .clk(Clk), .clr(\异步清0 ));
  Register #(.width(1), .trigger("rising"), .Select("low")) register_11 (
    .D(multiplexer_11_out), .en(EN), .Q(MemWrite_2), .clk(Clk), .clr(\异步清0 ));
  Register #(.width(4), .trigger("rising"), .Select("low")) register_12 (
    .D(multiplexer_12_out), .en(EN), .Q(AluOP_2), .clk(Clk), .clr(\异步清0 ));
  Register #(.width(1), .trigger("rising"), .Select("low")) register_13 (
    .D(multiplexer_13_out), .en(EN), .Q(AluSrcB_2), .clk(Clk), .clr(\异步清0 ));
  Register #(.width(1), .trigger("rising"), .Select("low")) register_14 (
    .D(multiplexer_14_out), .en(EN), .Q(RegWrite_2), .clk(Clk), .clr(\异步清0 ));
  Register #(.width(1), .trigger("rising"), .Select("low")) register_15 (
    .D(multiplexer_15_out), .en(EN), .Q(JAL_2), .clk(Clk), .clr(\异步清0 ));
  Register #(.width(2), .trigger("rising"), .Select("low")) register_16 (
    .D(multiplexer_16_out), .en(EN), .Q(RS_F_2), .clk(Clk), .clr(\异步清0 ));
  Register #(.width(32), .trigger("rising"), .Select("low")) register_17 (
    .D(multiplexer_17_out), .en(EN), .Q(PC_2), .clk(Clk), .clr(\异步清0 ));
  Register #(.width(32), .trigger("rising"), .Select("low")) register_18 (
    .D(multiplexer_18_out), .en(EN), .Q(IR_2), .clk(Clk), .clr(\异步清0 ));
  Register #(.width(32), .trigger("rising"), .Select("low")) register_19 (
    .D(multiplexer_19_out), .en(EN), .Q(RS_2), .clk(Clk), .clr(\异步清0 ));
  Register #(.width(32), .trigger("rising"), .Select("low")) register_20 (
    .D(multiplexer_20_out), .en(EN), .Q(RT_2), .clk(Clk), .clr(\异步清0 ));
  Register #(.width(5), .trigger("rising"), .Select("low")) register_21 (
    .D(multiplexer_21_out), .en(EN), .Q(WriteReg_num_2), .clk(Clk), .clr(\异步清0 ));
  Register #(.width(2), .trigger("rising"), .Select("low")) register_22 (
    .D(multiplexer_22_out), .en(EN), .Q(RT_F_2), .clk(Clk), .clr(\异步清0 ));
  Register #(.width(32), .trigger("rising"), .Select("low")) register_23 (
    .D(multiplexer_23_out), .en(EN), .Q(PC_4_2), .clk(Clk), .clr(\异步清0 ));
  Register #(.width(1), .trigger("rising"), .Select("low")) register_24 (
    .D(multiplexer_24_out), .en(EN), .Q(PredictJump_2), .clk(Clk), .clr(\异步清0 ));
  // Probe on RS_2
  Pull_Resistor #(.pull(0)) pull_resistor_2 (.node(\同步清0 ));

  // Other names for the same wires on the sheet: reset = \同步清0 
endmodule

module EX_MEM (
  input  SB,
  input  JMP,
  input  JR,
  input  MemToReg,
  input  MemWrite,
  input  RegWrite,
  input  JAL,
  input  syscall,
  input  [31:0] PC,
  input  [31:0] IR,
  input  [31:0] Result,
  input  [31:0] Writedata,
  input  [4:0] WriteReg_num,
  input  [31:0] R1,
  input  \同步清0 ,
  input  EN,
  input  Clk,
  input  Rst,
  output SB_2,
  output JMP_2,
  output JR_2,
  output MemToReg_2,
  output MemWrite_2,
  output RegWrite_2,
  output JAL_2,
  output syscall_2,
  output [31:0] PC_2,
  output [31:0] IR_2,
  output [31:0] Result_2,
  output [31:0] Writedata_2,
  output [4:0] WriteReg_num_2,
  output [31:0] R1_2
);

  wire multiplexer_1_out, multiplexer_2_out, multiplexer_3_out, multiplexer_4_out, multiplexer_5_out,
       multiplexer_6_out, multiplexer_7_out, multiplexer_8_out;
  wire [4:0] multiplexer_13_out;
  wire [31:0] multiplexer_9_out, multiplexer_10_out, multiplexer_11_out, multiplexer_12_out,
       multiplexer_14_out;

  Pull_Resistor #(.pull(0)) pull_resistor_1 (.node(\同步清0 ));
  Multiplexer #(.select(1), .width(1), .disabled("Z"), .enable("false")) multiplexer_1 (
    .in0(SB), .in1(1'b0), .out(multiplexer_1_out), .sel(\同步清0 ));
  Multiplexer #(.select(1), .width(1), .disabled("Z"), .enable("false")) multiplexer_2 (
    .in0(JMP), .in1(1'b0), .out(multiplexer_2_out), .sel(\同步清0 ));
  Multiplexer #(.select(1), .width(1), .disabled("Z"), .enable("false")) multiplexer_3 (
    .in0(JR), .in1(1'b0), .out(multiplexer_3_out), .sel(\同步清0 ));
  Multiplexer #(.select(1), .width(1), .disabled("Z"), .enable("false")) multiplexer_4 (
    .in0(MemToReg), .in1(1'b0), .out(multiplexer_4_out), .sel(\同步清0 ));
  Multiplexer #(.select(1), .width(1), .disabled("Z"), .enable("false")) multiplexer_5 (
    .in0(MemWrite), .in1(1'b0), .out(multiplexer_5_out), .sel(\同步清0 ));
  Pull_Resistor #(.pull(0)) pull_resistor_2 (.node(EN));
  Multiplexer #(.select(1), .width(1), .disabled("Z"), .enable("false")) multiplexer_6 (
    .in0(RegWrite), .in1(1'b0), .out(multiplexer_6_out), .sel(\同步清0 ));
  Multiplexer #(.select(1), .width(1), .disabled("Z"), .enable("false")) multiplexer_7 (
    .in0(JAL), .in1(1'b0), .out(multiplexer_7_out), .sel(\同步清0 ));
  Multiplexer #(.select(1), .width(1), .disabled("Z"), .enable("false")) multiplexer_8 (
    .in0(syscall), .in1(1'b0), .out(multiplexer_8_out), .sel(\同步清0 ));
  Multiplexer #(.select(1), .width(32), .disabled("Z"), .enable("false")) multiplexer_9 (
    .in0(PC), .in1({32{1'b0}}), .out(multiplexer_9_out), .sel(\同步清0 ));
  Multiplexer #(.select(1), .width(32), .disabled("Z"), .enable("false")) multiplexer_10 (
    .in0(IR), .in1({32{1'b0}}), .out(multiplexer_10_out), .sel(\同步清0 ));
  Multiplexer #(.select(1), .width(32), .disabled("Z"), .enable("false")) multiplexer_11 (
    .in0(Result), .in1({32{1'b0}}), .out(multiplexer_11_out), .sel(\同步清0 ));
  Multiplexer #(.select(1), .width(32), .disabled("Z"), .enable("false")) multiplexer_12 (
    .in0(Writedata), .in1({32{1'b0}}), .out(multiplexer_12_out), .sel(\同步清0 ));
  Multiplexer #(.select(1), .width(5), .disabled("Z"), .enable("false")) multiplexer_13 (
    .in0(WriteReg_num), .in1({5{1'b0}}), .out(multiplexer_13_out), .sel(\同步清0 ));
  Multiplexer #(.select(1), .width(32), .disabled("Z"), .enable("false")) multiplexer_14 (
    .in0(R1), .in1({32{1'b0}}), .out(multiplexer_14_out), .sel(\同步清0 ));
  Register #(.width(1), .trigger("rising"), .Select("low")) register_1 (
    .D(multiplexer_1_out), .en(EN), .Q(SB_2), .clk(Clk), .clr(Rst));
  Register #(.width(1), .trigger("rising"), .Select("low")) register_2 (
    .D(multiplexer_2_out), .en(EN), .Q(JMP_2), .clk(Clk), .clr(Rst));
  Register #(.width(1), .trigger("rising"), .Select("low")) register_3 (
    .D(multiplexer_3_out), .en(EN), .Q(JR_2), .clk(Clk), .clr(Rst));
  Register #(.width(1), .trigger("rising"), .Select("low")) register_4 (
    .D(multiplexer_4_out), .en(EN), .Q(MemToReg_2), .clk(Clk), .clr(Rst));
  Register #(.width(1), .trigger("rising"), .Select("low")) register_5 (
    .D(multiplexer_5_out), .en(EN), .Q(MemWrite_2), .clk(Clk), .clr(Rst));
  Register #(.width(1), .trigger("rising"), .Select("low")) register_6 (
    .D(multiplexer_6_out), .en(EN), .Q(RegWrite_2), .clk(Clk), .clr(Rst));
  Register #(.width(1), .trigger("rising"), .Select("low")) register_7 (
    .D(multiplexer_7_out), .en(EN), .Q(JAL_2), .clk(Clk), .clr(Rst));
  Register #(.width(1), .trigger("rising"), .Select("low")) register_8 (
    .D(multiplexer_8_out), .en(Clk), .Q(syscall_2), .clk(Clk), .clr(Rst));
  Register #(.width(32), .trigger("rising"), .Select("low")) register_9 (
    .D(multiplexer_9_out), .en(EN), .Q(PC_2), .clk(Clk), .clr(Rst));
  Register #(.width(32), .trigger("rising"), .Select("low")) register_10 (
    .D(multiplexer_10_out), .en(EN), .Q(IR_2), .clk(Clk), .clr(Rst));
  Register #(.width(32), .trigger("rising"), .Select("low")) register_11 (
    .D(multiplexer_11_out), .en(EN), .Q(Result_2), .clk(Clk), .clr(Rst));
  Register #(.width(32), .trigger("rising"), .Select("low")) register_12 (
    .D(multiplexer_12_out), .en(EN), .Q(Writedata_2), .clk(Clk), .clr(Rst));
  Register #(.width(5), .trigger("rising"), .Select("low")) register_13 (
    .D(multiplexer_13_out), .en(EN), .Q(WriteReg_num_2), .clk(Clk), .clr(Rst));
  Register #(.width(32), .trigger("rising"), .Select("low")) register_14 (
    .D(multiplexer_14_out), .en(EN), .Q(R1_2), .clk(Clk), .clr(Rst));

  // Other names for the same wires on the sheet: reset = \同步清0 
endmodule

module MEM_WB (
  input  JMP,
  input  JR,
  input  MemToReg,
  input  RegWrite,
  input  JAL,
  input  syscall,
  input  [31:0] PC,
  input  [31:0] IR,
  input  [31:0] Result,
  input  [31:0] Memdata,
  input  [4:0] WriteReg_num,
  input  [31:0] R1,
  input  [31:0] R2,
  input  \同步清0 ,
  input  En,
  input  Clk,
  input  Rst,
  output JMP_2,
  output JR_2,
  output MemToReg_2,
  output RegWrite_2,
  output JAL_2,
  output syscall_2,
  output [31:0] PC_2,
  output [31:0] IR_2,
  output [31:0] Result_2,
  output [31:0] Memdata_2,
  output [4:0] WriteReg_num_2,
  output [31:0] R1_2,
  output [31:0] R1_3
);

  wire multiplexer_1_out, multiplexer_2_out, multiplexer_3_out, multiplexer_4_out, multiplexer_5_out,
       multiplexer_6_out;
  wire [4:0] multiplexer_11_out;
  wire [31:0] multiplexer_7_out, multiplexer_8_out, multiplexer_9_out, multiplexer_10_out,
       multiplexer_12_out, multiplexer_13_out;

  Pull_Resistor #(.pull(0)) pull_resistor_1 (.node(\同步清0 ));
  Multiplexer #(.select(1), .width(1), .disabled("Z"), .enable("false")) multiplexer_1 (
    .in0(JMP), .in1(1'b0), .out(multiplexer_1_out), .sel(\同步清0 ));
  Multiplexer #(.select(1), .width(1), .disabled("Z"), .enable("false")) multiplexer_2 (
    .in0(JR), .in1(1'b0), .out(multiplexer_2_out), .sel(\同步清0 ));
  Multiplexer #(.select(1), .width(1), .disabled("Z"), .enable("false")) multiplexer_3 (
    .in0(MemToReg), .in1(1'b0), .out(multiplexer_3_out), .sel(\同步清0 ));
  Pull_Resistor #(.pull(0)) pull_resistor_2 (.node(En));
  Multiplexer #(.select(1), .width(1), .disabled("Z"), .enable("false")) multiplexer_4 (
    .in0(RegWrite), .in1(1'b0), .out(multiplexer_4_out), .sel(\同步清0 ));
  Multiplexer #(.select(1), .width(1), .disabled("Z"), .enable("false")) multiplexer_5 (
    .in0(JAL), .in1(1'b0), .out(multiplexer_5_out), .sel(\同步清0 ));
  Multiplexer #(.select(1), .width(1), .disabled("Z"), .enable("false")) multiplexer_6 (
    .in0(syscall), .in1(1'b0), .out(multiplexer_6_out), .sel(\同步清0 ));
  Multiplexer #(.select(1), .width(32), .disabled("Z"), .enable("false")) multiplexer_7 (
    .in0(PC), .in1({32{1'b0}}), .out(multiplexer_7_out), .sel(\同步清0 ));
  Multiplexer #(.select(1), .width(32), .disabled("Z"), .enable("false")) multiplexer_8 (
    .in0(IR), .in1({32{1'b0}}), .out(multiplexer_8_out), .sel(\同步清0 ));
  Multiplexer #(.select(1), .width(32), .disabled("Z"), .enable("false")) multiplexer_9 (
    .in0(Result), .in1({32{1'b0}}), .out(multiplexer_9_out), .sel(\同步清0 ));
  Multiplexer #(.select(1), .width(32), .disabled("Z"), .enable("false")) multiplexer_10 (
    .in0(Memdata), .in1({32{1'b0}}), .out(multiplexer_10_out), .sel(\同步清0 ));
  Multiplexer #(.select(1), .width(5), .disabled("Z"), .enable("false")) multiplexer_11 (
    .in0(WriteReg_num), .in1({5{1'b0}}), .out(multiplexer_11_out), .sel(\同步清0 ));
  Multiplexer #(.select(1), .width(32), .disabled("Z"), .enable("false")) multiplexer_12 (
    .in0(R1), .in1({32{1'b0}}), .out(multiplexer_12_out), .sel(\同步清0 ));
  Multiplexer #(.select(1), .width(32), .disabled("Z"), .enable("false")) multiplexer_13 (
    .in0(R2), .in1({32{1'b0}}), .out(multiplexer_13_out), .sel(\同步清0 ));
  Register #(.width(1), .trigger("rising"), .Select("low")) register_1 (
    .D(multiplexer_1_out), .en(En), .Q(JMP_2), .clk(Clk), .clr(Rst));
  Register #(.width(1), .trigger("rising"), .Select("low")) register_2 (
    .D(multiplexer_2_out), .en(En), .Q(JR_2), .clk(Clk), .clr(Rst));
  Register #(.width(1), .trigger("rising"), .Select("low")) register_3 (
    .D(multiplexer_3_out), .en(En), .Q(MemToReg_2), .clk(Clk), .clr(Rst));
  Register #(.width(1), .trigger("rising"), .Select("low")) register_4 (
    .D(multiplexer_4_out), .en(En), .Q(RegWrite_2), .clk(Clk), .clr(Rst));
  Register #(.width(1), .trigger("rising"), .Select("low")) register_5 (
    .D(multiplexer_5_out), .en(En), .Q(JAL_2), .clk(Clk), .clr(Rst));
  Register #(.width(1), .trigger("rising"), .Select("low")) register_6 (
    .D(multiplexer_6_out), .en(En), .Q(syscall_2), .clk(Clk), .clr(Rst));
  Register #(.width(32), .trigger("rising"), .Select("low")) register_7 (
    .D(multiplexer_7_out), .en(En), .Q(PC_2), .clk(Clk), .clr(Rst));
  Register #(.width(32), .trigger("rising"), .Select("low")) register_8 (
    .D(multiplexer_8_out), .en(En), .Q(IR_2), .clk(Clk), .clr(Rst));
  Register #(.width(32), .trigger("rising"), .Select("low")) register_9 (
    .D(multiplexer_9_out), .en(En), .Q(Result_2), .clk(Clk), .clr(Rst));
  Register #(.width(32), .trigger("rising"), .Select("low")) register_10 (
    .D(multiplexer_10_out), .en(En), .Q(Memdata_2), .clk(Clk), .clr(Rst));
  Register #(.width(5), .trigger("rising"), .Select("low")) register_11 (
    .D(multiplexer_11_out), .en(En), .Q(WriteReg_num_2), .clk(Clk), .clr(Rst));
  Register #(.width(32), .trigger("rising"), .Select("low")) register_12 (
    .D(multiplexer_12_out), .en(En), .Q(R1_2), .clk(Clk), .clr(Rst));
  Register #(.width(32), .trigger("rising"), .Select("low")) register_13 (
    .D(multiplexer_13_out), .en(En), .Q(R1_3), .clk(Clk), .clr(Rst));

  // Other names for the same wires on the sheet: reset = \同步清0 
endmodule

module \按字节存储电路  (
  input  [31:0] sdata,
  input  [31:0] cdata,
  input  [31:0] sel,
  output [31:0] ddata
);

  Multiplexer #(.select(2), .width(32), .disabled("Z"), .enable("false")) multiplexer_1 (
    .in0({sdata[31:8], cdata[7:0]}), .in1({sdata[31:16], cdata[7:0], sdata[7:0]}),
    .in2({sdata[31:24], cdata[7:0], sdata[15:0]}), .in3({cdata[7:0], sdata[23:0]}), .out(ddata),
    .sel(sel[1:0]));
endmodule

module \相关处理逻辑  (
  input  [31:0] Instr,
  input  EX_RegWrite,
  input  [4:0] EX_W_num,
  input  BranchTaken,
  input  MEM_RegWrite,
  input  [4:0] MEM_W_num,
  output stall,
  output flush
);

  wire and_1_out, and_2_out, and_3_out, and_4_out, comparator_2_eq, comparator_3_eq, comparator_4_eq,
       comparator_5_eq, comparator_6_eq, comparator_7_eq, Instr_sys, not_1_out, not_2_out,
       rs_rtused_1_rsused, rs_rtused_1_rtused;
  wire [4:0] multiplexer_1_out, multiplexer_2_out;

  Multiplexer #(.select(1), .width(5), .disabled("Z"), .enable("false")) multiplexer_1 (
    .in0(Instr[25:21]), .in1(5'b00010), .out(multiplexer_1_out), .sel(Instr_sys));
  Multiplexer #(.select(1), .width(5), .disabled("Z"), .enable("false")) multiplexer_2 (
    .in0(Instr[20:16]), .in1(5'b00100), .out(multiplexer_2_out), .sel(Instr_sys));
  Comparator #(.width(32), .mode("twosComplement")) comparator_1 (
    .a(Instr), .b(32'hc), .eq(Instr_sys));  // open: gt, lt
  RS_RTUsed rs_rtused_1 (
    .OP0(Instr[26]), .OP1(Instr[27]), .OP2(Instr[28]), .OP3(Instr[29]), .OP4(Instr[30]), .OP5(Instr[31]),
    .F0(Instr[0]), .F1(Instr[1]), .F2(Instr[2]), .F3(Instr[3]), .F4(Instr[4]), .F5(Instr[5]),
    .RsUsed(rs_rtused_1_rsused), .RtUsed(rs_rtused_1_rtused));
  not not_1 (not_1_out, comparator_2_eq);
  Comparator #(.width(5), .mode("twosComplement")) comparator_2 (
    .a(multiplexer_1_out), .b({5{1'b0}}), .eq(comparator_2_eq));  // open: gt, lt
  not not_2 (not_2_out, comparator_3_eq);
  Comparator #(.width(5), .mode("twosComplement")) comparator_3 (
    .a({5{1'b0}}), .b(multiplexer_2_out), .eq(comparator_3_eq));  // open: gt, lt
  Comparator #(.width(5), .mode("twosComplement")) comparator_4 (
    .a(multiplexer_1_out), .b(EX_W_num), .eq(comparator_4_eq));  // open: gt, lt
  Comparator #(.width(5), .mode("twosComplement")) comparator_5 (
    .a(EX_W_num), .b(multiplexer_2_out), .eq(comparator_5_eq));  // open: gt, lt
  Comparator #(.width(5), .mode("twosComplement")) comparator_6 (
    .a(multiplexer_1_out), .b(MEM_W_num), .eq(comparator_6_eq));  // open: gt, lt
  Comparator #(.width(5), .mode("twosComplement")) comparator_7 (
    .a(MEM_W_num), .b(multiplexer_2_out), .eq(comparator_7_eq));  // open: gt, lt
  and and_1 (and_1_out, rs_rtused_1_rsused, not_1_out, EX_RegWrite, comparator_4_eq);
  and and_2 (and_2_out, rs_rtused_1_rtused, not_2_out, EX_RegWrite, comparator_5_eq);
  and and_3 (and_3_out, rs_rtused_1_rsused, not_1_out, MEM_RegWrite, comparator_6_eq);
  and and_4 (and_4_out, rs_rtused_1_rtused, not_2_out, MEM_RegWrite, comparator_7_eq);
  or or_1 (stall, and_1_out, and_2_out, and_3_out, and_4_out);
  or or_2 (flush, stall, BranchTaken);

  // Notes on the sheet:
  //   rs
  //   rt
  //   OP
  //   FUNCT
  //   Rt_Used
  //   Rs_Used
  //   rs≠0
  //   rt≠0
  //   dataHazzard
endmodule

module RS_RTUsed (
  input  OP0,
  input  OP1,
  input  OP2,
  input  OP3,
  input  OP4,
  input  OP5,
  input  F0,
  input  F1,
  input  F2,
  input  F3,
  input  F4,
  input  F5,
  output RsUsed,
  output RtUsed
);

  wire and_1_out, and_2_out, and_3_out, and_4_out, and_5_out, and_6_out, and_7_out, and_8_out, and_9_out,
       and_10_out, and_11_out, and_12_out, and_13_out, and_14_out, and_15_out, and_16_out, and_17_out,
       and_18_out, and_19_out, and_20_out, and_21_out, and_22_out, and_23_out, and_24_out, and_25_out,
       and_26_out, and_27_out, and_28_out, and_29_out, and_30_out, and_31_out, and_32_out, and_33_out,
       and_34_out, and_35_out, and_36_out, and_37_out, and_38_out, and_39_out, and_40_out, not_1_out,
       not_2_out, not_3_out, not_4_out, not_5_out, not_6_out, not_7_out, not_8_out, not_9_out, not_10_out,
       not_11_out, not_12_out, not_13_out, not_14_out, not_15_out, not_16_out, not_17_out, not_18_out,
       not_19_out, not_20_out, not_21_out, not_22_out, not_23_out, not_24_out, not_25_out, not_26_out,
       not_27_out, not_28_out, not_29_out, not_30_out, not_31_out, not_32_out, not_33_out, not_34_out,
       not_35_out, not_36_out, not_37_out, not_38_out, not_39_out, not_40_out, not_41_out, not_42_out,
       not_43_out, not_44_out, not_45_out, not_46_out, not_47_out, not_48_out, not_49_out, not_50_out,
       not_51_out, not_52_out, not_53_out, not_54_out, not_55_out, not_56_out, not_57_out, not_58_out,
       not_59_out, not_60_out, not_61_out, not_62_out, not_63_out, not_64_out, not_65_out, not_66_out,
       not_67_out, not_68_out, not_69_out, not_70_out, not_71_out, not_72_out, not_73_out, not_74_out,
       not_75_out, not_76_out, not_77_out, not_78_out, not_79_out, not_80_out, not_81_out, not_82_out,
       not_83_out, not_84_out, not_85_out, not_86_out, not_87_out, not_88_out, not_89_out, not_90_out,
       not_91_out, not_92_out, not_93_out, not_94_out, not_95_out, not_96_out, not_97_out, not_98_out,
       not_99_out, not_100_out, not_101_out, not_102_out, not_103_out, not_104_out, not_105_out, not_106_out,
       not_107_out, not_108_out, not_109_out, not_110_out, not_111_out, not_112_out, not_113_out,
       not_114_out, not_115_out, not_116_out, not_117_out, not_118_out, not_119_out, not_120_out,
       not_121_out, not_122_out, not_123_out, not_124_out, not_125_out, not_126_out, not_127_out,
       not_128_out, not_129_out, not_130_out, not_131_out, not_132_out, not_133_out, not_134_out,
       not_135_out, not_136_out, not_137_out, not_138_out, not_139_out, not_140_out, not_141_out,
       not_142_out, not_143_out, not_144_out, not_145_out, not_146_out, not_147_out, not_148_out,
       not_149_out, not_150_out, not_151_out, not_152_out, not_153_out, not_154_out, not_155_out,
       not_156_out, not_157_out, not_158_out, not_159_out, not_160_out, not_161_out, not_162_out,
       not_163_out, not_164_out, not_165_out, not_166_out, not_167_out, not_168_out, not_169_out,
       not_170_out, not_171_out, not_172_out, not_173_out, not_174_out, not_175_out, not_176_out,
       not_177_out, not_178_out, not_179_out, not_180_out, not_181_out, not_182_out, not_183_out,
       not_184_out, not_185_out, not_186_out, not_187_out, not_188_out, not_189_out, not_190_out,
       not_191_out, not_192_out, not_193_out, not_194_out, not_195_out, not_196_out, not_197_out,
       not_198_out, not_199_out, not_200_out, not_201_out, not_202_out, not_203_out, not_204_out,
       not_205_out, not_206_out, not_207_out, not_208_out, not_209_out, not_210_out, not_211_out,
       not_212_out, not_213_out, not_214_out, not_215_out, not_216_out, not_217_out, not_218_out,
       not_219_out, not_220_out, not_221_out, not_222_out, not_223_out, not_224_out, not_225_out,
       not_226_out, not_227_out, not_228_out, not_229_out, not_230_out, not_231_out, not_232_out,
       not_233_out, not_234_out, not_235_out, not_236_out, not_237_out, not_238_out, not_239_out,
       not_240_out, not_241_out, not_242_out, not_243_out, not_244_out, not_245_out, not_246_out,
       not_247_out, not_248_out, not_249_out, not_250_out, not_251_out, not_252_out, not_253_out,
       not_254_out, not_255_out, not_256_out, not_257_out, not_258_out, not_259_out, not_260_out,
       not_261_out, not_262_out, not_263_out, not_264_out, not_265_out, not_266_out, not_267_out,
       not_268_out, not_269_out, not_270_out, not_271_out, not_272_out, not_273_out, not_274_out,
       not_275_out, not_276_out, not_277_out, not_278_out, not_279_out, not_280_out, not_281_out,
       not_282_out, not_283_out, not_284_out, not_285_out, not_286_out, not_287_out, not_288_out,
       not_289_out, not_290_out, not_291_out, not_292_out, not_293_out, not_294_out, not_295_out;

  not not_1 (not_1_out, OP5);
  not not_2 (not_2_out, OP4);
  not not_3 (not_3_out, OP3);
  not not_4 (not_4_out, OP2);
  not not_5 (not_5_out, OP1);
  not not_6 (not_6_out, OP0);
  not not_7 (not_7_out, F4);
  not not_8 (not_8_out, F3);
  not not_9 (not_9_out, F2);
  not not_10 (not_10_out, F1);
  not not_11 (not_11_out, F0);
  not not_12 (not_12_out, OP5);
  not not_13 (not_13_out, OP4);
  not not_14 (not_14_out, OP3);
  not not_15 (not_15_out, OP2);
  not not_16 (not_16_out, OP1);
  not not_17 (not_17_out, OP0);
  not not_18 (not_18_out, F4);
  not not_19 (not_19_out, F3);
  not not_20 (not_20_out, F2);
  not not_21 (not_21_out, F1);
  not not_22 (not_22_out, OP5);
  not not_23 (not_23_out, OP4);
  not not_24 (not_24_out, OP3);
  not not_25 (not_25_out, OP2);
  not not_26 (not_26_out, OP1);
  not not_27 (not_27_out, OP0);
  not not_28 (not_28_out, F4);
  not not_29 (not_29_out, F3);
  not not_30 (not_30_out, F2);
  not not_31 (not_31_out, F0);
  not not_32 (not_32_out, OP5);
  not not_33 (not_33_out, OP4);
  not not_34 (not_34_out, OP3);
  not not_35 (not_35_out, OP2);
  not not_36 (not_36_out, OP1);
  not not_37 (not_37_out, OP0);
  not not_38 (not_38_out, F4);
  not not_39 (not_39_out, F3);
  not not_40 (not_40_out, F1);
  not not_41 (not_41_out, F0);
  not not_42 (not_42_out, OP5);
  not not_43 (not_43_out, OP4);
  not not_44 (not_44_out, OP3);
  not not_45 (not_45_out, OP2);
  not not_46 (not_46_out, OP1);
  not not_47 (not_47_out, OP0);
  not not_48 (not_48_out, F4);
  not not_49 (not_49_out, F3);
  not not_50 (not_50_out, F1);
  not not_51 (not_51_out, OP5);
  not not_52 (not_52_out, OP4);
  not not_53 (not_53_out, OP3);
  not not_54 (not_54_out, OP2);
  not not_55 (not_55_out, OP1);
  not not_56 (not_56_out, OP0);
  not not_57 (not_57_out, F4);
  not not_58 (not_58_out, F3);
  not not_59 (not_59_out, OP5);
  not not_60 (not_60_out, OP4);
  not not_61 (not_61_out, OP3);
  not not_62 (not_62_out, OP2);
  not not_63 (not_63_out, OP1);
  not not_64 (not_64_out, OP0);
  not not_65 (not_65_out, F4);
  not not_66 (not_66_out, F2);
  not not_67 (not_67_out, F0);
  not not_68 (not_68_out, OP5);
  not not_69 (not_69_out, OP4);
  not not_70 (not_70_out, OP3);
  not not_71 (not_71_out, OP2);
  not not_72 (not_72_out, OP1);
  not not_73 (not_73_out, OP0);
  not not_74 (not_74_out, F4);
  not not_75 (not_75_out, F2);
  not not_76 (not_76_out, OP5);
  not not_77 (not_77_out, OP4);
  not not_78 (not_78_out, OP3);
  not not_79 (not_79_out, OP2);
  not not_80 (not_80_out, OP1);
  not not_81 (not_81_out, OP0);
  not not_82 (not_82_out, F5);
  not not_83 (not_83_out, F4);
  not not_84 (not_84_out, F2);
  not not_85 (not_85_out, F1);
  not not_86 (not_86_out, F0);
  not not_87 (not_87_out, OP5);
  not not_88 (not_88_out, OP4);
  not not_89 (not_89_out, OP3);
  not not_90 (not_90_out, OP2);
  not not_91 (not_91_out, OP1);
  not not_92 (not_92_out, OP0);
  not not_93 (not_93_out, F5);
  not not_94 (not_94_out, F4);
  not not_95 (not_95_out, F1);
  not not_96 (not_96_out, F0);
  not not_97 (not_97_out, OP5);
  not not_98 (not_98_out, OP4);
  not not_99 (not_99_out, OP3);
  not not_100 (not_100_out, OP1);
  not not_101 (not_101_out, OP0);
  not not_102 (not_102_out, OP5);
  not not_103 (not_103_out, OP4);
  not not_104 (not_104_out, OP3);
  not not_105 (not_105_out, OP1);
  not not_106 (not_106_out, OP5);
  not not_107 (not_107_out, OP4);
  not not_108 (not_108_out, OP2);
  not not_109 (not_109_out, OP1);
  not not_110 (not_110_out, OP0);
  not not_111 (not_111_out, OP5);
  not not_112 (not_112_out, OP4);
  not not_113 (not_113_out, OP1);
  not not_114 (not_114_out, OP0);
  not not_115 (not_115_out, OP5);
  not not_116 (not_116_out, OP4);
  not not_117 (not_117_out, OP2);
  not not_118 (not_118_out, OP1);
  not not_119 (not_119_out, OP5);
  not not_120 (not_120_out, OP4);
  not not_121 (not_121_out, OP2);
  not not_122 (not_122_out, OP0);
  not not_123 (not_123_out, OP5);
  not not_124 (not_124_out, OP4);
  not not_125 (not_125_out, OP1);
  not not_126 (not_126_out, OP4);
  not not_127 (not_127_out, OP3);
  not not_128 (not_128_out, OP2);
  not not_129 (not_129_out, OP4);
  not not_130 (not_130_out, OP2);
  not not_131 (not_131_out, OP5);
  not not_132 (not_132_out, OP4);
  not not_133 (not_133_out, OP3);
  not not_134 (not_134_out, OP2);
  not not_135 (not_135_out, OP1);
  not not_136 (not_136_out, OP0);
  not not_137 (not_137_out, F5);
  not not_138 (not_138_out, F4);
  not not_139 (not_139_out, F3);
  not not_140 (not_140_out, F1);
  not not_141 (not_141_out, F0);
  not not_142 (not_142_out, OP5);
  not not_143 (not_143_out, OP4);
  not not_144 (not_144_out, OP0);
  not not_145 (not_145_out, OP5);
  not not_146 (not_146_out, OP4);
  not not_147 (not_147_out, OP3);
  not not_148 (not_148_out, OP4);
  not not_149 (not_149_out, OP2);
  not not_150 (not_150_out, OP1);
  not not_151 (not_151_out, OP0);
  not not_152 (not_152_out, OP5);
  not not_153 (not_153_out, OP4);
  not not_154 (not_154_out, OP3);
  not not_155 (not_155_out, OP2);
  not not_156 (not_156_out, OP1);
  not not_157 (not_157_out, OP0);
  not not_158 (not_158_out, F5);
  not not_159 (not_159_out, F4);
  not not_160 (not_160_out, F3);
  not not_161 (not_161_out, F2);
  not not_162 (not_162_out, F1);
  not not_163 (not_163_out, F0);
  not not_164 (not_164_out, OP5);
  not not_165 (not_165_out, OP4);
  not not_166 (not_166_out, OP3);
  not not_167 (not_167_out, OP2);
  not not_168 (not_168_out, OP1);
  not not_169 (not_169_out, OP0);
  not not_170 (not_170_out, F5);
  not not_171 (not_171_out, F4);
  not not_172 (not_172_out, F3);
  not not_173 (not_173_out, F2);
  not not_174 (not_174_out, OP5);
  not not_175 (not_175_out, OP4);
  not not_176 (not_176_out, OP3);
  not not_177 (not_177_out, OP2);
  not not_178 (not_178_out, OP1);
  not not_179 (not_179_out, OP0);
  not not_180 (not_180_out, F5);
  not not_181 (not_181_out, F4);
  not not_182 (not_182_out, F3);
  not not_183 (not_183_out, F2);
  not not_184 (not_184_out, F0);
  not not_185 (not_185_out, OP5);
  not not_186 (not_186_out, OP4);
  not not_187 (not_187_out, OP3);
  not not_188 (not_188_out, OP2);
  not not_189 (not_189_out, OP1);
  not not_190 (not_190_out, OP0);
  not not_191 (not_191_out, F4);
  not not_192 (not_192_out, F3);
  not not_193 (not_193_out, F2);
  not not_194 (not_194_out, F1);
  not not_195 (not_195_out, F0);
  not not_196 (not_196_out, OP5);
  not not_197 (not_197_out, OP4);
  not not_198 (not_198_out, OP3);
  not not_199 (not_199_out, OP2);
  not not_200 (not_200_out, OP1);
  not not_201 (not_201_out, OP0);
  not not_202 (not_202_out, F4);
  not not_203 (not_203_out, F3);
  not not_204 (not_204_out, F2);
  not not_205 (not_205_out, F1);
  not not_206 (not_206_out, OP5);
  not not_207 (not_207_out, OP4);
  not not_208 (not_208_out, OP3);
  not not_209 (not_209_out, OP2);
  not not_210 (not_210_out, OP1);
  not not_211 (not_211_out, OP0);
  not not_212 (not_212_out, F4);
  not not_213 (not_213_out, F3);
  not not_214 (not_214_out, F2);
  not not_215 (not_215_out, F0);
  not not_216 (not_216_out, OP5);
  not not_217 (not_217_out, OP4);
  not not_218 (not_218_out, OP3);
  not not_219 (not_219_out, OP2);
  not not_220 (not_220_out, OP1);
  not not_221 (not_221_out, OP0);
  not not_222 (not_222_out, F4);
  not not_223 (not_223_out, F3);
  not not_224 (not_224_out, F1);
  not not_225 (not_225_out, F0);
  not not_226 (not_226_out, OP5);
  not not_227 (not_227_out, OP4);
  not not_228 (not_228_out, OP3);
  not not_229 (not_229_out, OP2);
  not not_230 (not_230_out, OP1);
  not not_231 (not_231_out, OP0);
  not not_232 (not_232_out, F4);
  not not_233 (not_233_out, F3);
  not not_234 (not_234_out, F1);
  not not_235 (not_235_out, OP5);
  not not_236 (not_236_out, OP4);
  not not_237 (not_237_out, OP3);
  not not_238 (not_238_out, OP2);
  not not_239 (not_239_out, OP1);
  not not_240 (not_240_out, OP0);
  not not_241 (not_241_out, F4);
  not not_242 (not_242_out, F3);
  not not_243 (not_243_out, OP5);
  not not_244 (not_244_out, OP4);
  not not_245 (not_245_out, OP3);
  not not_246 (not_246_out, OP2);
  not not_247 (not_247_out, OP1);
  not not_248 (not_248_out, OP0);
  not not_249 (not_249_out, F4);
  not not_250 (not_250_out, F2);
  not not_251 (not_251_out, F0);
  not not_252 (not_252_out, OP5);
  not not_253 (not_253_out, OP4);
  not not_254 (not_254_out, OP3);
  not not_255 (not_255_out, OP2);
  not not_256 (not_256_out, OP1);
  not not_257 (not_257_out, OP0);
  not not_258 (not_258_out, F4);
  not not_259 (not_259_out, F2);
  not not_260 (not_260_out, OP5);
  not not_261 (not_261_out, OP4);
  not not_262 (not_262_out, OP3);
  not not_263 (not_263_out, OP2);
  not not_264 (not_264_out, OP1);
  not not_265 (not_265_out, OP0);
  not not_266 (not_266_out, F5);
  not not_267 (not_267_out, F4);
  not not_268 (not_268_out, F1);
  not not_269 (not_269_out, F0);
  not not_270 (not_270_out, OP5);
  not not_271 (not_271_out, OP4);
  not not_272 (not_272_out, OP3);
  not not_273 (not_273_out, OP1);
  not not_274 (not_274_out, OP0);
  not not_275 (not_275_out, OP5);
  not not_276 (not_276_out, OP4);
  not not_277 (not_277_out, OP3);
  not not_278 (not_278_out, OP1);
  not not_279 (not_279_out, OP4);
  not not_280 (not_280_out, OP2);
  not not_281 (not_281_out, OP5);
  not not_282 (not_282_out, OP4);
  not not_283 (not_283_out, OP3);
  not not_284 (not_284_out, OP2);
  not not_285 (not_285_out, OP1);
  not not_286 (not_286_out, OP0);
  not not_287 (not_287_out, F5);
  not not_288 (not_288_out, F4);
  not not_289 (not_289_out, F3);
  not not_290 (not_290_out, F1);
  not not_291 (not_291_out, F0);
  not not_292 (not_292_out, OP4);
  not not_293 (not_293_out, OP2);
  not not_294 (not_294_out, OP1);
  not not_295 (not_295_out, OP0);
  and and_1 (and_1_out, not_1_out, not_2_out, not_3_out, not_4_out, not_5_out, not_6_out, F5, not_7_out, not_8_out, not_9_out, not_10_out, not_11_out);
  and and_2 (and_2_out, not_12_out, not_13_out, not_14_out, not_15_out, not_16_out, not_17_out, F5, not_18_out, not_19_out, not_20_out, not_21_out, F0);
  and and_3 (and_3_out, not_22_out, not_23_out, not_24_out, not_25_out, not_26_out, not_27_out, F5, not_28_out, not_29_out, not_30_out, F1, not_31_out);
  and and_4 (and_4_out, not_32_out, not_33_out, not_34_out, not_35_out, not_36_out, not_37_out, F5, not_38_out, not_39_out, F2, not_40_out, not_41_out);
  and and_5 (and_5_out, not_42_out, not_43_out, not_44_out, not_45_out, not_46_out, not_47_out, F5, not_48_out, not_49_out, F2, not_50_out, F0);
  and and_6 (and_6_out, not_51_out, not_52_out, not_53_out, not_54_out, not_55_out, not_56_out, F5, not_57_out, not_58_out, F2, F1, F0);
  and and_7 (and_7_out, not_59_out, not_60_out, not_61_out, not_62_out, not_63_out, not_64_out, F5, not_65_out, F3, not_66_out, F1, not_67_out);
  and and_8 (and_8_out, not_68_out, not_69_out, not_70_out, not_71_out, not_72_out, not_73_out, F5, not_74_out, F3, not_75_out, F1, F0);
  and and_9 (and_9_out, not_76_out, not_77_out, not_78_out, not_79_out, not_80_out, not_81_out, not_82_out, not_83_out, F3, not_84_out, not_85_out, not_86_out);
  and and_10 (and_10_out, not_87_out, not_88_out, not_89_out, not_90_out, not_91_out, not_92_out, not_93_out, not_94_out, F3, F2, not_95_out, not_96_out);
  and and_11 (and_11_out, not_97_out, not_98_out, not_99_out, OP2, not_100_out, not_101_out);
  and and_12 (and_12_out, not_102_out, not_103_out, not_104_out, OP2, not_105_out, OP0);
  and and_13 (and_13_out, not_106_out, not_107_out, OP3, not_108_out, not_109_out, not_110_out);
  and and_14 (and_14_out, not_111_out, not_112_out, OP3, OP2, not_113_out, not_114_out);
  and and_15 (and_15_out, not_115_out, not_116_out, OP3, not_117_out, not_118_out, OP0);
  and and_16 (and_16_out, not_119_out, not_120_out, OP3, not_121_out, OP1, not_122_out);
  and and_17 (and_17_out, not_123_out, not_124_out, OP3, OP2, not_125_out, OP0);
  and and_18 (and_18_out, OP5, not_126_out, not_127_out, not_128_out, OP1, OP0);
  and and_19 (and_19_out, OP5, not_129_out, OP3, not_130_out, OP1, OP0);
  and and_20 (and_20_out, not_131_out, not_132_out, not_133_out, not_134_out, not_135_out, not_136_out, not_137_out, not_138_out, not_139_out, F2, not_140_out, not_141_out);
  and and_21 (and_21_out, not_142_out, not_143_out, OP3, OP2, OP1, not_144_out);
  and and_22 (and_22_out, not_145_out, not_146_out, not_147_out, OP2, OP1, OP0);
  and and_23 (and_23_out, OP5, not_148_out, OP3, not_149_out, not_150_out, not_151_out);
  and and_24 (and_24_out, not_152_out, not_153_out, not_154_out, not_155_out, not_156_out, not_157_out, not_158_out, not_159_out, not_160_out, not_161_out, not_162_out, not_163_out);
  and and_25 (and_25_out, not_164_out, not_165_out, not_166_out, not_167_out, not_168_out, not_169_out, not_170_out, not_171_out, not_172_out, not_173_out, F1, F0);
  and and_26 (and_26_out, not_174_out, not_175_out, not_176_out, not_177_out, not_178_out, not_179_out, not_180_out, not_181_out, not_182_out, not_183_out, F1, not_184_out);
  and and_27 (and_27_out, not_185_out, not_186_out, not_187_out, not_188_out, not_189_out, not_190_out, F5, not_191_out, not_192_out, not_193_out, not_194_out, not_195_out);
  and and_28 (and_28_out, not_196_out, not_197_out, not_198_out, not_199_out, not_200_out, not_201_out, F5, not_202_out, not_203_out, not_204_out, not_205_out, F0);
  and and_29 (and_29_out, not_206_out, not_207_out, not_208_out, not_209_out, not_210_out, not_211_out, F5, not_212_out, not_213_out, not_214_out, F1, not_215_out);
  and and_30 (and_30_out, not_216_out, not_217_out, not_218_out, not_219_out, not_220_out, not_221_out, F5, not_222_out, not_223_out, F2, not_224_out, not_225_out);
  and and_31 (and_31_out, not_226_out, not_227_out, not_228_out, not_229_out, not_230_out, not_231_out, F5, not_232_out, not_233_out, F2, not_234_out, F0);
  and and_32 (and_32_out, not_235_out, not_236_out, not_237_out, not_238_out, not_239_out, not_240_out, F5, not_241_out, not_242_out, F2, F1, F0);
  and and_33 (and_33_out, not_243_out, not_244_out, not_245_out, not_246_out, not_247_out, not_248_out, F5, not_249_out, F3, not_250_out, F1, not_251_out);
  and and_34 (and_34_out, not_252_out, not_253_out, not_254_out, not_255_out, not_256_out, not_257_out, F5, not_258_out, F3, not_259_out, F1, F0);
  and and_35 (and_35_out, not_260_out, not_261_out, not_262_out, not_263_out, not_264_out, not_265_out, not_266_out, not_267_out, F3, F2, not_268_out, not_269_out);
  and and_36 (and_36_out, not_270_out, not_271_out, not_272_out, OP2, not_273_out, not_274_out);
  and and_37 (and_37_out, not_275_out, not_276_out, not_277_out, OP2, not_278_out, OP0);
  and and_38 (and_38_out, OP5, not_279_out, OP3, not_280_out, OP1, OP0);
  and and_39 (and_39_out, not_281_out, not_282_out, not_283_out, not_284_out, not_285_out, not_286_out, not_287_out, not_288_out, not_289_out, F2, not_290_out, not_291_out);
  and and_40 (and_40_out, OP5, not_292_out, OP3, not_293_out, not_294_out, not_295_out);
  or or_1 (RsUsed, and_1_out, and_2_out, and_3_out, and_4_out, and_5_out, and_6_out, and_7_out, and_8_out, and_9_out, and_10_out, and_11_out, and_12_out, and_13_out, and_14_out, and_15_out, and_16_out, and_17_out, and_18_out, and_19_out, and_20_out, and_21_out, and_22_out, and_23_out);
  or or_2 (RtUsed, and_24_out, and_25_out, and_26_out, and_27_out, and_28_out, and_29_out, and_30_out, and_31_out, and_32_out, and_33_out, and_34_out, and_35_out, and_36_out, and_37_out, and_38_out, and_39_out, and_40_out);
endmodule

module \重定向相关处理逻辑  (
  input  [31:0] Instr,
  input  BranchTaken,
  input  MemRead,
  input  [4:0] EX_W_num,
  input  EX_RegWrite,
  input  MEM_RegWrite,
  input  [4:0] MEM_W_num,
  output stall,
  output flush,
  output [1:0] RS_F,
  output [1:0] RT_F
);

  wire and_1_out, and_2_out, comparator_2_eq, comparator_3_eq, comparator_4_eq, comparator_5_eq,
       comparator_6_eq, comparator_7_eq, Instr_sys, not_1_out, not_2_out, rs_rtused_1_rsused,
       rs_rtused_1_rtused;
  wire [1:0] and_4_out, and_6_out;
  wire [4:0] multiplexer_1_out, multiplexer_2_out;

  Multiplexer #(.select(1), .width(5), .disabled("Z"), .enable("false")) multiplexer_1 (
    .in0(Instr[25:21]), .in1(5'b00010), .out(multiplexer_1_out), .sel(Instr_sys));
  Multiplexer #(.select(1), .width(5), .disabled("Z"), .enable("false")) multiplexer_2 (
    .in0(Instr[20:16]), .in1(5'b00100), .out(multiplexer_2_out), .sel(Instr_sys));
  Comparator #(.width(32), .mode("twosComplement")) comparator_1 (
    .a(Instr), .b(32'hc), .eq(Instr_sys));  // open: gt, lt
  RS_RTUsed rs_rtused_1 (
    .OP0(Instr[26]), .OP1(Instr[27]), .OP2(Instr[28]), .OP3(Instr[29]), .OP4(Instr[30]), .OP5(Instr[31]),
    .F0(Instr[0]), .F1(Instr[1]), .F2(Instr[2]), .F3(Instr[3]), .F4(Instr[4]), .F5(Instr[5]),
    .RsUsed(rs_rtused_1_rsused), .RtUsed(rs_rtused_1_rtused));
  not not_1 (not_1_out, comparator_2_eq);
  Comparator #(.width(5), .mode("twosComplement")) comparator_2 (
    .a(multiplexer_1_out), .b({5{1'b0}}), .eq(comparator_2_eq));  // open: gt, lt
  Comparator #(.width(5), .mode("twosComplement")) comparator_3 (
    .a({5{1'b0}}), .b(multiplexer_2_out), .eq(comparator_3_eq));  // open: gt, lt
  not not_2 (not_2_out, comparator_3_eq);
  Comparator #(.width(5), .mode("twosComplement")) comparator_4 (
    .a(multiplexer_1_out), .b(EX_W_num), .eq(comparator_4_eq));  // open: gt, lt
  Comparator #(.width(5), .mode("twosComplement")) comparator_5 (
    .a(EX_W_num), .b(multiplexer_2_out), .eq(comparator_5_eq));  // open: gt, lt
  Comparator #(.width(5), .mode("twosComplement")) comparator_6 (
    .a(multiplexer_1_out), .b(MEM_W_num), .eq(comparator_6_eq));  // open: gt, lt
  Comparator #(.width(5), .mode("twosComplement")) comparator_7 (
    .a(MEM_W_num), .b(multiplexer_2_out), .eq(comparator_7_eq));  // open: gt, lt
  and and_1 (and_1_out, rs_rtused_1_rsused, not_1_out, MemRead, comparator_4_eq);
  and and_2 (and_2_out, rs_rtused_1_rtused, not_2_out, MemRead, comparator_5_eq);
  and and_3 (and_4_out[1], rs_rtused_1_rsused, not_1_out, EX_RegWrite, comparator_4_eq);
  and and_4 (and_4_out[0], rs_rtused_1_rsused, not_1_out, MEM_RegWrite, comparator_6_eq);
  and and_5 (and_6_out[1], rs_rtused_1_rtused, not_2_out, EX_RegWrite, comparator_5_eq);
  and and_6 (and_6_out[0], rs_rtused_1_rtused, not_2_out, MEM_RegWrite, comparator_7_eq);
  Multiplexer #(.select(2), .width(2), .disabled("Z"), .enable("false")) multiplexer_3 (
    .in0(2'b00), .in1(2'b01), .in2(2'b10), .in3(2'b10), .out(RS_F), .sel(and_4_out));
  Multiplexer #(.select(2), .width(2), .disabled("Z"), .enable("false")) multiplexer_4 (
    .in0(2'b00), .in1(2'b01), .in2(2'b10), .in3(2'b10), .out(RT_F), .sel(and_6_out));
  or or_1 (stall, and_1_out, and_2_out);
  or or_2 (flush, stall, BranchTaken);

  // Notes on the sheet:
  //   rs
  //   rt
  //   OP
  //   FUNCT
  //   Rt_Used
  //   rt≠0
  //   Rs_Used
  //   rs≠0
  //   LoadUse
  //   RSFoward
  //   RTFoward
endmodule

module \中断按键  (
  input  clk,
  input  \中断源 ,
  input  \同步清零信号 ,
  output \与中断屏蔽位与 ,
  output \中断等待信号 
);

  wire and_1_out, d_ff_1_q, or_2_out;

  or or_1 (\中断等待信号 , \与中断屏蔽位与 , d_ff_1_q);
  D_Flip_Flop #(.trigger("rising"), .Pre_Clr_Positions("LEGACY"), .NegatePresetClear("false"), .enable("true"), .NewFFLayout("false")) d_ff_1 (
    .clk(\中断源 ), .D(1'b1), .Q(d_ff_1_q), .reset(\与中断屏蔽位与 ));  // open: Qn, preset, en
  or or_2 (or_2_out, d_ff_1_q, \与中断屏蔽位与 );
  and and_1 (and_1_out, or_2_out, ~\同步清零信号 );  // AND_Gate
  D_Flip_Flop #(.trigger("rising"), .Pre_Clr_Positions("LEGACY"), .NegatePresetClear("false"), .enable("true"), .NewFFLayout("false")) IR1 (
    .clk(clk), .D(and_1_out), .Q(\与中断屏蔽位与 ));  // open: Qn, preset, en, reset

  // Notes on the sheet:
  //   中断信号采样参考电路
  //   Reset 
endmodule

module fall_regfile (
  input  [31:0] Din,
  input  Clk,
  input  WE,
  input  [4:0] R1_num,
  input  [4:0] W_num,
  input  [4:0] R2_num,
  output [31:0] R1,
  output [31:0] R2
);

  // RegisterFile registerfile_1: pin names not known; wires that end beside it: Din, Clk, WE, W_num, R1_num, R2_num, R1, R2
endmodule

module \分支预测  (
  output RegWrite,
  output MemWrite,
  output [31:0] IF_PC,
  output [31:0] ID_PC,
  output [31:0] EX_PC,
  output [31:0] M_PC,
  output [31:0] WB_PC,
  output [31:0] RDin,
  output [31:0] MDin,
  output [31:0] LedData
);

  wire and_1_out, and_2_out, and_3_out, and_4_out, and_5_out, and_7_out, Beq, BGTZ, Bne, Branch, BranchTaken,
       CLK, clock_1_out, clock_2_out, comparator_1_gt, comparator_2_eq, comparator_2_lt, comparator_3_eq, En,
       Equal, ex_mem_1_jal_2, ex_mem_1_memtoreg_2, ex_mem_1_syscall_2, EX_PredictJump, EX_RegWrite, flush,
       Go, h_en, Halt, id_ex_1_alusrcb_2, id_ex_1_jal_2, id_ex_1_memwrite_2, id_ex_1_sb_2, id_ex_1_syscall_2,
       if_id_1_predictjump_2, IR1, IR2, IR3, JAL, JMP, JR, MEM_RegWrite, MemRead, MemToReg, mips_probe_5_p3,
       nand_1_out, not_1_out, not_2_out, not_3_out, not_4_out, PredictErr, PredictJump, RegDst, RST, SB,
       SignedExt, SLLV, stall, Syscall, W1, W2, W3, \单周期硬布线控制器_1_alu_src , \单周期硬布线控制器_1_beq ,
       \单周期硬布线控制器_1_bgtz , \单周期硬布线控制器_1_bne , \单周期硬布线控制器_1_jal , \单周期硬布线控制器_1_jmp , \单周期硬布线控制器_1_jr ,
       \单周期硬布线控制器_1_memtoreg , \单周期硬布线控制器_1_memwrite , \单周期硬布线控制器_1_regwrite , \单周期硬布线控制器_1_sb ,
       \单周期硬布线控制器_1_signedext , \单周期硬布线控制器_1_sllv , \单周期硬布线控制器_1_syscall ;
  wire [0:0] or_4_out;
  wire [1:0] id_ex_1_rs_f_2, id_ex_1_rt_f_2, RS_F, RT_F;
  wire [3:0] id_ex_1_aluop_2, \单周期硬布线控制器_1_alu_op ;
  wire [4:0] EX_W_num, MEM_W_num, mem_wb_1_writereg_num_2, multiplexer_4_out, multiplexer_6_out,
       multiplexer_7_out, multiplexer_12_out, W_num;
  wire [12:0] CNT_num;
  wire [15:0] \LoadUse次数 , \总周期数 , \插入气泡数 , \无条件分支数 , \条件分支成功数 ;
  wire [31:0] A0, adder_1_out, adder_3_out, ALUresult, BAddr, bit_extender_1_out, bit_extender_2_out,
       BranchAddr, btb_1_jumpaddr, EX_IR, ex_mem_1_r1_2, EX_PC_4, fall_regfile_1_r1, fall_regfile_1_r2,
       GPRrs, GPRrt, id_ex_1_rs_2, id_ex_1_rt_2, ID_IR, if_id_1_pc_4_2, IF_IR, MEM_IR, mem_wb_1_memdata_2,
       mem_wb_1_result_2, mips_alu_1_result, multiplexer_1_out, multiplexer_2_out, multiplexer_3_out,
       multiplexer_9_out, multiplexer_10_out, multiplexer_11_out, multiplexer_14_out, ram_1_data,
       shifter_1_out, V0, WB_IR, \按字节存储电路_1_ddata ;

  Button \u_总复位  (.out(RST));
  Button _1 (.out(IR1));
  Button _2 (.out(IR2));
  Button _3 (.out(IR3));
  // Probe on \总周期数 
  // Probe on \总周期数 
  Button \u_继续运行  (.out(Go));
  LED #(.active("true")) led_1 (.in(W1));
  LED #(.active("true")) led_2 (.in(W2));
  LED #(.active("true")) led_3 (.in(W3));
  not not_1 (not_1_out, Halt);
  not not_2 (not_2_out, stall);
  Counter #(.width(16), .max('hffff), .ongoal("wrap"), .trigger("rising"), .behavior("new")) counter_1 (
    .count(JMP), .Q(\无条件分支数 ), .clk(CLK), .clr(RST));  // open: load, D, carry, preset, down
  Hex_Digit_Display hex_digit_display_1 (.value(LedData[31:28]));  // open: dp
  // Probe on IF_PC[19:0]
  // Mips_Probe mips_probe_1: pin names not known; wires that end beside it: IF_IR
  and and_1 (and_1_out, not_1_out, not_2_out);
  Hex_Digit_Display hex_digit_display_2 (.value(LedData[27:24]));  // open: dp
  Hex_Digit_Display hex_digit_display_3 (.value(LedData[23:20]));  // open: dp
  // Probe on ID_PC[19:0]
  // Mips_Probe mips_probe_2: pin names not known; wires that end beside it: ID_IR
  or or_1 (En, and_1_out, Go);
  Hex_Digit_Display hex_digit_display_4 (.value(LedData[15:12]));  // open: dp
  Hex_Digit_Display hex_digit_display_5 (.value(LedData[19:16]));  // open: dp
  // Probe on multiplexer_3_out
  Hex_Digit_Display hex_digit_display_6 (.value(LedData[11:8]));  // open: dp
  Hex_Digit_Display hex_digit_display_7 (.value(LedData[7:4]));  // open: dp
  Clock #(.highDuration(1), .lowDuration(1)) clock_1 (.out(clock_1_out));
  // Probe on EX_PC[19:0]
  // Mips_Probe mips_probe_3: pin names not known; wires that end beside it: clock_1_out, EX_IR, CLK
  and and_2 (and_2_out, BranchTaken, ~JMP);  // AND_Gate
  Counter #(.width(16), .max('hffff), .ongoal("wrap"), .trigger("rising"), .behavior("new")) counter_2 (
    .count(and_2_out), .Q(\条件分支成功数 ), .clk(CLK), .clr(RST));  // open: load, D, carry, preset, down
  Multiplexer #(.select(1), .width(32), .disabled("Z"), .enable("false")) multiplexer_1 (
    .in0(multiplexer_2_out), .in1(multiplexer_3_out), .out(multiplexer_1_out), .sel(PredictErr));
  Multiplexer #(.select(1), .width(32), .disabled("Z"), .enable("false")) multiplexer_2 (
    .in0(adder_1_out), .in1(btb_1_jumpaddr), .out(multiplexer_2_out), .sel(PredictJump));
  Multiplexer #(.select(1), .width(32), .disabled("Z"), .enable("false")) multiplexer_3 (
    .in0(EX_PC_4), .in1(BranchAddr), .out(multiplexer_3_out), .sel(BranchTaken));
  and and_3 (and_3_out, Beq, Equal);
  and and_4 (and_4_out, ~Equal, Bne);  // AND_Gate
  Comparator #(.width(32), .mode("twosComplement")) comparator_1 (
    .a(GPRrs), .b({32{1'b0}}), .gt(comparator_1_gt));  // open: eq, lt
  and and_5 (and_5_out, comparator_1_gt, BGTZ);
  Hex_Digit_Display hex_digit_display_8 (.value(LedData[3:0]));  // open: dp
  Register #(.width(32), .trigger("rising"), .Select("low")) PC (
    .D(multiplexer_1_out), .en(En), .Q(IF_PC), .clk(CLK), .clr(RST));
  BTB btb_1 (
    .PC(IF_PC), .EX_PC(EX_PC), .JumpAddr(btb_1_jumpaddr), .EX_BranchAddr(BranchAddr),
    .PredictJump(PredictJump), .clk(CLK), .EX_Branch(Branch), .EX_BranchTaken(BranchTaken));
  or or_2 (Branch, Bne, Beq, BGTZ, JMP);
  // Probe on \总周期数 
  // Probe on M_PC[19:0]
  // Mips_Probe mips_probe_4: pin names not known; wires that end beside it: MEM_IR
  not not_3 (not_3_out, Halt);
  Counter #(.width(16), .max('hffff), .ongoal("wrap"), .trigger("rising"), .behavior("new")) counter_3 (
    .count(not_3_out), .Q(\总周期数 ), .clk(CLK), .clr(RST));  // open: load, D, carry, preset, down
  or or_3 (BranchTaken, and_3_out, and_4_out, and_5_out, JMP);
  // Probe on \总周期数 
  // Probe on \无条件分支数 
  // Probe on \条件分支成功数 
  // Probe on \插入气泡数 
  // Probe on \LoadUse次数 
  // Probe on IF_PC[11:0]
  // Probe on WB_PC[19:0]
  // Mips_Probe mips_probe_5: pin names not known; wires that end beside it: stall, WB_IR, mips_probe_5_p3
  Counter #(.width(16), .max('hffff), .ongoal("wrap"), .trigger("rising"), .behavior("new")) counter_4 (
    .count(stall), .Q(\插入气泡数 ), .clk(CLK), .clr(RST));  // open: load, D, carry, preset, down
  ROM #(.addrWidth(10), .dataWidth(32), .Select("high")) rom_1 (.addr(IF_PC[11:2]), .data(IF_IR));
  Adder #(.width(32)) adder_1 (.a(IF_PC), .b(32'h4), .out(adder_1_out), .cin(1'b0));  // open: cout
  // Probe on adder_1_out
  // Probe on ID_PC[11:0]
  // Probe on EX_PC[11:0]
  IF_ID if_id_1 (
    .PC(IF_PC), .IR(IF_IR), .PC_4(adder_1_out), .PC_2(ID_PC), .IR_2(ID_IR), .PC_4_2(if_id_1_pc_4_2),
    .Clk(CLK), .\异步清0 (RST), .EN(En), .PredictJump_2(if_id_1_predictjump_2), .\同步清0 (PredictErr),
    .PredictJump(PredictJump));
  // Probe on M_PC[11:0]
  D_Flip_Flop #(.trigger("high"), .Pre_Clr_Positions("LEGACY"), .NegatePresetClear("false"), .enable("true"), .NewFFLayout("false")) d_ff_1 (.Q(mips_probe_5_p3));  // open: clk, D, Qn, preset, en, reset
  // Probe on 13'h300
  // Mips_Probe mips_probe_6: pin names not known; wires that end beside it: ID_IR
  // Probe on WB_PC[11:0]
  Comparator #(.width(13), .mode("twosComplement")) comparator_2 (
    .a(CNT_num), .b(13'h300), .eq(comparator_2_eq), .lt(comparator_2_lt));  // open: gt
  Clock #(.highDuration(1), .lowDuration(1)) clock_2 (.out(clock_2_out));
  nand nand_1 (nand_1_out, mips_probe_5_p3, comparator_2_eq);
  Counter #(.width(13), .max('h1fff), .ongoal("stay"), .trigger("rising"), .behavior("old")) counter_5 (
    .count(comparator_2_lt), .Q(CNT_num), .clk(clock_2_out));  // open: load, D, carry, clr, preset
  Counter #(.width(16), .max('hffff), .ongoal("wrap"), .trigger("rising"), .behavior("new")) counter_6 (
    .count(stall), .Q(\LoadUse次数 ), .clk(CLK), .clr(RST));  // open: load, D, carry, preset, down
  Multiplexer #(.select(1), .width(5), .disabled("Z"), .enable("false")) multiplexer_4 (
    .in0(ID_IR[20:16]), .in1(ID_IR[15:11]), .out(multiplexer_4_out), .sel(RegDst));
  Multiplexer #(.select(3), .width(32), .disabled("Z"), .enable("false")) multiplexer_5 (
    .in1(BAddr), .in2({EX_PC_4[31:28], EX_IR[25:0], 2'b00}), .in6(GPRrs), .out(BranchAddr),
    .sel({JR, JMP, or_4_out[0]}));  // open: in0, in3, in4, in5, in7
  or or_4 (or_4_out[0], Bne, Beq);
  assign CLK = nand_1_out ? clock_2_out : 1'bz;  // Controlled_Buffer controlled_buffer_1
  Multiplexer #(.select(1), .width(5), .disabled("Z"), .enable("false")) multiplexer_6 (
    .in0(ID_IR[25:21]), .in1(5'b00010), .out(multiplexer_6_out), .sel(\单周期硬布线控制器_1_syscall ));
  Multiplexer #(.select(1), .width(5), .disabled("Z"), .enable("false")) multiplexer_7 (
    .in0(ID_IR[20:16]), .in1(5'b00100), .out(multiplexer_7_out), .sel(\单周期硬布线控制器_1_syscall ));
  Pull_Resistor #(.pull(1)) pull_resistor_1 (.node(CLK));
  \单周期硬布线控制器  \u_单周期硬布线控制器_1  (
    .Func(ID_IR[5:0]), .OP(ID_IR[31:26]), .ALU_OP(\单周期硬布线控制器_1_alu_op ), .MemToReg(\单周期硬布线控制器_1_memtoreg ),
    .MemWrite(\单周期硬布线控制器_1_memwrite ), .ALU_SRC(\单周期硬布线控制器_1_alu_src ), .RegWrite(\单周期硬布线控制器_1_regwrite ),
    .SysCALL(\单周期硬布线控制器_1_syscall ), .SignedExt(\单周期硬布线控制器_1_signedext ), .RegDst(RegDst),
    .JR(\单周期硬布线控制器_1_jr ), .JMP(\单周期硬布线控制器_1_jmp ), .Beq(\单周期硬布线控制器_1_beq ), .JAL(\单周期硬布线控制器_1_jal ),
    .Bne(\单周期硬布线控制器_1_bne ), .SB(\单周期硬布线控制器_1_sb ), .BGTZ(\单周期硬布线控制器_1_bgtz ), .SLLV(\单周期硬布线控制器_1_sllv ));
  fall_regfile fall_regfile_1 (
    .Din(RDin), .Clk(CLK), .R1(fall_regfile_1_r1), .R2(fall_regfile_1_r2), .WE(RegWrite), .W_num(W_num),
    .R1_num(multiplexer_6_out), .R2_num(multiplexer_7_out));
  not not_4 (not_4_out, Halt);
  or or_5 (h_en, not_4_out, Go);
  ID_EX id_ex_1 (
    .JMP(\单周期硬布线控制器_1_jmp ), .JR(\单周期硬布线控制器_1_jr ), .SignEXt(\单周期硬布线控制器_1_signedext ),
    .Beq(\单周期硬布线控制器_1_beq ), .Bne(\单周期硬布线控制器_1_bne ), .MemToReg(\单周期硬布线控制器_1_memtoreg ),
    .MemWrite(\单周期硬布线控制器_1_memwrite ), .AluOP(\单周期硬布线控制器_1_alu_op ), .AluSrcB(\单周期硬布线控制器_1_alu_src ),
    .RegWrite(\单周期硬布线控制器_1_regwrite ), .PC(ID_PC), .IR(ID_IR), .RS(fall_regfile_1_r1),
    .RT(fall_regfile_1_r2), .WriteReg_num(multiplexer_4_out), .PC_4(if_id_1_pc_4_2), .JMP_2(JMP), .JR_2(JR),
    .SignEXt_2(SignedExt), .Beq_2(Beq), .Bne_2(Bne), .MemToReg_2(MemRead), .MemWrite_2(id_ex_1_memwrite_2),
    .AluOP_2(id_ex_1_aluop_2), .AluSrcB_2(id_ex_1_alusrcb_2), .RegWrite_2(EX_RegWrite), .PC_2(EX_PC),
    .IR_2(EX_IR), .RS_2(id_ex_1_rs_2), .RT_2(id_ex_1_rt_2), .WriteReg_num_2(EX_W_num), .PC_4_2(EX_PC_4),
    .Clk(CLK), .\异步清0 (RST), .JAL(\单周期硬布线控制器_1_jal ), .JAL_2(id_ex_1_jal_2), .EN(h_en),
    .RT_F_2(id_ex_1_rt_f_2), .RT_F(RT_F), .\同步清0 (flush), .RS_F_2(id_ex_1_rs_f_2), .RS_F(RS_F),
    .BGTZ(\单周期硬布线控制器_1_bgtz ), .BGTZ_2(BGTZ), .SLLV(\单周期硬布线控制器_1_sllv ), .SLLV_2(SLLV),
    .SB(\单周期硬布线控制器_1_sb ), .SB_2(id_ex_1_sb_2), .syscall(\单周期硬布线控制器_1_syscall ),
    .syscall_2(id_ex_1_syscall_2), .PredictJump(if_id_1_predictjump_2), .PredictJump_2(EX_PredictJump));
  xor xor_1 (PredictErr, EX_PredictJump, BranchTaken);
  assign bit_extender_1_out = {{16{1'b0}}, EX_IR[15:0]};  // Bit_Extender bit_extender_1
  assign bit_extender_2_out = {{16{EX_IR[15]}}, EX_IR[15:0]};  // Bit_Extender bit_extender_2
  Multiplexer #(.select(2), .width(32), .disabled("Z"), .enable("false")) multiplexer_8 (
    .in0(id_ex_1_rs_2), .in1(RDin), .in2(ALUresult), .out(GPRrs), .sel(id_ex_1_rs_f_2));  // open: in3
  Multiplexer #(.select(2), .width(32), .disabled("Z"), .enable("false")) multiplexer_9 (
    .in0(id_ex_1_rt_2), .in1(RDin), .in2(ALUresult), .out(multiplexer_9_out), .sel(id_ex_1_rt_f_2));  // open: in3
  Multiplexer #(.select(1), .width(32), .disabled("Z"), .enable("false")) multiplexer_10 (
    .in0(bit_extender_1_out), .in1(bit_extender_2_out), .out(multiplexer_10_out), .sel(SignedExt));
  \重定向相关处理逻辑  \u_重定向相关处理逻辑_1  (
    .Instr(ID_IR), .BranchTaken(PredictErr), .MemRead(MemRead), .EX_W_num(EX_W_num),
    .EX_RegWrite(EX_RegWrite), .MEM_RegWrite(MEM_RegWrite), .MEM_W_num(MEM_W_num), .stall(stall),
    .flush(flush), .RS_F(RS_F), .RT_F(RT_F));
  Shifter #(.width(32), .shift("ll")) shifter_1 (.in(bit_extender_2_out), .\dist (5'b00010), .out(shifter_1_out));
  Multiplexer #(.select(1), .width(32), .disabled("Z"), .enable("false")) multiplexer_11 (
    .in0(multiplexer_9_out), .in1(multiplexer_10_out), .out(multiplexer_11_out), .sel(id_ex_1_alusrcb_2));
  Adder #(.width(32)) adder_2 (.a(shifter_1_out), .b(EX_PC_4), .out(BAddr), .cin(1'b0));  // open: cout
  MIPS_ALU mips_alu_1 (
    .X(GPRrs), .Y(multiplexer_11_out), .AluOP(id_ex_1_aluop_2), .Equal(Equal), .Result(mips_alu_1_result),
    .shamt(multiplexer_12_out));  // open: Result_2
  Multiplexer #(.select(1), .width(5), .disabled("Z"), .enable("false")) multiplexer_12 (
    .in0(EX_IR[10:6]), .in1(GPRrs[4:0]), .out(multiplexer_12_out), .sel(SLLV));
  Comparator #(.width(32), .mode("twosComplement")) comparator_3 (
    .a(V0), .b(32'ha), .eq(comparator_3_eq));  // open: gt, lt
  EX_MEM ex_mem_1 (
    .MemToReg(MemRead), .RegWrite(EX_RegWrite), .PC(EX_PC), .IR(EX_IR), .Result(mips_alu_1_result),
    .Writedata(multiplexer_9_out), .WriteReg_num(EX_W_num), .MemToReg_2(ex_mem_1_memtoreg_2),
    .RegWrite_2(MEM_RegWrite), .PC_2(M_PC), .IR_2(MEM_IR), .Result_2(ALUresult), .Writedata_2(GPRrt),
    .WriteReg_num_2(MEM_W_num), .Clk(CLK), .Rst(RST), .MemWrite_2(MemWrite), .MemWrite(id_ex_1_memwrite_2),
    .JAL(id_ex_1_jal_2), .JAL_2(ex_mem_1_jal_2), .EN(h_en), .R1_2(ex_mem_1_r1_2), .R1(GPRrs),
    .syscall_2(ex_mem_1_syscall_2), .syscall(id_ex_1_syscall_2), .SB(id_ex_1_sb_2), .SB_2(SB));  // open: JMP, JR, JMP_2, JR_2, 同步清0
  and and_6 (Halt, Syscall, comparator_3_eq);
  and and_7 (and_7_out, ~comparator_3_eq, Syscall);  // AND_Gate
  Register #(.width(32), .trigger("rising"), .Select("low")) register_1 (
    .D(A0), .en(and_7_out), .Q(LedData), .clk(CLK));  // open: clr
  RAM #(.addrWidth(10), .dataWidth(32), .bus("separate"), .Select("high")) ram_1 (
    .addr(ALUresult[11:2]), .din(MDin), .data(ram_1_data), .str(MemWrite), .clk(CLK), .ld(1'b1), .clr(RST));  // open: sel
  \按字节存储电路  \u_按字节存储电路_1  (.cdata(GPRrt), .sel(ALUresult), .sdata(ram_1_data), .ddata(\按字节存储电路_1_ddata ));
  MEM_WB mem_wb_1 (
    .MemToReg(ex_mem_1_memtoreg_2), .RegWrite(MEM_RegWrite), .PC(M_PC), .IR(MEM_IR), .Result(ALUresult),
    .Memdata(ram_1_data), .WriteReg_num(MEM_W_num), .MemToReg_2(MemToReg), .RegWrite_2(RegWrite),
    .PC_2(WB_PC), .IR_2(WB_IR), .Result_2(mem_wb_1_result_2), .Memdata_2(mem_wb_1_memdata_2),
    .WriteReg_num_2(mem_wb_1_writereg_num_2), .Clk(CLK), .Rst(RST), .JAL(ex_mem_1_jal_2), .JAL_2(JAL),
    .R1_2(V0), .R1(ex_mem_1_r1_2), .En(h_en), .syscall_2(Syscall), .syscall(ex_mem_1_syscall_2), .R1_3(A0),
    .R2(GPRrt));  // open: JMP_2, JR_2, JMP, JR, 同步清0
  Multiplexer #(.select(1), .width(32), .disabled("Z"), .enable("false")) multiplexer_13 (
    .in0(GPRrt), .in1(\按字节存储电路_1_ddata ), .out(MDin), .sel(SB));
  Multiplexer #(.select(1), .width(32), .disabled("Z"), .enable("false")) multiplexer_14 (
    .in0(mem_wb_1_result_2), .in1(mem_wb_1_memdata_2), .out(multiplexer_14_out), .sel(MemToReg));
  Multiplexer #(.select(1), .width(5), .disabled("Z"), .enable("false")) multiplexer_15 (
    .in0(mem_wb_1_writereg_num_2), .in1({5{1'b1}}), .out(W_num), .sel(JAL));
  // Probe on W_num
  Adder #(.width(32)) adder_3 (.a(WB_PC), .b(32'h4), .out(adder_3_out), .cin(1'b0));  // open: cout
  Multiplexer #(.select(1), .width(32), .disabled("Z"), .enable("false")) multiplexer_16 (
    .in0(multiplexer_14_out), .in1(adder_3_out), .out(RDin), .sel(JAL));
  // Probe on RDin

  // Other names for the same wires on the sheet: JMPAddr[31:2] = {EX_PC_4[31:28], EX_IR[25:0]};
  //   shamt[4:0] = EX_IR[10:6]; MEM_PC[31:0] = M_PC; PC[31:0] = IF_PC

  // Notes on the sheet:
  //   中断源
  //   时空图监测，可删除
  //   中断等待指示
  //   数码管输出
  //   指令存储器
  //   contents of rom_1 (hex, n*v repeats v):
  //   20110001 8000c05 20110001 20120002 20130003 8000c09 20110001 20120002 20130003 8000c0d 20110001
  //   20120002 20130003 8000c11 20110001 20120002 20130003 c000cf5 20100001 20110001 118fc0 112020
  //   20020022 c 118882 12200001 8000c15 112020 20020022 c 20110001 118880 112020 20020022 c 12200001
  //   8000c1f 20110001 118fc0 112020 20020022 c 1188c3 112020 20020022 c 118903 112020 20020022 c 118903
  //   112020 20020022 c 118903 112020 20020022 c 118903 112020 20020022 c 118903 112020 20020022 c 118903
  //   112020 20020022 c 118903 112020 20020022 c 20100001 109fc0 139fc3 8021 2012000c 24160003 26100001
  //   3210000f 20080008 20090001 139900 2709825 132020 20020022 c 1094022 1500fff9 22100001 2018000f
  //   2188024 108700 20080008 20090001 139902 2709825 132021 20020022 c 1094022 1500fff9 108702 2c9b022
  //   12c00001 8000c50 4020 1084027 84400 3508ffff 82021 20020022 c 2010ffff 20110000 ae300000 22100001
  //   22310004 ae300000 22100001 22310004 ae300000 22100001 22310004 ae300000 22100001 22310004 ae300000
  //   22100001 22310004 ae300000 22100001 22310004 ae300000 22100001 22310004 ae300000 22100001 22310004
  //   ae300000 22100001 22310004 ae300000 22100001 22310004 ae300000 22100001 22310004 ae300000 22100001
  //   22310004 ae300000 22100001 22310004 ae300000 22100001 22310004 ae300000 22100001 22310004 ae300000
  //   22100001 22310004 22100001 8020 2011003c 8e130000 8e340000 274402a 11000002 ae330000 ae140000
  //   2231fffc 1611fff8 102020 20020022 c 22100004 2011003c 1611fff2 2002000a c 20080001 20090003 20110876
  //   112020 20020022 c 200b0008 1118804 1318804 112020 20020022 c 216bffff 1560fff9 2002000a c 2008ffff
  //   20117777 112020 20020022 c 200b0010 3a31ffff 112020 20020022 c 216bffff 1560fffa 2002000a c 20090000
  //   200b0020 20110000 20120001 a1310000 112020 20020022 c 2328820 21290001 216bffff 1560fff8 200b0008
  //   20090000 8d310000 112020 20020022 c 21290004 216bffff 1560fff9 2002000a c 2011000f 112020 20020022 c
  //   2231ffff 1e20fffb 2002000a c 20100000 22100001 102020 20020022 c 22100002 102020 20020022 c 22100003
  //   102020 20020022 c 22100004 102020 20020022 c 22100005 102020 20020022 c 22100006 102020 20020022 c
  //   22100007 102020 20020022 c 22100008 102020 20020022 20020022 c 3e00008
  //   控制位
  //   流水调试日志用
  //   暂停节拍，不能为0
  //   戳工具置1进入计数暂停模式，ctrl+k时钟自动运行到对应节拍暂停
  //   ctrl+k关闭时钟连续运行，将控制位置零，进入单步调试模式调试
  //   OP
  //   Func
  //   rs
  //   rt
  //   rd
  //   可计数暂停的时钟源
  //   SB
  //   JMP
  //   JR
  //   SignedExt
  //   SLLV
  //   OP
  //   Func
  //   Syscall
  //   BGTZ
  //   Beq
  //   Bne
  //   MemToReg
  //   MemWrite
  //   AluOP
  //   AluSrcB
  //   RegWrite
  //   JAL
  //   Regdst
  //   为方便自动评测，需要输出流水线各段保存的PC值，注意是PC不是PC+4，另外ID段寄存器写入信息，Mem段内存写入信息也要输出
  //   shamt
  //   addr
  //   imm
  //   符号扩展
  //   WriteReg#
  //   ALUsrc
endmodule
module \流水线中断  (
  output RegWrite,
  output MemWrite,
  output [31:0] IF_PC,
  output [31:0] ID_PC,
  output [31:0] EX_PC,
  output [31:0] M_PC,
  output [31:0] WB_PC,
  output [31:0] RDin,
  output [31:0] MDin,
  output [31:0] LedData
);

  wire and_1_out, and_2_out, and_5_out, and_6_out, and_7_out, and_8_out, Beq, BGTZ, Bne, BranchTaken, CLK,
       clock_1_out, clock_2_out, clrA, clrB, clrC, comparator_1_eq, comparator_1_lt, comparator_3_eq,
       comparator_4_gt, d_ff_1_q, En, Equal, eret, ex_mem_1_jal_2, ex_mem_1_memtoreg_2, ex_mem_1_syscall_2,
       EX_RegWrite, flush, Go, h_en, Halt, id_ex_1_alusrcb_2, id_ex_1_jal_2, id_ex_1_memtoreg_2,
       id_ex_1_memwrite_2, id_ex_1_sb_2, id_ex_1_syscall_2, \IE中断使能寄存器_q , Int, IR1, IR2, IR3, JAL, JMP, JR,
       MEM_RegWrite, MemToReg, nand_1_out, not_1_out, not_2_out, not_3_out, not_4_out, or_2_out, or_3_out,
       RegDst, RST, SB, SignedExt, SLLV, stall, Syscall, W1, W2, W3, \中断按键_1_与中断屏蔽位与 , \中断按键_2_与中断屏蔽位与 ,
       \中断按键_3_与中断屏蔽位与 , \单周期硬布线控制器_1_alu_src , \单周期硬布线控制器_1_beq , \单周期硬布线控制器_1_bgtz , \单周期硬布线控制器_1_bne ,
       \单周期硬布线控制器_1_jal , \单周期硬布线控制器_1_jmp , \单周期硬布线控制器_1_jr , \单周期硬布线控制器_1_memtoreg ,
       \单周期硬布线控制器_1_memwrite , \单周期硬布线控制器_1_regwrite , \单周期硬布线控制器_1_sb , \单周期硬布线控制器_1_signedext ,
       \单周期硬布线控制器_1_sllv , \单周期硬布线控制器_1_syscall ;
  wire [1:0] priority_encoder_1_out, register_2_q;
  wire [3:0] id_ex_1_aluop_2, \单周期硬布线控制器_1_alu_op ;
  wire [4:0] EX_W_num, MEM_W_num, mem_wb_1_writereg_num_2, multiplexer_4_out, multiplexer_5_out,
       multiplexer_6_out, multiplexer_10_out, W_num;
  wire [12:0] CNT_num;
  wire [15:0] \LoadUse次数 , \总周期数 , \插入气泡数 , \无条件分支数 , \条件分支成功数 ;
  wire [27:0] id_ex_1_pc_4_2;
  wire [31:0] A0, adder_1_out, adder_3_out, BAddr, bit_extender_1_out, bit_extender_2_out, EX_IR,
       ex_mem_1_r1_2, ex_mem_1_result_2, fall_regfile_1_r1, fall_regfile_1_r2, GPRrs, GPRrt, id_ex_1_rt_2,
       ID_IR, if_id_1_pc_4_2, IF_IR, Int_addr, MEM_IR, mem_wb_1_memdata_2, mem_wb_1_result_2,
       mips_alu_1_result, multiplexer_1_out, multiplexer_2_out, multiplexer_3_out, multiplexer_8_out,
       multiplexer_9_out, multiplexer_12_out, ram_1_data, ret_addr, shifter_1_out, V0, WB_IR,
       \按字节存储电路_1_ddata ;
  wire [31:28] JMPAddr;

  Button \u_总复位  (.out(RST));
  Button _1 (.out(IR1));
  Button _2 (.out(IR2));
  Button _3 (.out(IR3));
  // Probe on \总周期数 
  // Probe on \总周期数 
  Button \u_继续运行  (.out(Go));
  LED #(.active("true")) led_1 (.in(W1));
  LED #(.active("true")) led_2 (.in(W2));
  LED #(.active("true")) led_3 (.in(W3));
  not not_1 (not_1_out, Halt);
  not not_2 (not_2_out, stall);
  Counter #(.width(16), .max('hffff), .ongoal("wrap"), .trigger("rising"), .behavior("new")) counter_1 (
    .count(JMP), .Q(\无条件分支数 ), .clk(CLK), .clr(RST));  // open: load, D, carry, preset, down
  Hex_Digit_Display hex_digit_display_1 (.value(LedData[31:28]));  // open: dp
  // Probe on IF_PC[19:0]
  // Mips_Probe mips_probe_1: pin names not known; wires that end beside it: IF_IR
  and and_1 (and_1_out, not_1_out, not_2_out);
  Multiplexer #(.select(3), .width(32), .disabled("Z"), .enable("false")) multiplexer_1 (
    .in0(adder_1_out), .in1(BAddr), .in3({JMPAddr, EX_IR[25:0], 2'b00}), .in7(GPRrs),
    .out(multiplexer_1_out), .sel({JR, JMP, BranchTaken}));  // open: in2, in4, in5, in6
  Hex_Digit_Display hex_digit_display_2 (.value(LedData[27:24]));  // open: dp
  Hex_Digit_Display hex_digit_display_3 (.value(LedData[23:20]));  // open: dp
  // Probe on ID_PC[19:0]
  // Mips_Probe mips_probe_2: pin names not known; wires that end beside it: ID_IR
  or or_1 (En, and_1_out, Go);
  Register #(.width(32), .trigger("rising"), .Select("low")) register_1 (
    .D(multiplexer_1_out), .en(Int), .Q(ret_addr), .clk(CLK));  // open: clr
  Hex_Digit_Display hex_digit_display_4 (.value(LedData[19:16]));  // open: dp
  Hex_Digit_Display hex_digit_display_5 (.value(LedData[15:12]));  // open: dp
  Multiplexer #(.select(1), .width(32), .disabled("Z"), .enable("false")) multiplexer_2 (
    .in0(multiplexer_1_out), .in1(Int_addr), .out(multiplexer_2_out), .sel(Int));
  Hex_Digit_Display hex_digit_display_6 (.value(LedData[11:8]));  // open: dp
  Hex_Digit_Display hex_digit_display_7 (.value(LedData[7:4]));  // open: dp
  Clock #(.highDuration(1), .lowDuration(1)) clock_1 (.out(clock_1_out));
  // Probe on EX_PC[19:0]
  // Mips_Probe mips_probe_3: pin names not known; wires that end beside it: clock_1_out, EX_IR, CLK
  and and_2 (and_2_out, BranchTaken, ~JMP);  // AND_Gate
  Counter #(.width(16), .max('hffff), .ongoal("wrap"), .trigger("rising"), .behavior("new")) counter_2 (
    .count(and_2_out), .Q(\条件分支成功数 ), .clk(CLK), .clr(RST));  // open: load, D, carry, preset, down
  Multiplexer #(.select(1), .width(32), .disabled("Z"), .enable("false")) multiplexer_3 (
    .in0(multiplexer_2_out), .in1(ret_addr), .out(multiplexer_3_out), .sel(eret));
  Hex_Digit_Display hex_digit_display_8 (.value(LedData[3:0]));  // open: dp
  Register #(.width(32), .trigger("rising"), .Select("low")) PC (
    .D(multiplexer_3_out), .en(En), .Q(IF_PC), .clk(CLK), .clr(RST));
  // Probe on \总周期数 
  // Probe on M_PC[19:0]
  // Mips_Probe mips_probe_4: pin names not known; wires that end beside it: MEM_IR
  not not_3 (not_3_out, Halt);
  Counter #(.width(16), .max('hffff), .ongoal("wrap"), .trigger("rising"), .behavior("new")) counter_3 (
    .count(not_3_out), .Q(\总周期数 ), .clk(CLK), .clr(RST));  // open: load, D, carry, preset, down
  // Probe on \总周期数 
  // Probe on \无条件分支数 
  // Probe on \条件分支成功数 
  // Probe on \插入气泡数 
  // Probe on \LoadUse次数 
  Adder #(.width(32)) adder_1 (.a(IF_PC), .b(32'h4), .out(adder_1_out), .cin(1'b0));  // open: cout
  // Probe on IF_PC[11:0]
  // Probe on WB_PC[19:0]
  // Mips_Probe mips_probe_5: pin names not known; wires that end beside it: stall, WB_IR
  Counter #(.width(16), .max('hffff), .ongoal("wrap"), .trigger("rising"), .behavior("new")) counter_4 (
    .count(stall), .Q(\插入气泡数 ), .clk(CLK), .clr(RST));  // open: load, D, carry, preset, down
  ROM #(.addrWidth(10), .dataWidth(32), .Select("high")) rom_1 (.addr(IF_PC[11:2]), .data(IF_IR));
  // Probe on EX_PC[11:0]
  // Probe on ID_PC[11:0]
  IF_ID if_id_1 (
    .PC(IF_PC), .IR(IF_IR), .PC_4(adder_1_out), .PC_2(ID_PC), .IR_2(ID_IR), .PC_4_2(if_id_1_pc_4_2),
    .Clk(CLK), .\异步清0 (RST), .EN(En), .\同步清0 (BranchTaken));  // open: PredictJump_2, PredictJump
  // Probe on M_PC[11:0]
  D_Flip_Flop #(.trigger("high"), .Pre_Clr_Positions("LEGACY"), .NegatePresetClear("false"), .enable("true"), .NewFFLayout("false")) d_ff_1 (.Q(d_ff_1_q));  // open: clk, D, Qn, preset, en, reset
  // Probe on 13'he20
  // Mips_Probe mips_probe_6: pin names not known; wires that end beside it: ID_IR
  \中断按键  \u_中断按键_1  (.clk(CLK), .\中断源 (IR1), .\中断等待信号 (W1), .\与中断屏蔽位与 (\中断按键_1_与中断屏蔽位与 ), .\同步清零信号 (clrA));
  \中断按键  \u_中断按键_2  (.clk(CLK), .\中断源 (IR2), .\中断等待信号 (W2), .\与中断屏蔽位与 (\中断按键_2_与中断屏蔽位与 ), .\同步清零信号 (clrB));
  \中断按键  \u_中断按键_3  (.clk(CLK), .\中断源 (IR3), .\中断等待信号 (W3), .\与中断屏蔽位与 (\中断按键_3_与中断屏蔽位与 ), .\同步清零信号 (clrC));
  // Probe on WB_PC[11:0]
  Comparator #(.width(13), .mode("twosComplement")) comparator_1 (
    .a(CNT_num), .b(13'he20), .eq(comparator_1_eq), .lt(comparator_1_lt));  // open: gt
  Clock #(.highDuration(1), .lowDuration(1)) clock_2 (.out(clock_2_out));
  nand nand_1 (nand_1_out, d_ff_1_q, comparator_1_eq);
  Counter #(.width(13), .max('h1fff), .ongoal("stay"), .trigger("rising"), .behavior("old")) counter_5 (
    .count(comparator_1_lt), .Q(CNT_num), .clk(clock_2_out), .clr(RST));  // open: load, D, carry, preset
  Multiplexer #(.select(1), .width(5), .disabled("Z"), .enable("false")) multiplexer_4 (
    .in0(ID_IR[20:16]), .in1(ID_IR[15:11]), .out(multiplexer_4_out), .sel(RegDst));
  Comparator #(.width(32), .mode("twosComplement")) comparator_2 (
    .a(32'h42000018), .b(IF_IR), .eq(eret));  // open: gt, lt
  or or_2 (or_2_out, \中断按键_1_与中断屏蔽位与 , \中断按键_2_与中断屏蔽位与 , \中断按键_3_与中断屏蔽位与 );
  Priority_Encoder #(.select(2), .disabled("Z")) priority_encoder_1 (
    .in1(\中断按键_1_与中断屏蔽位与 ), .in2(\中断按键_2_与中断屏蔽位与 ), .in3(\中断按键_3_与中断屏蔽位与 ), .out(priority_encoder_1_out));  // open: in0, gs, en_out, en_in
  assign CLK = nand_1_out ? clock_2_out : 1'bz;  // Controlled_Buffer controlled_buffer_1
  Multiplexer #(.select(1), .width(5), .disabled("Z"), .enable("false")) multiplexer_5 (
    .in0(ID_IR[25:21]), .in1(5'b00010), .out(multiplexer_5_out), .sel(\单周期硬布线控制器_1_syscall ));
  Multiplexer #(.select(1), .width(5), .disabled("Z"), .enable("false")) multiplexer_6 (
    .in0(ID_IR[20:16]), .in1(5'b00100), .out(multiplexer_6_out), .sel(\单周期硬布线控制器_1_syscall ));
  or or_3 (or_3_out, eret, ~or_2_out);  // OR_Gate
  Multiplexer #(.select(2), .width(32), .disabled("Z"), .enable("false")) multiplexer_7 (
    .in1(32'h30ac), .in2(32'h3150), .in3(32'h31f4), .out(Int_addr), .sel(priority_encoder_1_out));  // open: in0
  Pull_Resistor #(.pull(1)) pull_resistor_1 (.node(CLK));
  \单周期硬布线控制器  \u_单周期硬布线控制器_1  (
    .Func(ID_IR[5:0]), .OP(ID_IR[31:26]), .ALU_OP(\单周期硬布线控制器_1_alu_op ), .MemToReg(\单周期硬布线控制器_1_memtoreg ),
    .MemWrite(\单周期硬布线控制器_1_memwrite ), .ALU_SRC(\单周期硬布线控制器_1_alu_src ), .RegWrite(\单周期硬布线控制器_1_regwrite ),
    .SysCALL(\单周期硬布线控制器_1_syscall ), .SignedExt(\单周期硬布线控制器_1_signedext ), .RegDst(RegDst),
    .JR(\单周期硬布线控制器_1_jr ), .JMP(\单周期硬布线控制器_1_jmp ), .Beq(\单周期硬布线控制器_1_beq ), .JAL(\单周期硬布线控制器_1_jal ),
    .Bne(\单周期硬布线控制器_1_bne ), .SB(\单周期硬布线控制器_1_sb ), .BGTZ(\单周期硬布线控制器_1_bgtz ), .SLLV(\单周期硬布线控制器_1_sllv ));
  fall_regfile fall_regfile_1 (
    .Din(RDin), .Clk(CLK), .R1(fall_regfile_1_r1), .R2(fall_regfile_1_r2), .WE(RegWrite), .W_num(W_num),
    .R1_num(multiplexer_5_out), .R2_num(multiplexer_6_out));
  Register #(.width(1), .trigger("rising"), .Select("low")) \IE中断使能寄存器  (
    .D(or_3_out), .en(En), .Q(\IE中断使能寄存器_q ), .clk(CLK));  // open: clr
  Demultiplexer #(.select(2), .width(1), .tristate("false"), .disabled("Z"), .enable("false")) demultiplexer_1 (
    .out1(clrA), .out2(clrB), .out3(clrC), .in(eret), .sel(register_2_q));  // open: out0
  and and_3 (Int, \IE中断使能寄存器_q , or_2_out);
  Register #(.width(2), .trigger("rising"), .Select("low")) register_2 (
    .D(priority_encoder_1_out), .en(Int), .Q(register_2_q), .clk(CLK));  // open: clr
  not not_4 (not_4_out, Halt);
  // Probe on register_2_q
  or or_4 (h_en, not_4_out, Go);
  ID_EX id_ex_1 (
    .JMP(\单周期硬布线控制器_1_jmp ), .JR(\单周期硬布线控制器_1_jr ), .SignEXt(\单周期硬布线控制器_1_signedext ),
    .Beq(\单周期硬布线控制器_1_beq ), .Bne(\单周期硬布线控制器_1_bne ), .MemToReg(\单周期硬布线控制器_1_memtoreg ),
    .MemWrite(\单周期硬布线控制器_1_memwrite ), .AluOP(\单周期硬布线控制器_1_alu_op ), .AluSrcB(\单周期硬布线控制器_1_alu_src ),
    .RegWrite(\单周期硬布线控制器_1_regwrite ), .PC(ID_PC), .IR(ID_IR), .RS(fall_regfile_1_r1),
    .RT(fall_regfile_1_r2), .WriteReg_num(multiplexer_4_out), .PC_4(if_id_1_pc_4_2), .JMP_2(JMP), .JR_2(JR),
    .SignEXt_2(SignedExt), .Beq_2(Beq), .Bne_2(Bne), .MemToReg_2(id_ex_1_memtoreg_2),
    .MemWrite_2(id_ex_1_memwrite_2), .AluOP_2(id_ex_1_aluop_2), .AluSrcB_2(id_ex_1_alusrcb_2),
    .RegWrite_2(EX_RegWrite), .PC_2(EX_PC), .IR_2(EX_IR), .RS_2(GPRrs), .RT_2(id_ex_1_rt_2),
    .WriteReg_num_2(EX_W_num), .PC_4_2({JMPAddr, id_ex_1_pc_4_2}), .Clk(CLK), .\异步清0 (RST),
    .JAL(\单周期硬布线控制器_1_jal ), .JAL_2(id_ex_1_jal_2), .EN(h_en), .\同步清0 (flush), .BGTZ(\单周期硬布线控制器_1_bgtz ),
    .BGTZ_2(BGTZ), .SLLV(\单周期硬布线控制器_1_sllv ), .SLLV_2(SLLV), .SB(\单周期硬布线控制器_1_sb ), .SB_2(id_ex_1_sb_2),
    .syscall(\单周期硬布线控制器_1_syscall ), .syscall_2(id_ex_1_syscall_2));  // open: RT_F_2, RT_F, RS_F_2, RS_F, PredictJump, PredictJump_2
  assign bit_extender_1_out = {{16{1'b0}}, EX_IR[15:0]};  // Bit_Extender bit_extender_1
  assign bit_extender_2_out = {{16{EX_IR[15]}}, EX_IR[15:0]};  // Bit_Extender bit_extender_2
  Multiplexer #(.select(1), .width(32), .disabled("Z"), .enable("false")) multiplexer_8 (
    .in0(bit_extender_1_out), .in1(bit_extender_2_out), .out(multiplexer_8_out), .sel(SignedExt));
  Shifter #(.width(32), .shift("ll")) shifter_1 (.in(bit_extender_2_out), .\dist (5'b00010), .out(shifter_1_out));
  Multiplexer #(.select(1), .width(32), .disabled("Z"), .enable("false")) multiplexer_9 (
    .in0(id_ex_1_rt_2), .in1(multiplexer_8_out), .out(multiplexer_9_out), .sel(id_ex_1_alusrcb_2));
  Adder #(.width(32)) adder_2 (
    .a(shifter_1_out), .b({JMPAddr, id_ex_1_pc_4_2}), .out(BAddr), .cin(1'b0));  // open: cout
  \相关处理逻辑  \u_相关处理逻辑_1  (
    .Instr(ID_IR), .EX_RegWrite(EX_RegWrite), .EX_W_num(EX_W_num), .BranchTaken(BranchTaken),
    .MEM_RegWrite(MEM_RegWrite), .MEM_W_num(MEM_W_num), .stall(stall), .flush(flush));
  MIPS_ALU mips_alu_1 (
    .X(GPRrs), .Y(multiplexer_9_out), .AluOP(id_ex_1_aluop_2), .Equal(Equal), .Result(mips_alu_1_result),
    .shamt(multiplexer_10_out));  // open: Result_2
  Multiplexer #(.select(1), .width(5), .disabled("Z"), .enable("false")) multiplexer_10 (
    .in0(EX_IR[10:6]), .in1(GPRrs[4:0]), .out(multiplexer_10_out), .sel(SLLV));
  // Probe on mips_alu_1_result
  Comparator #(.width(32), .mode("twosComplement")) comparator_3 (
    .a(V0), .b(32'ha), .eq(comparator_3_eq));  // open: gt, lt
  EX_MEM ex_mem_1 (
    .MemToReg(id_ex_1_memtoreg_2), .RegWrite(EX_RegWrite), .PC(EX_PC), .IR(EX_IR),
    .Result(mips_alu_1_result), .Writedata(id_ex_1_rt_2), .WriteReg_num(EX_W_num),
    .MemToReg_2(ex_mem_1_memtoreg_2), .RegWrite_2(MEM_RegWrite), .PC_2(M_PC), .IR_2(MEM_IR),
    .Result_2(ex_mem_1_result_2), .Writedata_2(GPRrt), .WriteReg_num_2(MEM_W_num), .Clk(CLK), .Rst(RST),
    .MemWrite_2(MemWrite), .MemWrite(id_ex_1_memwrite_2), .JAL(id_ex_1_jal_2), .JAL_2(ex_mem_1_jal_2),
    .EN(h_en), .R1_2(ex_mem_1_r1_2), .R1(GPRrs), .syscall_2(ex_mem_1_syscall_2), .syscall(id_ex_1_syscall_2),
    .SB(id_ex_1_sb_2), .SB_2(SB));  // open: JMP, JR, JMP_2, JR_2, 同步清0
  and and_4 (Halt, Syscall, comparator_3_eq);
  and and_5 (and_5_out, ~comparator_3_eq, Syscall);  // AND_Gate
  Register #(.width(32), .trigger("rising"), .Select("low")) register_3 (
    .D(A0), .en(and_5_out), .Q(LedData), .clk(CLK));  // open: clr
  // Probe on ex_mem_1_result_2
  RAM #(.addrWidth(10), .dataWidth(32), .bus("separate"), .Select("high")) ram_1 (
    .addr(ex_mem_1_result_2[11:2]), .din(MDin), .data(ram_1_data), .str(MemWrite), .clk(CLK), .ld(1'b1),
    .clr(RST));  // open: sel
  \按字节存储电路  \u_按字节存储电路_1  (.cdata(GPRrt), .sel(ex_mem_1_result_2), .sdata(ram_1_data), .ddata(\按字节存储电路_1_ddata ));
  MEM_WB mem_wb_1 (
    .MemToReg(ex_mem_1_memtoreg_2), .RegWrite(MEM_RegWrite), .PC(M_PC), .IR(MEM_IR),
    .Result(ex_mem_1_result_2), .Memdata(ram_1_data), .WriteReg_num(MEM_W_num), .MemToReg_2(MemToReg),
    .RegWrite_2(RegWrite), .PC_2(WB_PC), .IR_2(WB_IR), .Result_2(mem_wb_1_result_2),
    .Memdata_2(mem_wb_1_memdata_2), .WriteReg_num_2(mem_wb_1_writereg_num_2), .Clk(CLK), .Rst(RST),
    .JAL(ex_mem_1_jal_2), .JAL_2(JAL), .R1_2(V0), .R1(ex_mem_1_r1_2), .En(h_en), .syscall_2(Syscall),
    .syscall(ex_mem_1_syscall_2), .R1_3(A0), .R2(GPRrt));  // open: JMP_2, JR_2, JMP, JR, 同步清0
  Multiplexer #(.select(1), .width(32), .disabled("Z"), .enable("false")) multiplexer_11 (
    .in0(GPRrt), .in1(\按字节存储电路_1_ddata ), .out(MDin), .sel(SB));
  Multiplexer #(.select(1), .width(32), .disabled("Z"), .enable("false")) multiplexer_12 (
    .in0(mem_wb_1_result_2), .in1(mem_wb_1_memdata_2), .out(multiplexer_12_out), .sel(MemToReg));
  Multiplexer #(.select(1), .width(5), .disabled("Z"), .enable("false")) multiplexer_13 (
    .in0(mem_wb_1_writereg_num_2), .in1({5{1'b1}}), .out(W_num), .sel(JAL));
  // Probe on W_num
  and and_6 (and_6_out, Beq, Equal);
  and and_7 (and_7_out, ~Equal, Bne);  // AND_Gate
  Comparator #(.width(32), .mode("twosComplement")) comparator_4 (
    .a(GPRrs), .b({32{1'b0}}), .gt(comparator_4_gt));  // open: eq, lt
  and and_8 (and_8_out, comparator_4_gt, BGTZ);
  or or_5 (BranchTaken, and_6_out, and_7_out, and_8_out, JMP);
  Adder #(.width(32)) adder_3 (.a(WB_PC), .b(32'h4), .out(adder_3_out), .cin(1'b0));  // open: cout
  Multiplexer #(.select(1), .width(32), .disabled("Z"), .enable("false")) multiplexer_14 (
    .in0(multiplexer_12_out), .in1(adder_3_out), .out(RDin), .sel(JAL));

  // Other names for the same wires on the sheet: JMPAddr[27:2] = EX_IR[25:0]; shamt[4:0] = EX_IR[10:6];
  //   MEM_PC[31:0] = M_PC; PC[31:0] = IF_PC

  // Notes on the sheet:
  //   中断源
  //   时空图监测，可删除
  //   中断等待指示
  //   数码管输出
  //   指令存储器
  //   contents of rom_1 (hex, n*v repeats v):
  //   201d07d0 20100001 109fc0 139fc3 8021 2012000c 24160008 26100001 3210000f 20080008 20090001 139900
  //   2709825 132020 20020022 c 1094022 1500fff9 22100001 2018000f 2188024 108700 20080008 20090001 139902
  //   2709825 132021 20020022 c 1094022 1500fff9 108702 2c9b022 12c00001 8000c07 4020 1084027 84400
  //   3508ffff 82021 20020022 c 8000c01 afa20000 23bd0004 afa40000 23bd0004 afb00000 23bd0004 afb30000
  //   23bd0004 afb40000 23bd0004 afb50000 23bd0004 afb60000 23bd0004 20160001 20140003 20150001 168020
  //   108100 2149825 132020 20020022 c 1600fffa 295a022 1680fff7 23bdfffc 8fb60000 23bdfffc 8fb50000
  //   23bdfffc 8fb40000 23bdfffc 8fb30000 23bdfffc 8fb00000 23bdfffc 8fa40000 23bdfffc 8fa20000 42000018
  //   afa20000 23bd0004 afa40000 23bd0004 afb00000 23bd0004 afb30000 23bd0004 afb40000 23bd0004 afb50000
  //   23bd0004 afb60000 23bd0004 20160002 20140003 20150001 168020 108100 2149825 132020 20020022 c
  //   1600fffa 295a022 1680fff7 23bdfffc 8fb60000 23bdfffc 8fb50000 23bdfffc 8fb40000 23bdfffc 8fb30000
  //   23bdfffc 8fb00000 23bdfffc 8fa40000 23bdfffc 8fa20000 42000018 afa20000 23bd0004 afa40000 23bd0004
  //   afb00000 23bd0004 afb30000 23bd0004 afb40000 23bd0004 afb50000 23bd0004 afb60000 23bd0004 20160003
  //   20140003 20150001 168020 108100 2149825 132020 20020022 c 1600fffa 295a022 1680fff7 23bdfffc
  //   8fb60000 23bdfffc 8fb50000 23bdfffc 8fb40000 23bdfffc 8fb30000 23bdfffc 8fb00000 23bdfffc 8fa40000
  //   23bdfffc 8fa20000 42000018
  //   控制位
  //   流水调试日志用
  //   暂停节拍，不能为0
  //   戳工具置1进入计数暂停模式，ctrl+k时钟自动运行到对应节拍暂停
  //   ctrl+k关闭时钟连续运行，将控制位置零，进入单步调试模式调试
  //   OP
  //   Func
  //   rs
  //   rt
  //   rd
  //   eret指令
  //   中断程序入口地址
  //   有中断
  //   可计数暂停的时钟源
  //   SB
  //   JMP
  //   JR
  //   SignedExt
  //   SLLV
  //   OP
  //   Func
  //   Syscall
  //   BGTZ
  //   Beq
  //   Bne
  //   MemToReg
  //   MemWrite
  //   AluOP
  //   AluSrcB
  //   RegWrite
  //   JAL
  //   Regdst
  //   为方便自动评测，需要输出流水线各段保存的PC值，注意是PC不是PC+4，另外ID段寄存器写入信息，Mem段内存写入信息也要输出
  //   中断请求
  //   shamt
  //   addr
  //   imm
  //   符号扩展
  //   WriteReg#
endmodule

module BTB (
  input  [31:0] PC,
  input  [31:0] EX_PC,
  input  [31:0] EX_BranchAddr,
  input  clk,
  input  EX_Branch,
  input  EX_BranchTaken,
  output [31:0] JumpAddr,
  output PredictJump
);

  wire clr0, clr1, clr2, clr3, clr4, clr5, clr6, clr7, comparator_1_eq, comparator_2_eq, comparator_3_eq,
       comparator_4_eq, comparator_5_eq, comparator_6_eq, comparator_7_eq, comparator_8_eq, comparator_9_eq,
       comparator_10_eq, comparator_11_eq, comparator_12_eq, comparator_13_eq, comparator_14_eq,
       comparator_15_eq, comparator_16_eq, hit, L0, L1, L2, L3, L4, L5, L6, L7, not_9_out, or_2_out, Predict,
       V0, V1, V2, V3, V4, V5, V6, V7, w_hit, w_miss, WriteL0, WriteL1, WriteL2, WriteL3, WriteL4, WriteL5,
       WriteL6, WriteL7;
  wire [1:0] \分支预测历史位_2_q , \分支预测历史位_3_q , \分支预测历史位_4_q , \分支预测历史位_5_q , \分支预测历史位_6_q , \分支预测历史位_7_q ,
       \分支预测历史位_8_q , \分支预测历史位_q , \分支预测状态转移_1_outstate , \分支预测状态转移_2_outstate , \分支预测状态转移_3_outstate ,
       \分支预测状态转移_4_outstate , \分支预测状态转移_5_outstate , \分支预测状态转移_6_outstate , \分支预测状态转移_7_outstate ,
       \分支预测状态转移_8_outstate ;
  wire [2:0] k, \max2归并比较_1_max_num , \max2归并比较_2_max_num , \max2归并比较_3_max_num , \max2归并比较_4_max_num ,
       \max2归并比较_5_max_num , \max2归并比较_6_max_num ;
  wire [15:0] C0, C1, C2, C3, C4, C5, C6, C7;
  wire [16:0] \max2归并比较_1_max , \max2归并比较_2_max , \max2归并比较_3_max , \max2归并比较_4_max , \max2归并比较_5_max ,
       \max2归并比较_6_max ;
  wire [16:16] not_1_out, not_2_out, not_3_out, not_4_out, not_5_out, not_6_out, not_7_out, not_8_out;
  wire [31:0] PC0, PC1, PC2, PC3, PC4, PC5, PC6, PC7, \分支目标地址_2_q , \分支目标地址_3_q , \分支目标地址_4_q , \分支目标地址_5_q ,
       \分支目标地址_6_q , \分支目标地址_7_q , \分支目标地址_8_q , \分支目标地址_q ;

  Pull_Resistor #(.pull(0)) pull_resistor_1 (.node(WriteL5));
  Pull_Resistor #(.pull(0)) pull_resistor_2 (.node(WriteL6));
  Pull_Resistor #(.pull(0)) pull_resistor_3 (.node(WriteL7));
  Pull_Resistor #(.pull(0)) pull_resistor_4 (.node(WriteL0));
  Pull_Resistor #(.pull(0)) pull_resistor_5 (.node(WriteL1));
  Register #(.width(1), .trigger("rising"), .Select("low")) valid (
    .D(1'b1), .en(WriteL2), .Q(V2), .clk(clk));  // open: clr
  Pull_Resistor #(.pull(0)) pull_resistor_6 (.node(WriteL2));
  Register #(.width(1), .trigger("rising"), .Select("low")) valid_2 (
    .D(1'b1), .en(WriteL3), .Q(V3), .clk(clk));  // open: clr
  Pull_Resistor #(.pull(0)) pull_resistor_7 (.node(WriteL3));
  Register #(.width(1), .trigger("rising"), .Select("low")) valid_3 (
    .D(1'b1), .en(WriteL4), .Q(V4), .clk(clk));  // open: clr
  Pull_Resistor #(.pull(0)) pull_resistor_8 (.node(WriteL4));
  Register #(.width(1), .trigger("rising"), .Select("low")) valid_4 (
    .D(1'b1), .en(WriteL5), .Q(V5), .clk(clk));  // open: clr
  Register #(.width(1), .trigger("rising"), .Select("low")) valid_5 (
    .D(1'b1), .en(WriteL6), .Q(V6), .clk(clk));  // open: clr
  Register #(.width(1), .trigger("rising"), .Select("low")) valid_6 (
    .D(1'b1), .en(WriteL7), .Q(V7), .clk(clk));  // open: clr
  Register #(.width(1), .trigger("rising"), .Select("low")) valid_7 (
    .D(1'b1), .en(WriteL0), .Q(V0), .clk(clk));  // open: clr
  Register #(.width(1), .trigger("rising"), .Select("low")) valid_8 (
    .D(1'b1), .en(WriteL1), .Q(V1), .clk(clk));  // open: clr
  Register #(.width(32), .trigger("rising"), .Select("low")) \u_分支指令地址  (
    .D(EX_PC), .en(WriteL3), .Q(PC3), .clk(clk));  // open: clr
  Register #(.width(32), .trigger("rising"), .Select("low")) \u_分支指令地址_2  (
    .D(EX_PC), .en(WriteL4), .Q(PC4), .clk(clk));  // open: clr
  Register #(.width(32), .trigger("rising"), .Select("low")) \u_分支指令地址_3  (
    .D(EX_PC), .en(WriteL5), .Q(PC5), .clk(clk));  // open: clr
  Register #(.width(32), .trigger("rising"), .Select("low")) \u_分支指令地址_4  (
    .D(EX_PC), .en(WriteL6), .Q(PC6), .clk(clk));  // open: clr
  Register #(.width(32), .trigger("rising"), .Select("low")) \u_分支指令地址_5  (
    .D(EX_PC), .en(WriteL7), .Q(PC7), .clk(clk));  // open: clr
  Register #(.width(32), .trigger("rising"), .Select("low")) \u_分支指令地址_6  (
    .D(EX_PC), .en(WriteL0), .Q(PC0), .clk(clk));  // open: clr
  Register #(.width(32), .trigger("rising"), .Select("low")) \u_分支指令地址_7  (
    .D(EX_PC), .en(WriteL1), .Q(PC1), .clk(clk));  // open: clr
  Register #(.width(32), .trigger("rising"), .Select("low")) \u_分支指令地址_8  (
    .D(EX_PC), .en(WriteL2), .Q(PC2), .clk(clk));  // open: clr
  Register #(.width(32), .trigger("rising"), .Select("low")) \u_分支目标地址  (
    .D(EX_BranchAddr), .en(WriteL6), .Q(\分支目标地址_q ), .clk(clk));  // open: clr
  Register #(.width(32), .trigger("rising"), .Select("low")) \u_分支目标地址_2  (
    .D(EX_BranchAddr), .en(WriteL7), .Q(\分支目标地址_2_q ), .clk(clk));  // open: clr
  Register #(.width(32), .trigger("rising"), .Select("low")) \u_分支目标地址_3  (
    .D(EX_BranchAddr), .en(WriteL0), .Q(\分支目标地址_3_q ), .clk(clk));  // open: clr
  Register #(.width(32), .trigger("rising"), .Select("low")) \u_分支目标地址_4  (
    .D(EX_BranchAddr), .en(WriteL1), .Q(\分支目标地址_4_q ), .clk(clk));  // open: clr
  Register #(.width(32), .trigger("rising"), .Select("low")) \u_分支目标地址_5  (
    .D(EX_BranchAddr), .en(WriteL2), .Q(\分支目标地址_5_q ), .clk(clk));  // open: clr
  Register #(.width(32), .trigger("rising"), .Select("low")) \u_分支目标地址_6  (
    .D(EX_BranchAddr), .en(WriteL3), .Q(\分支目标地址_6_q ), .clk(clk));  // open: clr
  Register #(.width(32), .trigger("rising"), .Select("low")) \u_分支目标地址_7  (
    .D(EX_BranchAddr), .en(WriteL4), .Q(\分支目标地址_7_q ), .clk(clk));  // open: clr
  Register #(.width(32), .trigger("rising"), .Select("low")) \u_分支目标地址_8  (
    .D(EX_BranchAddr), .en(WriteL5), .Q(\分支目标地址_8_q ), .clk(clk));  // open: clr
  Transistor #(.\type ("n"), .gate("tl"), .width(32)) transistor_1 (.in(\分支目标地址_2_q ), .out(JumpAddr), .gate(L7));
  Transistor #(.\type ("n"), .gate("tl"), .width(32)) transistor_2 (.in(\分支目标地址_3_q ), .out(JumpAddr), .gate(L0));
  Transistor #(.\type ("n"), .gate("tl"), .width(32)) transistor_3 (.in(\分支目标地址_4_q ), .out(JumpAddr), .gate(L1));
  Transistor #(.\type ("n"), .gate("tl"), .width(32)) transistor_4 (.in(\分支目标地址_5_q ), .out(JumpAddr), .gate(L2));
  Transistor #(.\type ("n"), .gate("tl"), .width(32)) transistor_5 (.in(\分支目标地址_6_q ), .out(JumpAddr), .gate(L3));
  Transistor #(.\type ("n"), .gate("tl"), .width(32)) transistor_6 (.in(\分支目标地址_7_q ), .out(JumpAddr), .gate(L4));
  Transistor #(.\type ("n"), .gate("tl"), .width(32)) transistor_7 (.in(\分支目标地址_8_q ), .out(JumpAddr), .gate(L5));
  Transistor #(.\type ("n"), .gate("tl"), .width(32)) transistor_8 (.in(\分支目标地址_q ), .out(JumpAddr), .gate(L6));
  Register #(.width(2), .trigger("rising"), .Select("low")) \u_分支预测历史位  (
    .D(\分支预测状态转移_2_outstate ), .en(clr1), .Q(\分支预测历史位_q ), .clk(clk));  // open: clr
  Register #(.width(2), .trigger("rising"), .Select("low")) \u_分支预测历史位_2  (
    .D(\分支预测状态转移_3_outstate ), .en(clr2), .Q(\分支预测历史位_2_q ), .clk(clk));  // open: clr
  Register #(.width(2), .trigger("rising"), .Select("low")) \u_分支预测历史位_3  (
    .D(\分支预测状态转移_4_outstate ), .en(clr3), .Q(\分支预测历史位_3_q ), .clk(clk));  // open: clr
  Register #(.width(2), .trigger("rising"), .Select("low")) \u_分支预测历史位_4  (
    .D(\分支预测状态转移_5_outstate ), .en(clr4), .Q(\分支预测历史位_4_q ), .clk(clk));  // open: clr
  Register #(.width(2), .trigger("rising"), .Select("low")) \u_分支预测历史位_5  (
    .D(\分支预测状态转移_6_outstate ), .en(clr5), .Q(\分支预测历史位_5_q ), .clk(clk));  // open: clr
  Register #(.width(2), .trigger("rising"), .Select("low")) \u_分支预测历史位_6  (
    .D(\分支预测状态转移_7_outstate ), .en(clr6), .Q(\分支预测历史位_6_q ), .clk(clk));  // open: clr
  Register #(.width(2), .trigger("rising"), .Select("low")) \u_分支预测历史位_7  (
    .D(\分支预测状态转移_8_outstate ), .en(clr7), .Q(\分支预测历史位_7_q ), .clk(clk));  // open: clr
  \分支预测状态转移  \u_分支预测状态转移_1  (.inState(\分支预测历史位_8_q ), .BranchTaken(EX_BranchTaken), .outState(\分支预测状态转移_1_outstate ));
  Register #(.width(2), .trigger("rising"), .Select("low")) \u_分支预测历史位_8  (
    .D(\分支预测状态转移_1_outstate ), .en(clr0), .Q(\分支预测历史位_8_q ), .clk(clk));  // open: clr
  \分支预测状态转移  \u_分支预测状态转移_2  (.inState(\分支预测历史位_q ), .BranchTaken(EX_BranchTaken), .outState(\分支预测状态转移_2_outstate ));
  \分支预测状态转移  \u_分支预测状态转移_3  (.inState(\分支预测历史位_2_q ), .BranchTaken(EX_BranchTaken), .outState(\分支预测状态转移_3_outstate ));
  \分支预测状态转移  \u_分支预测状态转移_4  (.inState(\分支预测历史位_3_q ), .BranchTaken(EX_BranchTaken), .outState(\分支预测状态转移_4_outstate ));
  \分支预测状态转移  \u_分支预测状态转移_5  (.inState(\分支预测历史位_4_q ), .BranchTaken(EX_BranchTaken), .outState(\分支预测状态转移_5_outstate ));
  \分支预测状态转移  \u_分支预测状态转移_6  (.inState(\分支预测历史位_5_q ), .BranchTaken(EX_BranchTaken), .outState(\分支预测状态转移_6_outstate ));
  \分支预测状态转移  \u_分支预测状态转移_7  (.inState(\分支预测历史位_6_q ), .BranchTaken(EX_BranchTaken), .outState(\分支预测状态转移_7_outstate ));
  \分支预测状态转移  \u_分支预测状态转移_8  (.inState(\分支预测历史位_7_q ), .BranchTaken(EX_BranchTaken), .outState(\分支预测状态转移_8_outstate ));
  Transistor #(.\type ("n"), .gate("tl"), .width(1)) transistor_9 (.in(\分支预测历史位_8_q [1]), .out(Predict), .gate(L0));
  Transistor #(.\type ("n"), .gate("tl"), .width(1)) transistor_10 (.in(\分支预测历史位_q [1]), .out(Predict), .gate(L1));
  Transistor #(.\type ("n"), .gate("tl"), .width(1)) transistor_11 (.in(\分支预测历史位_2_q [1]), .out(Predict), .gate(L2));
  Transistor #(.\type ("n"), .gate("tl"), .width(1)) transistor_12 (.in(\分支预测历史位_3_q [1]), .out(Predict), .gate(L3));
  Transistor #(.\type ("n"), .gate("tl"), .width(1)) transistor_13 (.in(\分支预测历史位_4_q [1]), .out(Predict), .gate(L4));
  Transistor #(.\type ("n"), .gate("tl"), .width(1)) transistor_14 (.in(\分支预测历史位_5_q [1]), .out(Predict), .gate(L5));
  Transistor #(.\type ("n"), .gate("tl"), .width(1)) transistor_15 (.in(\分支预测历史位_6_q [1]), .out(Predict), .gate(L6));
  Transistor #(.\type ("n"), .gate("tl"), .width(1)) transistor_16 (.in(\分支预测历史位_7_q [1]), .out(Predict), .gate(L7));
  Counter #(.width(16), .max('hffff), .ongoal("wrap"), .trigger("rising"), .behavior("new")) \u_置换标记  (
    .load(WriteL0), .D({16{1'b0}}), .Q(C0), .clk(clk), .clr(clr0));  // open: count, carry, preset, down
  Counter #(.width(16), .max('hffff), .ongoal("wrap"), .trigger("rising"), .behavior("new")) \u_置换标记_2  (
    .load(WriteL1), .D({16{1'b0}}), .Q(C1), .clk(clk), .clr(clr1));  // open: count, carry, preset, down
  Counter #(.width(16), .max('hffff), .ongoal("wrap"), .trigger("rising"), .behavior("new")) \u_置换标记_3  (
    .load(WriteL2), .D({16{1'b0}}), .Q(C2), .clk(clk), .clr(clr2));  // open: count, carry, preset, down
  Counter #(.width(16), .max('hffff), .ongoal("wrap"), .trigger("rising"), .behavior("new")) \u_置换标记_4  (
    .load(WriteL3), .D({16{1'b0}}), .Q(C3), .clk(clk), .clr(clr3));  // open: count, carry, preset, down
  Counter #(.width(16), .max('hffff), .ongoal("wrap"), .trigger("rising"), .behavior("new")) \u_置换标记_5  (
    .load(WriteL4), .D({16{1'b0}}), .Q(C4), .clk(clk), .clr(clr4));  // open: count, carry, preset, down
  Counter #(.width(16), .max('hffff), .ongoal("wrap"), .trigger("rising"), .behavior("new")) \u_置换标记_6  (
    .load(WriteL5), .D({16{1'b0}}), .Q(C5), .clk(clk), .clr(clr5));  // open: count, carry, preset, down
  Counter #(.width(16), .max('hffff), .ongoal("wrap"), .trigger("rising"), .behavior("new")) \u_置换标记_7  (
    .Q(C6), .clk(clk), .clr(clr6));  // open: load, D, count, carry, preset, down
  Counter #(.width(16), .max('hffff), .ongoal("wrap"), .trigger("rising"), .behavior("new")) \u_置换标记_8  (
    .Q(C7), .clk(clk), .clr(clr7));  // open: load, D, count, carry, preset, down
  Decoder #(.select(3), .tristate("false"), .disabled("Z"), .enable("true")) decoder_1 (
    .out0(WriteL0), .out1(WriteL1), .out2(WriteL2), .out3(WriteL3), .out4(WriteL4), .out5(WriteL5),
    .out6(WriteL6), .out7(WriteL7), .sel(k), .en(w_miss));
  Comparator #(.width(32), .mode("twosComplement")) comparator_1 (
    .a(PC), .b(PC0), .eq(comparator_1_eq));  // open: gt, lt
  Comparator #(.width(32), .mode("twosComplement")) comparator_2 (
    .a(PC), .b(PC1), .eq(comparator_2_eq));  // open: gt, lt
  Comparator #(.width(32), .mode("twosComplement")) comparator_3 (
    .a(PC), .b(PC2), .eq(comparator_3_eq));  // open: gt, lt
  Comparator #(.width(32), .mode("twosComplement")) comparator_4 (
    .a(PC), .b(PC3), .eq(comparator_4_eq));  // open: gt, lt
  Comparator #(.width(32), .mode("twosComplement")) comparator_5 (
    .a(PC), .b(PC4), .eq(comparator_5_eq));  // open: gt, lt
  Comparator #(.width(32), .mode("twosComplement")) comparator_6 (
    .a(PC), .b(PC5), .eq(comparator_6_eq));  // open: gt, lt
  Comparator #(.width(32), .mode("twosComplement")) comparator_7 (
    .a(PC), .b(PC6), .eq(comparator_7_eq));  // open: gt, lt
  Comparator #(.width(32), .mode("twosComplement")) comparator_8 (
    .a(PC), .b(PC7), .eq(comparator_8_eq));  // open: gt, lt
  Comparator #(.width(32), .mode("twosComplement")) comparator_9 (
    .a(EX_PC), .b(PC0), .eq(comparator_9_eq));  // open: gt, lt
  Comparator #(.width(32), .mode("twosComplement")) comparator_10 (
    .a(EX_PC), .b(PC1), .eq(comparator_10_eq));  // open: gt, lt
  Comparator #(.width(32), .mode("twosComplement")) comparator_11 (
    .a(EX_PC), .b(PC2), .eq(comparator_11_eq));  // open: gt, lt
  Comparator #(.width(32), .mode("twosComplement")) comparator_12 (
    .a(EX_PC), .b(PC3), .eq(comparator_12_eq));  // open: gt, lt
  Comparator #(.width(32), .mode("twosComplement")) comparator_13 (
    .a(EX_PC), .b(PC4), .eq(comparator_13_eq));  // open: gt, lt
  Comparator #(.width(32), .mode("twosComplement")) comparator_14 (
    .a(EX_PC), .b(PC5), .eq(comparator_14_eq));  // open: gt, lt
  Comparator #(.width(32), .mode("twosComplement")) comparator_15 (
    .a(EX_PC), .b(PC6), .eq(comparator_15_eq));  // open: gt, lt
  Comparator #(.width(32), .mode("twosComplement")) comparator_16 (
    .a(EX_PC), .b(PC7), .eq(comparator_16_eq));  // open: gt, lt
  not not_1 (not_1_out[16], V0);
  not not_2 (not_2_out[16], V1);
  not not_3 (not_3_out[16], V2);
  not not_4 (not_4_out[16], V3);
  not not_5 (not_5_out[16], V4);
  not not_6 (not_6_out[16], V5);
  not not_7 (not_7_out[16], V6);
  not not_8 (not_8_out[16], V7);
  and and_1 (L0, V0, comparator_1_eq);
  and and_2 (L1, V1, comparator_2_eq);
  and and_3 (L2, V2, comparator_3_eq);
  and and_4 (L3, V3, comparator_4_eq);
  and and_5 (L4, V4, comparator_5_eq);
  and and_6 (L5, V5, comparator_6_eq);
  and and_7 (L6, V6, comparator_7_eq);
  and and_8 (L7, V7, comparator_8_eq);
  and and_9 (clr0, V0, comparator_9_eq);
  and and_10 (clr1, V1, comparator_10_eq);
  and and_11 (clr2, V2, comparator_11_eq);
  and and_12 (clr3, V3, comparator_12_eq);
  and and_13 (clr4, V4, comparator_13_eq);
  and and_14 (clr5, V5, comparator_14_eq);
  and and_15 (clr6, V6, comparator_15_eq);
  and and_16 (clr7, V7, comparator_16_eq);
  \MAX2归并比较  \max2归并比较_1  (
    .Y({not_2_out[16], C1}), .X({not_1_out[16], C0}), .Y_num(3'b001), .X_num(3'b000), .MAX(\max2归并比较_1_max ),
    .MAX_num(\max2归并比较_1_max_num ));
  \MAX2归并比较  \max2归并比较_2  (
    .Y({not_4_out[16], C3}), .X({not_3_out[16], C2}), .Y_num(3'b011), .X_num(3'b010), .MAX(\max2归并比较_2_max ),
    .MAX_num(\max2归并比较_2_max_num ));
  \MAX2归并比较  \max2归并比较_3  (
    .Y({not_6_out[16], C5}), .X({not_5_out[16], C4}), .Y_num(3'b101), .X_num(3'b100), .MAX(\max2归并比较_3_max ),
    .MAX_num(\max2归并比较_3_max_num ));
  \MAX2归并比较  \max2归并比较_4  (
    .Y({not_8_out[16], C7}), .X({not_7_out[16], C6}), .Y_num(3'b111), .X_num(3'b110), .MAX(\max2归并比较_4_max ),
    .MAX_num(\max2归并比较_4_max_num ));
  \MAX2归并比较  \max2归并比较_5  (
    .Y(\max2归并比较_2_max ), .X(\max2归并比较_1_max ), .Y_num(\max2归并比较_2_max_num ), .X_num(\max2归并比较_1_max_num ),
    .MAX(\max2归并比较_5_max ), .MAX_num(\max2归并比较_5_max_num ));
  \MAX2归并比较  \max2归并比较_6  (
    .Y(\max2归并比较_4_max ), .X(\max2归并比较_3_max ), .Y_num(\max2归并比较_4_max_num ), .X_num(\max2归并比较_3_max_num ),
    .MAX(\max2归并比较_6_max ), .MAX_num(\max2归并比较_6_max_num ));
  or or_1 (hit, L0, L1, L2, L3, L4, L5, L6, L7);
  or or_2 (or_2_out, clr0, clr1, clr2, clr3, clr4, clr5, clr6, clr7);
  \MAX2归并比较  \max2归并比较_7  (
    .Y(\max2归并比较_6_max ), .X(\max2归并比较_5_max ), .Y_num(\max2归并比较_6_max_num ), .X_num(\max2归并比较_5_max_num ),
    .MAX_num(k));  // open: MAX
  Multiplexer #(.select(1), .width(1), .disabled("Z"), .enable("false")) multiplexer_1 (
    .in0(1'b0), .in1(Predict), .out(PredictJump), .sel(hit));
  not not_9 (not_9_out, or_2_out);
  // Probe on k
  and and_17 (w_miss, not_9_out, EX_Branch);
  and and_18 (w_hit, or_2_out, EX_Branch);

  // Notes on the sheet:
  //   输入
  //   输出
endmodule

module \MAX2归并比较  (
  input  [16:0] Y,
  input  [16:0] X,
  input  [2:0] Y_num,
  input  [2:0] X_num,
  output [16:0] MAX,
  output [2:0] MAX_num
);

  wire comparator_1_eq, comparator_1_gt, or_1_out;

  Multiplexer #(.select(1), .width(17), .disabled("Z"), .enable("false")) multiplexer_1 (
    .in0(Y), .in1(X), .out(MAX), .sel(or_1_out));
  Comparator #(.width(17), .mode("unsigned")) comparator_1 (
    .a(X), .b(Y), .gt(comparator_1_gt), .eq(comparator_1_eq));  // open: lt
  or or_1 (or_1_out, comparator_1_gt, comparator_1_eq);
  Multiplexer #(.select(1), .width(3), .disabled("Z"), .enable("false")) multiplexer_2 (
    .in0(Y_num), .in1(X_num), .out(MAX_num), .sel(or_1_out));

  // Notes on the sheet:
  //   输出两个输入中的较大值，并输出较大值的2位编号
endmodule

module \分支预测状态转移  (
  input  [1:0] inState,
  input  BranchTaken,
  output [1:0] outState
);

  wire and_1_out, and_2_out, and_3_out, and_4_out, not_1_out, not_2_out, not_3_out, not_4_out, not_5_out;

  not not_1 (not_1_out, inState[0]);
  not not_2 (not_2_out, inState[1]);
  not not_3 (not_3_out, inState[0]);
  not not_4 (not_4_out, inState[0]);
  not not_5 (not_5_out, BranchTaken);
  and and_1 (and_1_out, inState[0], BranchTaken);
  and and_2 (and_2_out, inState[1], not_1_out);
  and and_3 (and_3_out, not_2_out, not_3_out, BranchTaken);
  and and_4 (and_4_out, inState[1], not_4_out, not_5_out);
  or or_1 (outState[1], and_1_out, and_2_out);
  or or_2 (outState[0], and_3_out, and_4_out);
endmodule
